// Digital circuit CE_ADDER.dig as structural Verilog
module CE_ADDER (
  input  [7:0] A_AD,
  input  [15:0] B_AD,
  input  DI_AD,
  input  CI_AD,
  input  [3:0] S_AD,
  output VO_AD,
  output CO_AD,
  output [7:0] Q_AD,
  output [7:0] QH_AD
);

  wire add_1_c_o, add_2_c_o, add_3_c_o, add_4_c_o, add_5_c_o, and_2_out, and_3_out, and_4_out, and_5_out, D,
       multiplexer_3_out, multiplexer_4_out, nand_1_out, xor_1_out, xor_2_out, xor_3_out;
  wire [2:2] or_1_out, or_2_out;
  wire [3:0] add_4_s, add_5_s, add_6_s, add_7_s;
  wire [6:0] add_1_s;
  wire [6:6] not_1_out;
  wire [7:0] bitextender_1_out, ce_compl_1_do, multiplexer_1_out, multiplexer_2_out;
  wire [7:7] add_2_s;

  and and_1 (D, S_AD[2], DI_AD);
  not not_1 (not_1_out[6], D);
  CE_COMPL ce_compl_1 (.DI(B_AD[7:0]), .D(D), .DO(ce_compl_1_do));
  Multiplexer #(.Selector_Bits(2), .Bits(8)) multiplexer_1 (
    .sel(S_AD[1:0]), .in_0(A_AD), .in_1({8{1'b0}}), .in_2(A_AD), .in_3(B_AD[7:0]), .out(multiplexer_1_out));
  Multiplexer #(.Selector_Bits(2), .Bits(8)) multiplexer_2 (
    .sel(S_AD[1:0]), .in_0(B_AD[7:0]), .in_1(B_AD[7:0]), .in_2(ce_compl_1_do),
    .in_3({1'b1, {2{not_1_out[6]}}, 2'b11, {2{not_1_out[6]}}, 1'b1}), .out(multiplexer_2_out));
  BitExtender #(.inputBits(1), .outputBits(8)) bitextender_1 (.in(S_AD[1]), .out(bitextender_1_out));
  Add #(.Bits(7)) add_1 (
    .a(multiplexer_1_out[6:0]), .b(multiplexer_2_out[6:0]), .c_i(multiplexer_3_out), .s(add_1_s),
    .c_o(add_1_c_o));
  Add add_2 (.a(multiplexer_1_out[7]), .b(multiplexer_2_out[7]), .c_i(add_1_c_o), .s(add_2_s[7]), .c_o(add_2_c_o));
  Add #(.Bits(8)) add_3 (.a(B_AD[15:8]), .b(bitextender_1_out), .c_i(add_2_c_o), .s(QH_AD), .c_o(add_3_c_o));
  Add #(.Bits(4)) add_4 (
    .a(multiplexer_1_out[3:0]), .b(multiplexer_2_out[3:0]), .c_i(CI_AD), .s(add_4_s), .c_o(add_4_c_o));
  Add #(.Bits(4)) add_5 (
    .a(multiplexer_1_out[7:4]), .b(multiplexer_2_out[7:4]), .c_i(or_1_out[2]), .s(add_5_s), .c_o(add_5_c_o));
  Multiplexer #(.Selector_Bits(3)) multiplexer_3 (
    .sel(S_AD[2:0]), .in_0(1'b0), .in_1(1'b1), .in_2(1'b1), .in_3(1'b0), .in_4(CI_AD), .in_5(CI_AD),
    .in_6(CI_AD), .in_7(CI_AD), .out(multiplexer_3_out));
  or or_1 (or_1_out[2], and_4_out, and_2_out, add_4_c_o);
  xor xor_1 (xor_1_out, multiplexer_1_out[3], multiplexer_2_out[3]);
  xor xor_2 (xor_2_out, multiplexer_1_out[3], add_6_s[3]);
  and and_2 (and_2_out, add_4_s[1], add_4_s[3]);
  and and_3 (and_3_out, add_5_s[1], add_5_s[3]);
  and and_4 (and_4_out, add_4_s[2], add_4_s[3]);
  and and_5 (and_5_out, add_5_s[2], add_5_s[3]);
  or or_2 (or_2_out[2], and_5_out, and_3_out, add_5_c_o);
  nand nand_1 (nand_1_out, xor_1_out, xor_2_out);
  Multiplexer multiplexer_4 (.sel(S_AD[3]), .in_0(add_2_c_o), .in_1(add_3_c_o), .out(multiplexer_4_out));
  Add #(.Bits(4)) add_6 (.a(add_4_s), .b({1'b0, {2{or_1_out[2]}}, 1'b0}), .c_i(1'b0), .s(add_6_s));  // open: c_o
  Add #(.Bits(4)) add_7 (.a(add_5_s), .b({1'b0, {2{or_2_out[2]}}, 1'b0}), .c_i(1'b0), .s(add_7_s));  // open: c_o
  xor xor_3 (xor_3_out, add_1_c_o, add_2_c_o);
  Multiplexer multiplexer_5 (.sel(D), .in_0(xor_3_out), .in_1(nand_1_out), .out(VO_AD));
  Multiplexer multiplexer_6 (.sel(D), .in_0(multiplexer_4_out), .in_1(or_2_out[2]), .out(CO_AD));
  Multiplexer #(.Bits(8)) multiplexer_7 (.sel(D), .in_0({add_2_s[7], add_1_s}), .in_1({add_7_s, add_6_s}), .out(Q_AD));

  // Other names for the same wires on the sheet: A[7:0] = A_AD; B[7:0] = B_AD[7:0]; BH[7:0] = B_AD[15:8]; C = CI_AD;
  //   QH[7:0] = QH_AD; S0 = S_AD[0]; S1 = S_AD[1]; S2 = S_AD[2]; S3 = S_AD[3]

  // Notes on the sheet:
  //   A_AD: Input A
  //   B_AD: Input B
  //   DI_AD: Decimal in
  //   CI_AD: Carry in
  //   S_AD: Add
  //   Increment
  //   Subtract
  //   Decrement
  //   Add with Carry
  //   Increment with Carry
  //   Subtract with Carry
  //   Decrement with Carry
  //   Increment Word
  //   Decrement Word
  //   VO_AD: Overflow out
  //   CO_AD: Carry out
  //   Q_AD: Output Low
  //   QH_AD: Output High
endmodule
