// Digital circuit CE_ASR.dig as structural Verilog
module CE_ASR (
  input  [15:0] IN,
  input  SEL,
  output C_o,
  output [7:0] Q,
  output [7:0] QH
);

  Multiplexer multiplexer_1 (.sel(SEL), .in_0(IN[7]), .in_1(IN[8]), .out(Q[7]));
  // Probe on {{2{IN[15]}}, IN[14:9], Q[7], IN[7:1]}

  assign C_o = IN[0];
  assign Q[6:0] = IN[7:1];
  assign QH = {{2{IN[15]}}, IN[14:9]};

  // Notes on the sheet:
  //   C_o: Carry Out
  //   IN: Input
  //   Q: Output Low
  //   QH: Output High
  //   SEL: 8/16 bit Select
endmodule
