// Digital circuit CE_BUFFER.dig as structural Verilog
module CE_BUFFER (
  input  [7:0] I,
  input  E,
  output [7:0] Q
);

  Multiplexer #(.Bits(8)) multiplexer_1 (.sel(E), .in_0({8{1'b0}}), .in_1(I), .out(Q));

  // Notes on the sheet:
  //   I: Input
  //   Q: Output
  //   E: Enable
endmodule
