// Digital circuit CE_COMPL.dig as structural Verilog
module CE_COMPL (
  input  [7:0] DI,
  input  D,
  output [7:0] DO
);

  wire [3:0] _9s_CH_out, _9s_CL_out;
  wire [7:0] not_1_out;

  assign not_1_out = ~DI;  // Not not_1, 8 bits wide
  LookUpTable #(.Bits(4)) _9s_CL (.in0(DI[0]), .in1(DI[1]), .in2(DI[2]), .in3(DI[3]), .out(_9s_CL_out));
  LookUpTable #(.Bits(4)) _9s_CH (.in0(DI[4]), .in1(DI[5]), .in2(DI[6]), .in3(DI[7]), .out(_9s_CH_out));
  Multiplexer #(.Bits(8)) multiplexer_1 (.sel(D), .in_0(not_1_out), .in_1({_9s_CH_out, _9s_CL_out}), .out(DO));

  // Notes on the sheet:
  //   D: Decimal
  //   contents of _9s_CL (hex, n*v repeats v):
  //   9,8,7,6,5,4,3,2,1
  //   contents of _9s_CH (hex, n*v repeats v):
  //   9,8,7,6,5,4,3,2,1
endmodule
