// Digital circuit CE_DFF.dig as structural Verilog
module CE_DFF (
  input  C,
  input  D,
  input  E,
  input  R,
  output Q,
  output nQ
);

  wire multiplexer_1_out, multiplexer_2_out, or_1_out;

  Multiplexer multiplexer_1 (.sel(or_1_out), .in_0(Q), .in_1(multiplexer_2_out), .out(multiplexer_1_out));
  Multiplexer multiplexer_2 (.sel(R), .in_0(D), .in_1(1'b0), .out(multiplexer_2_out));
  or or_1 (or_1_out, E, R);
  D_FF d_ff_1 (.D(multiplexer_1_out), .C(C), .Q(Q), .nQ(nQ));

  // Notes on the sheet:
  //   D: Data In
  //   E: Enable
  //   Q: Output
  //   nQ: Inverted Output
  //   R: Reset
endmodule
