// Digital circuit CE_EDFF.dig as structural Verilog
module CE_EDFF (
  input  R,
  input  C,
  input  IN,
  output Q,
  output nQ
);

  wire multiplexer_1_out, not_1_out;

  Multiplexer multiplexer_1 (.sel(R), .in_0(IN), .in_1(C), .out(multiplexer_1_out));
  not not_1 (not_1_out, R);
  D_FF d_ff_1 (.D(not_1_out), .C(multiplexer_1_out), .Q(Q), .nQ(nQ));

  // Notes on the sheet:
  //   R: Reset
  //   IN: Input
endmodule
