// Digital circuit CE_JKFF.dig as structural Verilog
module CE_JKFF (
  input  C,
  input  J,
  input  K,
  input  R,
  output Q,
  output nQ
);

  wire and_1_out, or_1_out;

  and and_1 (and_1_out, J, ~R);  // And
  or or_1 (or_1_out, K, R);
  JK_FF jk_ff_1 (.J(and_1_out), .C(C), .K(or_1_out), .Q(Q), .nQ(nQ));
endmodule
