// Digital circuit CE_LFSR.dig as structural Verilog
module CE_LFSR (
  input  CLK,
  output [7:0] OUT
);

  wire d_ff_4_q, d_ff_14_q, xnor_1_out, xor_1_out, xor_2_out;
  wire [7:0] d_ff_1_q, d_ff_2_q, not_1_out, xor_3_out;

  D_FF d_ff_1 (.D(xor_1_out), .C(CLK), .Q(d_ff_1_q[0]));  // open: nQ
  D_FF d_ff_2 (.D(d_ff_1_q[0]), .C(CLK), .Q(d_ff_2_q[2]));  // open: nQ
  D_FF d_ff_3 (.D(d_ff_2_q[2]), .C(CLK), .Q(d_ff_2_q[7]));  // open: nQ
  D_FF d_ff_4 (.D(d_ff_2_q[7]), .C(CLK), .Q(d_ff_4_q));  // open: nQ
  D_FF d_ff_5 (.D(d_ff_4_q), .C(CLK), .Q(d_ff_1_q[1]));  // open: nQ
  D_FF d_ff_6 (.D(d_ff_1_q[1]), .C(CLK), .Q(d_ff_1_q[6]));  // open: nQ
  D_FF d_ff_7 (.D(d_ff_1_q[6]), .C(CLK), .Q(d_ff_2_q[1]));  // open: nQ
  D_FF d_ff_8 (.D(d_ff_2_q[1]), .C(CLK), .Q(d_ff_2_q[3]));  // open: nQ
  D_FF d_ff_9 (.D(d_ff_2_q[3]), .C(CLK), .Q(d_ff_2_q[4]));  // open: nQ
  D_FF d_ff_10 (.D(d_ff_2_q[4]), .C(CLK), .Q(d_ff_2_q[6]));  // open: nQ
  D_FF d_ff_11 (.D(d_ff_2_q[6]), .C(CLK), .Q(d_ff_1_q[3]));  // open: nQ
  D_FF d_ff_12 (.D(d_ff_1_q[3]), .C(CLK), .Q(d_ff_1_q[7]));  // open: nQ
  xor xor_1 (xor_1_out, d_ff_1_q[7], xor_2_out);
  D_FF d_ff_13 (.D(d_ff_1_q[7]), .C(CLK), .Q(d_ff_1_q[4]));  // open: nQ
  xor xor_2 (xor_2_out, d_ff_1_q[4], xnor_1_out);
  D_FF d_ff_14 (.D(d_ff_1_q[4]), .C(CLK), .Q(d_ff_14_q));  // open: nQ
  D_FF d_ff_15 (.D(d_ff_14_q), .C(CLK), .Q(d_ff_2_q[0]));  // open: nQ
  xnor xnor_1 (xnor_1_out, d_ff_2_q[0], d_ff_2_q[5]);
  D_FF d_ff_16 (.D(d_ff_2_q[0]), .C(CLK), .Q(d_ff_2_q[5]));  // open: nQ
  D_FF d_ff_17 (.D(d_ff_2_q[5]), .C(CLK), .Q(d_ff_1_q[2]));  // open: nQ
  assign xor_3_out = d_ff_2_q ^ {d_ff_1_q[7:6], d_ff_2_q[0], d_ff_1_q[4:0]};  // XOr xor_3, 8 bits wide
  Multiplexer #(.Bits(8)) multiplexer_1 (.sel(d_ff_4_q), .in_0(xor_3_out), .in_1(not_1_out), .out(OUT));
  assign not_1_out = ~xor_3_out;  // Not not_1, 8 bits wide

  // Other names for the same wires on the sheet: C = CLK

  // Notes on the sheet:
  //   CLK: Clock
  //   OUT: Output
endmodule
