// Digital circuit CE_M_ALU.dig as structural Verilog
module CE_M_ALU (
  input  [7:0] ALA_A,
  input  [15:0] ALB_A,
  input  [9:0] A_CTRL_A,
  input  SOB_A,
  input  CIB_A,
  input  R_A,
  input  nC_A,
  input  C_A,
  input  ABT_A,
  output [15:0] ALO_A,
  output [6:0] FLO_A,
  output BY_A
);

  wire and_1_out, and_2_out, and_3_out, and_4_out, and_5_out, and_6_out, and_7_out, and_8_out, and_9_out,
       and_10_out, and_11_out, and_12_out, and_13_out, and_14_out, and_15_out, AZS, ce_adder_1_co_ad,
       ce_asr_1_c_o, ce_cbh_1_c_o, ce_chb_1_c_o, ce_nz_1_q, ce_nz_2_q, ce_nz_3_q, ce_nz_4_q, ce_srl_1_c_o,
       ce_srr_1_c_o, CI, DONE, multiplexer_3_out, multiplexer_5_out, multiplexer_6_out, multiplexer_9_out,
       multiplexer_10_out, multiplexer_11_out, multiplexer_12_out, multiplexer_13_out, multiplexer_14_out,
       nD2, NI, or_2_out, or_3_out, or_4_out, or_6_out, or_7_out, or_8_out, or_9_out, or_10_out, SL0, SL3,
       VI, ZI;
  wire [1:1] and_18_out;
  wire [2:0] QHS;
  wire [3:0] SL1, SL2;
  wire [6:0] multiplexer_2_out, multiplexer_8_out, SL4;
  wire [7:0] and_17_out, ANDQ, ce_adder_1_q_ad, ce_adder_1_qh_ad, ce_asr_1_q, ce_asr_1_qh, ce_cbh_1_q,
       ce_chb_1_q, ce_srl_1_q, ce_srl_1_qh, ce_srr_1_q, ce_srr_1_qh, decoder_1_out_0,
       dig_div_unsigned_1_qo_ud, dig_div_unsigned_1_ro_ud, mul_1_mul, mul_1_mul_2, multiplexer_1_out,
       multiplexer_4_out, or_5_out, Q, xor_1_out;

  and and_1 (and_1_out, ~A_CTRL_A[1], ~A_CTRL_A[2], A_CTRL_A[3], ~A_CTRL_A[4], ~A_CTRL_A[5], ~A_CTRL_A[6], ~A_CTRL_A[7], ~A_CTRL_A[8], ~A_CTRL_A[9]);  // And
  and and_2 (and_2_out, ~A_CTRL_A[1], ~A_CTRL_A[2], A_CTRL_A[3], A_CTRL_A[4], ~A_CTRL_A[5], ~A_CTRL_A[6], ~A_CTRL_A[7], ~A_CTRL_A[8], ~A_CTRL_A[9]);  // And
  and and_3 (and_3_out, ~A_CTRL_A[1], ~A_CTRL_A[2], A_CTRL_A[3], ~A_CTRL_A[4], A_CTRL_A[5], ~A_CTRL_A[6], ~A_CTRL_A[7], ~A_CTRL_A[8], ~A_CTRL_A[9]);  // And
  and and_4 (and_4_out, ~A_CTRL_A[1], ~A_CTRL_A[2], A_CTRL_A[3], A_CTRL_A[4], A_CTRL_A[5], ~A_CTRL_A[6], ~A_CTRL_A[7], ~A_CTRL_A[8], ~A_CTRL_A[9]);  // And
  and and_5 (and_5_out, A_CTRL_A[1], A_CTRL_A[2], A_CTRL_A[3], ~A_CTRL_A[4], ~A_CTRL_A[9]);  // And
  and and_6 (and_6_out, A_CTRL_A[1], A_CTRL_A[2], ~A_CTRL_A[3], ~A_CTRL_A[4], ~A_CTRL_A[5], A_CTRL_A[7], A_CTRL_A[8], ~A_CTRL_A[9]);  // And
  and and_7 (and_7_out, A_CTRL_A[1], A_CTRL_A[2], ~A_CTRL_A[3], A_CTRL_A[4], ~A_CTRL_A[5], ~A_CTRL_A[6], A_CTRL_A[7], A_CTRL_A[8], ~A_CTRL_A[9]);  // And
  and and_8 (and_8_out, A_CTRL_A[1], A_CTRL_A[2], ~A_CTRL_A[3], A_CTRL_A[4], ~A_CTRL_A[5], ~A_CTRL_A[6], A_CTRL_A[7], A_CTRL_A[8], A_CTRL_A[9]);  // And
  and and_9 (and_9_out, ~A_CTRL_A[1], A_CTRL_A[2], ~A_CTRL_A[3], A_CTRL_A[4], ~A_CTRL_A[5], ~A_CTRL_A[6], A_CTRL_A[7], A_CTRL_A[8], A_CTRL_A[9]);  // And
  and and_10 (and_10_out, A_CTRL_A[1], A_CTRL_A[2], ~A_CTRL_A[3], A_CTRL_A[4], ~A_CTRL_A[5], A_CTRL_A[6], A_CTRL_A[7], A_CTRL_A[8], A_CTRL_A[9]);  // And
  and and_11 (and_11_out, A_CTRL_A[1], A_CTRL_A[2], ~A_CTRL_A[3], A_CTRL_A[4], ~A_CTRL_A[5], A_CTRL_A[6], A_CTRL_A[7], A_CTRL_A[8], ~A_CTRL_A[9]);  // And
  or or_1 (AZS, and_1_out, and_2_out, and_3_out, and_4_out, and_5_out);
  PriorityEncoder #(.Selector_Bits(3)) priorityencoder_1 (
    .in0(1'b0), .in1(and_6_out), .in2(and_7_out), .in3(and_8_out), .in4(and_9_out), .in5(and_10_out),
    .in6(and_11_out), .in7(1'b0), .num(QHS));  // open: any
  ROM #(.AddrBits(9), .Bits(17)) ALU (.A(A_CTRL_A[9:1]), .sel(1'b1), .D({SL4, SL3, SL2, SL1, SL0}));
  and and_12 (and_12_out, ~SL2[0], ~SL2[1], ~SL2[2], SL2[3]);  // And
  and and_13 (and_13_out, SL2[0], ~SL2[1], ~SL2[2], SL2[3]);  // And
  Multiplexer #(.Bits(8)) multiplexer_1 (.sel(SL0), .in_0(Q), .in_1(ALB_A[7:0]), .out(multiplexer_1_out));
  Multiplexer #(.Bits(8)) multiplexer_2 (
    .sel(AZS), .in_0(multiplexer_1_out), .in_1(ANDQ), .out({NI, multiplexer_2_out}));
  or or_2 (or_2_out, and_12_out, and_13_out);
  nor nor_1 (ZI, multiplexer_2_out[0], multiplexer_2_out[1], multiplexer_2_out[2], multiplexer_2_out[3], multiplexer_2_out[4], multiplexer_2_out[5], multiplexer_2_out[6], NI);
  Decoder #(.Selector_Bits(3)) decoder_1 (
    .sel(A_CTRL_A[7:5]), .out_0(decoder_1_out_0[0]), .out_1(decoder_1_out_0[1]), .out_2(decoder_1_out_0[2]),
    .out_3(decoder_1_out_0[3]), .out_4(decoder_1_out_0[4]), .out_5(decoder_1_out_0[5]),
    .out_6(decoder_1_out_0[6]), .out_7(decoder_1_out_0[7]));
  Multiplexer multiplexer_3 (.sel(or_2_out), .in_0(1'b0), .in_1(FLO_A[0]), .out(multiplexer_3_out));
  and and_14 (and_14_out, ~SL2[0], ~SL2[1], SL2[2], SL2[3], A_CTRL_A[0]);  // And
  and and_15 (and_15_out, SL2[0], ~SL2[1], SL2[2], SL2[3], A_CTRL_A[0]);  // And
  or or_3 (or_3_out, ABT_A, R_A);
  Multiplexer #(.Bits(8)) multiplexer_4 (.sel(SL1[0]), .in_0(ALA_A), .in_1(decoder_1_out_0), .out(multiplexer_4_out));
  or or_4 (or_4_out, and_14_out, and_15_out);
  CE_ADDER ce_adder_1 (
    .A_AD(ALA_A), .B_AD(ALB_A), .DI_AD(FLO_A[3]), .CI_AD(FLO_A[0]), .S_AD(SL1), .VO_AD(VI),
    .CO_AD(ce_adder_1_co_ad), .Q_AD(ce_adder_1_q_ad), .QH_AD(ce_adder_1_qh_ad));
  CE_SRL ce_srl_1 (
    .C_i(multiplexer_3_out), .IN(ALB_A), .SEL(SL1[1]), .C_o(ce_srl_1_c_o), .Q(ce_srl_1_q), .QH(ce_srl_1_qh));
  CE_ASR ce_asr_1 (.IN(ALB_A), .SEL(SL1[1]), .C_o(ce_asr_1_c_o), .Q(ce_asr_1_q), .QH(ce_asr_1_qh));
  CE_SRR ce_srr_1 (
    .C_i(multiplexer_3_out), .IN(ALB_A), .SEL(SL1[1]), .C_o(ce_srr_1_c_o), .Q(ce_srr_1_q), .QH(ce_srr_1_qh));
  assign ANDQ = ALA_A & ALB_A[7:0];  // And and_16, 8 bits wide
  assign and_17_out = ~multiplexer_4_out & ALB_A[7:0];  // And and_17, 8 bits wide
  assign or_5_out = multiplexer_4_out | ALB_A[7:0];  // Or or_5, 8 bits wide
  assign xor_1_out = ALA_A ^ ALB_A[7:0];  // XOr xor_1, 8 bits wide
  Mul #(.Bits(8)) mul_1 (.a(ALA_A), .b(ALB_A[7:0]), .mul({mul_1_mul_2, mul_1_mul}));
  DIG_Div_unsigned dig_div_unsigned_1 (
    .AI_UD(ALA_A), .BI_UD(ALB_A[7:0]), .C_UD(C_A), .nC_UD(nC_A), .EN_UD(or_4_out), .R_UD(or_3_out),
    .QO_UD(dig_div_unsigned_1_qo_ud), .RO_UD(dig_div_unsigned_1_ro_ud), .BY_UD(BY_A), .DONE_UD(DONE));
  CE_CHB ce_chb_1 (.I(ALB_A[7:0]), .Q(ce_chb_1_q), .C_O(ce_chb_1_c_o));
  CE_CBH ce_cbh_1 (.I(ALB_A[7:0]), .Q(ce_cbh_1_q), .C_O(ce_cbh_1_c_o));
  not not_1 (nD2, ALB_A[2]);
  and and_18 (and_18_out[1], ~A_CTRL_A[1], ~A_CTRL_A[2], ~A_CTRL_A[3], A_CTRL_A[4], ~A_CTRL_A[5], A_CTRL_A[6], ~A_CTRL_A[7], ~A_CTRL_A[8], ~A_CTRL_A[9]);  // And
  Multiplexer multiplexer_5 (.sel(SL0), .in_0(VI), .in_1(ALB_A[6]), .out(multiplexer_5_out));
  Multiplexer multiplexer_6 (.sel(SL0), .in_0(NI), .in_1(ALB_A[7]), .out(multiplexer_6_out));
  Multiplexer #(.Selector_Bits(3), .Bits(8)) multiplexer_7 (
    .sel(QHS), .in_0({8{1'b0}}), .in_1(ce_adder_1_qh_ad), .in_2(ce_srl_1_qh), .in_3(ce_asr_1_qh),
    .in_4(ce_srr_1_qh), .in_5(ce_srl_1_qh), .in_6(ce_srr_1_qh), .in_7({8{1'b0}}), .out(ALO_A[15:8]));
  Multiplexer #(.Bits(7)) multiplexer_8 (.sel(or_6_out), .in_0({7{1'b0}}), .in_1(SL4), .out(multiplexer_8_out));
  or or_6 (or_6_out, DONE, A_CTRL_A[0]);
  Multiplexer #(.Selector_Bits(2)) multiplexer_9 (
    .sel({and_18_out[1], SL3}), .in_0(multiplexer_5_out), .in_1(SL0), .in_2(ALB_A[6]), .in_3(SL0),
    .out(multiplexer_9_out));
  Multiplexer #(.Selector_Bits(2)) multiplexer_10 (
    .sel({and_18_out[1], SL3}), .in_0(multiplexer_6_out), .in_1(SL0), .in_2(ALB_A[7]), .in_3(SL0),
    .out(multiplexer_10_out));
  Multiplexer #(.Selector_Bits(2)) multiplexer_11 (
    .sel({and_18_out[1], SL3}), .in_0(CI), .in_1(SL0), .in_2(ALB_A[0]), .in_3(SL0), .out(multiplexer_11_out));
  Multiplexer #(.Selector_Bits(2)) multiplexer_12 (
    .sel({and_18_out[1], SL3}), .in_0(ZI), .in_1(SL0), .in_2(ALB_A[1]), .in_3(SL0), .out(multiplexer_12_out));
  Multiplexer multiplexer_13 (.sel(and_18_out[1]), .in_0(SL0), .in_1(nD2), .out(multiplexer_13_out));
  or or_7 (or_7_out, multiplexer_13_out, CIB_A);
  or or_8 (or_8_out, multiplexer_8_out[2], CIB_A);
  Multiplexer multiplexer_14 (.sel(and_18_out[1]), .in_0(SL0), .in_1(ALB_A[3]), .out(multiplexer_14_out));
  or or_9 (or_9_out, multiplexer_9_out, SOB_A);
  or or_10 (or_10_out, multiplexer_8_out[5], SOB_A);
  CE_NZ ce_nz_1 (.IN(mul_1_mul_2), .Q(ce_nz_1_q));
  CE_NZ ce_nz_2 (.IN(mul_1_mul), .Q(ce_nz_2_q));
  CE_NZ ce_nz_3 (.IN(dig_div_unsigned_1_ro_ud), .Q(ce_nz_3_q));
  CE_NZ ce_nz_4 (.IN(dig_div_unsigned_1_qo_ud), .Q(ce_nz_4_q));
  CE_DFF ce_dff_1 (.C(nC_A), .D(multiplexer_11_out), .E(multiplexer_8_out[0]), .R(R_A), .Q(FLO_A[0]));  // open: nQ
  CE_DFF ce_dff_2 (.C(nC_A), .D(multiplexer_12_out), .E(multiplexer_8_out[1]), .R(R_A), .Q(FLO_A[1]));  // open: nQ
  CE_DFF ce_dff_3 (.C(nC_A), .D(or_7_out), .E(or_8_out), .R(R_A), .nQ(FLO_A[2]));  // open: Q
  CE_DFF ce_dff_4 (.C(nC_A), .D(multiplexer_14_out), .E(multiplexer_8_out[3]), .R(R_A), .Q(FLO_A[3]));  // open: nQ
  CE_DFF ce_dff_5 (.C(nC_A), .D(SL0), .E(multiplexer_8_out[4]), .R(R_A), .nQ(FLO_A[4]));  // open: Q
  CE_DFF ce_dff_6 (.C(nC_A), .D(or_9_out), .E(or_10_out), .R(R_A), .Q(FLO_A[5]));  // open: nQ
  CE_DFF ce_dff_7 (.C(nC_A), .D(multiplexer_10_out), .E(multiplexer_8_out[6]), .R(R_A), .Q(FLO_A[6]));  // open: nQ
  Multiplexer #(.Selector_Bits(4), .Bits(8)) multiplexer_15 (
    .sel(SL2), .in_0(ce_adder_1_q_ad), .in_1(ANDQ), .in_2(and_17_out), .in_3(or_5_out), .in_4(xor_1_out),
    .in_5(ce_srl_1_q), .in_6(ce_asr_1_q), .in_7(ce_srr_1_q), .in_8(ce_srl_1_q), .in_9(ce_srr_1_q),
    .in_10(mul_1_mul), .in_11(mul_1_mul_2), .in_12(dig_div_unsigned_1_qo_ud),
    .in_13(dig_div_unsigned_1_ro_ud), .in_14(ce_chb_1_q), .in_15(ce_cbh_1_q), .out(Q));
  Multiplexer #(.Selector_Bits(4)) multiplexer_16 (
    .sel(SL2), .in_0(ce_adder_1_co_ad), .in_1(1'b0), .in_2(1'b0), .in_3(1'b0), .in_4(1'b0),
    .in_5(ce_srl_1_c_o), .in_6(ce_asr_1_c_o), .in_7(ce_srr_1_c_o), .in_8(ce_srl_1_c_o), .in_9(ce_srr_1_c_o),
    .in_10(ce_nz_1_q), .in_11(ce_nz_2_q), .in_12(ce_nz_3_q), .in_13(ce_nz_4_q), .in_14(ce_chb_1_c_o),
    .in_15(ce_cbh_1_c_o), .out(CI));
  Multiplexer #(.Bits(8)) multiplexer_17 (.sel(SL0), .in_0(Q), .in_1(ALB_A[7:0]), .out(ALO_A[7:0]));

  // Other names for the same wires on the sheet: A[7:0] = ALA_A; E = A_CTRL_A[0]; OPC[8:0] = A_CTRL_A[9:1];
  //   ABT = ABT_A; B[7:0] = ALB_A[7:0]; B16[15:0] = ALB_A; D0 = ALB_A[0]; D1 = ALB_A[1]; D3 = ALB_A[3]; D4 = ALB_A[4];
  //   D5 = ALB_A[5]; D6 = ALB_A[6]; D7 = ALB_A[7]; BH[7:0] = ALB_A[15:8]; BY = BY_A; C = C_A; CIB = CIB_A;
  //   CO = FLO_A[0]; DO = FLO_A[3]; nC = nC_A; nEO = FLO_A[4]; nIO = FLO_A[2]; NO = FLO_A[6]; QH[7:0] = ALO_A[15:8];
  //   R = R_A; SOB = SOB_A; VO = FLO_A[5]; ZO = FLO_A[1]

  // Notes on the sheet:
  //   ALO_A: Output
  //   FLO_A: Flag output
  //   ALA_A: A Input
  //   ALB_A: B Input
  //   A_CTRL_A: ALU Control
  //   SOB_A: Set Overflow... Bit?
  //   CIB_A: Clear Interrupt Bit
  //   R_A: Reset
  //   ABT_A: Abort Input
  //   contents of ALU (hex, n*v repeats v):
  //   10801,10860,600,4200,860,10860,10ca0,42,10801,10860,10ca0,10801,860,10860,10ca0,10801,
  //   10801,10860,10860,10801,840,10860,10ca0,42,600,10860,10802,10802,840,10860,10ca0,
  //   10801,10801,10820,10801,10801,18801,10820,10d00,42,1bc00,10820,10d00,10801,18801,
  //   10820,10d00,10801,10801,10820,10820,10801,18801,10820,10d00,42,601,10820,10806,10806,
  //   18801,10820,10d00,10801,1bc00,10880,10801,10cc0,10cc0,10880,10ce0,42,10801,10880,
  //   10ce0,10801,10801,10880,10ce0,10801,10801,10880,10880,10801,10cc0,10880,10ce0,42,
  //   1201,10880,10801,10801,10801,10880,10ce0,10801,10801,10c08,10801,10801,10801,10c08,
  //   10d20,42,10801,10c08,10d20,10801,10801,10c08,10d20,10801,10801,10c08,10c08,10801,
  //   10801,10c08,10d20,42,1200,10c08,10801,10801,10801,10c08,10d20,10801,10801,10801,10801,
  //   10801,10801,10801,10801,62,10806,18801,10801,10801,10801,10801,10801,10801,10801,
  //   10801,10801,10801,10801,10801,10801,62,10801,10801,10801,10801,10801,10801,10801,
  //   10801,10801,10801,10801,10801,10801,10801,10801,62,10801,10801,10801,10801,10801,
  //   10801,10801,10801,10801,10801,10801,10801,10801,10801,10801,62,8200,10801,10801,10801,
  //   10801,10801,10801,10801,10c04,10c04,10c04,10816,10c04,10c04,10806,62,10802,10c04,
  //   10806,10ca4,10c04,10c04,10806,10801,10801,10c04,10c04,10801,10c04,10c04,10806,62,
  //   2200,10c04,10801,10801,10c04,10c04,10806,10801,10c04,10c0c,10801,10812,10c04,10c0c,
  //   10802,62,10802,10c0c,10801,10d04,10c04,10c0c,10802,10801,10801,10c0c,10c0c,10801,
  //   10801,10c0c,10802,62,2201,10c0c,10801,10801,10801,10c0c,10802,10801,10801,10801,10801,
  //   10801,10801,10d40,10801,10801,10801,10d40,10801,10801,10801,10d40,10801,10801,10801,
  //   10801,10801,10801,10801,10d40,10801,10801,10801,10d40,10801,10801,10801,10d40,10801,
  //   10801,10801,10801,10801,10801,10801,10d60,10801,10801,10801,10d60,10801,10801,10801,
  //   10d60,10801,10801,10801,10801,10801,10801,10801,10d60,10801,10801,10801,10d60,10801,
  //   10801,10801,10d60,10801,10801,10801,10801,10801,10801,10801,10da0,10801,10801,10801,
  //   10da0,10801,10801,10801,10da0,10801,10801,10801,10801,10801,10801,10801,10da0,10801,
  //   10801,10801,10da0,10801,10801,10801,10da0,10801,10801,10801,10801,10801,10801,10801,
  //   10d80,10801,10801,10801,10d80,10801,10801,10801,10d80,10801,10801,10801,10801,10801,
  //   10801,10801,10d80,10801,10801,10801,10d80,10801,10801,10801,10d80,10801,10801,10801,
  //   10801,10801,10801,10801,10801,10801,10801,10801,10801,10801,10801,10801,10801,10801,
  //   10801,10801,10801,10801,10801,10801,10801,10801,10801,10801,10801,10801,10801,10801,
  //   10801,10801,10801,10801,10801,10801,10801,10801,10801,10801,10801,10801,10801,10801,
  //   10801,10801,10801,10801,10801,10801,10801,10801,10801,10801,10801,10801,10801,10801,
  //   10801,10801,10801,10801,10801,10801,10801,10801,10801,10801,10801,10801,10801,10c0e,
  //   10801,10de0,10801,10ce4,10cc4,10801,10801,10c0e,10801,10801,10801,10801,10801,10801,
  //   10801,10c0e,10801,10801,10801,10801,10801,10801,10801,10c0e,10801,10801,10801,10801,
  //   10801,10801,10801,10c0a,10801,10dc0,10801,10801,10d24,10801,10801,10c0a,10801,10801,
  //   10801,10801,10801,10801,10801,10c0a,10801,10801,10801,10801,10801,10801,10801,10c0a,
  //   10801
endmodule
