// Digital circuit CE_M_CPU_TOP.dig as structural Verilog
module CE_M_CPU_TOP (
  input  R_CPU,
  input  C_CPU,
  input  nIRQ_CPU,
  input  nNMI_CPU,
  input  nABT_CPU,
  input  nSOB_CPU,
  input  nRDY_CPU,
  input  BE_CPU,
  output [7:0] D_CPU,
  output [15:0] AO_CPU,
  output RnW_CPU,
  output nMLB_CPU,
  output VDA_CPU,
  output VPA_CPU,
  output VBA_CPU,
  output VSA_CPU,
  output VVA_CPU
);

  wire AA, and_1_out, and_2_out, and_3_out, and_4_out, and_5_out, BY, C, ce_m_cu_1_int_u, ce_m_cu_1_ldir_u,
       ce_m_cu_1_wai_u, ce_m_regs_1_vpa_r, ce_m_regs_1_vva_r, nC, not_1_out, or_1_out, pincontrol_1_p2, RDY;
  wire [1:0] ce_m_cu_1_anri_u;
  wire [2:0] ce_m_cu_1_m_ctrl_u, ce_m_cu_1_pco_u, not_3_out;
  wire [3:0] ce_m_cu_1_spo_u;
  wire [6:0] ce_m_alu_1_flo_a;
  wire [7:0] ce_lfsr_1_out, ce_m_regs_1_ala_r, ce_m_regs_1_do_r, DI;
  wire [9:0] ce_m_cu_1_a_ctrl_u;
  wire [15:0] ce_m_alu_1_alo_a, ce_m_regs_1_alb_r;
  wire [31:0] ce_m_cu_1_r_ctrl_u;

  Multiplexer multiplexer_1 (.sel(RDY), .in_0(C_CPU), .in_1(1'b1), .out(C));
  and and_1 (and_1_out, BE_CPU, ~nIRQ_CPU);  // And
  and and_2 (and_2_out, BE_CPU, ~nNMI_CPU);  // And
  and and_3 (and_3_out, BE_CPU, ~nABT_CPU);  // And
  and and_4 (and_4_out, BE_CPU, ~nSOB_CPU);  // And
  not not_1 (not_1_out, nRDY_CPU);
  not not_2 (nC, C);
  D_FF d_ff_1 (.D(not_1_out), .C(C_CPU), .Q(RDY));  // open: nQ
  CE_LFSR ce_lfsr_1 (.CLK(C_CPU), .OUT(ce_lfsr_1_out));
  CE_M_REGS ce_m_regs_1 (
    .R_R(R_CPU), .nC_R(nC), .DI_R(DI), .ALUI_R(ce_m_alu_1_alo_a), .RNDI_R(ce_lfsr_1_out),
    .FLI_R({ce_m_alu_1_flo_a[6:3], not_3_out[2], ce_m_alu_1_flo_a[2:0]}), .ANRI_R(ce_m_cu_1_anri_u),
    .R_CTRL_R(ce_m_cu_1_r_ctrl_u), .PCO_R(ce_m_cu_1_pco_u), .SPO_R(ce_m_cu_1_spo_u),
    .ALA_R(ce_m_regs_1_ala_r), .ALB_R(ce_m_regs_1_alb_r), .DO_R(ce_m_regs_1_do_r), .VPA_R(ce_m_regs_1_vpa_r),
    .VBA_R(VBA_CPU), .VSA_R(VSA_CPU), .VVA_R(ce_m_regs_1_vva_r), .AO_R(AO_CPU));
  CE_M_CU ce_m_cu_1 (
    .R_U(R_CPU), .C_U(C), .nC_U(nC), .DI_U(DI), .FLI_U(ce_m_alu_1_flo_a), .IRQ_U(and_1_out),
    .NMI_U(and_2_out), .ABT_U(and_3_out), .BY_U(BY), .ANRI_U(ce_m_cu_1_anri_u), .INT_U(ce_m_cu_1_int_u),
    .LDIR_U(ce_m_cu_1_ldir_u), .A_CTRL_U(ce_m_cu_1_a_ctrl_u), .R_CTRL_U(ce_m_cu_1_r_ctrl_u),
    .SPO_U(ce_m_cu_1_spo_u), .M_CTRL_U(ce_m_cu_1_m_ctrl_u), .PCO_U(ce_m_cu_1_pco_u), .WAI_U(ce_m_cu_1_wai_u),
    .AA_U(AA));
  CE_M_ALU ce_m_alu_1 (
    .FLO_A(ce_m_alu_1_flo_a), .ALO_A(ce_m_alu_1_alo_a), .BY_A(BY), .R_A(R_CPU), .C_A(C), .nC_A(nC),
    .ALA_A(ce_m_regs_1_ala_r), .ALB_A(ce_m_regs_1_alb_r), .A_CTRL_A(ce_m_cu_1_a_ctrl_u), .SOB_A(and_4_out),
    .CIB_A(ce_m_cu_1_int_u), .ABT_A(AA));
  and and_5 (and_5_out, VSA_CPU, ce_m_cu_1_int_u);
  assign {not_3_out[2], nMLB_CPU, not_3_out[0]} = ~ce_m_cu_1_m_ctrl_u;  // Not not_3, 3 bits wide
  or or_1 (or_1_out, BY, ce_m_cu_1_wai_u);
  or or_2 (VVA_CPU, ce_m_regs_1_vva_r, and_5_out);
  and and_6 (RnW_CPU, BE_CPU, not_3_out[0]);
  // PinControl #(.Bits(8)) pincontrol_1: pin names not known; wires that end beside it: ce_m_regs_1_do_r, pincontrol_1_p2, DI, D_CPU
  not not_4 (pincontrol_1_p2, RnW_CPU);
  and and_7 (VDA_CPU, ~ce_m_cu_1_ldir_u, ~or_1_out);  // And
  and and_8 (VPA_CPU, ce_m_regs_1_vpa_r, ~or_1_out);  // And

  // Other names for the same wires on the sheet: BE = BE_CPU; CB = C_CPU; R = R_CPU

  // Notes on the sheet:
  //   R_CPU: Reset, default 1
  //   nIRQ_CPU: Interrupt Request, default 1
  //   nNMI_CPU: Non-Maskable Interrupt, default 1
  //   nABT_CPU: Abort, default 1
  //   nSOB_CPU: Set Overflow Bit, default 1
  //   nRDY_CPU: Ready, default 1
  //   BE_CPU: Bus Enable, default 1
  //   D_CPU: Data In/Output
  //   AO_CPU: Address Output
  //   RnW_CPU: Read/Write
  //   nMLB_CPU: Memory Lock Bit
  //   VDA_CPU: Valid Data Address
  //   VPA_CPU: Valid Program Address
  //   VBA_CPU: Valid Base Page Address
  //   VSA_CPU: Valid Stack Address
  //   VVA_CPU: Valid Vector Address
endmodule
