// Digital circuit CE_M_CU.dig as structural Verilog
module CE_M_CU (
  input  R_U,
  input  C_U,
  input  nC_U,
  input  [7:0] DI_U,
  input  [6:0] FLI_U,
  input  IRQ_U,
  input  NMI_U,
  input  ABT_U,
  input  BY_U,
  output [1:0] ANRI_U,
  output INT_U,
  output LDIR_U,
  output [9:0] A_CTRL_U,
  output [31:0] R_CTRL_U,
  output [3:0] SPO_U,
  output [2:0] M_CTRL_U,
  output [2:0] PCO_U,
  output WAI_U,
  output AA_U
);

  wire ABT_nq, ACY0, and_1_out, and_2_out, and_3_out, and_4_out, and_5_out, and_6_out, and_7_out, and_8_out,
       and_11_out, and_12_out, and_16_out, and_17_out, and_18_out, CABT, CABT_q, CIRQ_q, CLR, CNMI_q,
       comparator_1_eq, COND, CONE, CY0, END, INTQ, IRQ, multiplexer_1_out, NMI, nor_1_out, O2C, or_1_out,
       or_2_out, or_3_out, or_4_out, or_5_out, or_6_out, or_7_out, or_8_out, or_9_out, or_11_out, or_12_out,
       or_13_out, or_14_out, RES, SKIP;
  wire [1:0] priorityencoder_1_num;
  wire [2:0] add_1_s, CY, neg_1_out, PCO_d;
  wire [3:0] CONS, multiplexer_2_out, multiplexer_3_out;
  wire [7:0] INA_d, INST0_d, INST1_d, multiplexer_4_out, multiplexer_5_out, multiplexer_6_out,
       multiplexer_7_out, multiplexer_8_out, OPC_d, RES_d;
  wire [8:8] multiplexer_9_out;
  wire [9:9] multiplexer_11_out;
  wire [11:0] ROM12_d;
  wire [31:0] ROM32_d;
  wire [31:29] multiplexer_10_out;

  or or_1 (or_1_out, FLI_U[2], NMI, AA_U, RES);
  or or_2 (or_2_out, NMI, AA_U, RES);
  or or_3 (or_3_out, AA_U, RES);
  and and_1 (and_1_out, ~or_1_out, IRQ_U);  // And
  and and_2 (and_2_out, ~or_2_out, NMI_U);  // And
  and and_3 (and_3_out, ~or_3_out, ABT_U);  // And
  Comparator #(.Bits(8)) comparator_1 (.a(A_CTRL_U[8:1]), .b(8'h5c), .eq(comparator_1_eq));  // open: gt, lt
  CE_JKFF CIRQ (.C(C_U), .J(and_1_out), .K(CLR), .R(CLR), .Q(CIRQ_q));  // open: nQ
  CE_JKFF CNMI (.C(nC_U), .J(and_2_out), .K(CLR), .R(CLR), .Q(CNMI_q));  // open: nQ
  CE_JKFF u_CABT (.C(nC_U), .J(and_3_out), .K(CLR), .R(CLR), .Q(CABT_q));  // open: nQ
  CE_DFF COPC2 (.C(C_U), .D(comparator_1_eq), .E(1'b1), .R(R_U), .Q(O2C));  // open: nQ
  or or_4 (or_4_out, CIRQ_q, CNMI_q);
  or or_5 (or_5_out, CLR, O2C);
  and and_4 (and_4_out, ~or_5_out, END, CIRQ_q);  // And
  and and_5 (and_5_out, ~or_5_out, END, CNMI_q);  // And
  and and_6 (and_6_out, ~or_5_out, CABT_q);  // And
  and and_7 (and_7_out, O2C, or_6_out);
  or or_6 (or_6_out, AA_U, END);
  and and_8 (and_8_out, END, A_CTRL_U[9]);
  CE_JKFF u_IRQ (.C(nC_U), .J(and_4_out), .K(CLR), .R(CLR), .Q(IRQ));  // open: nQ
  CE_JKFF u_NMI (.C(nC_U), .J(and_5_out), .K(CLR), .R(CLR), .Q(NMI));  // open: nQ
  CE_JKFF ABT (.C(nC_U), .J(and_6_out), .K(CLR), .R(CLR), .Q(AA_U), .nQ(ABT_nq));
  CE_JKFF OPC2 (.C(nC_U), .J(and_7_out), .K(and_8_out), .R(R_U), .Q(A_CTRL_U[9]));  // open: nQ
  and and_9 (CABT, ABT_nq, CABT_q);
  and and_10 (INTQ, or_4_out, ~O2C, ~IRQ, ~NMI);  // And
  ROM #(.AddrBits(9), .Bits(8)) OPC (.A(A_CTRL_U[9:1]), .sel(1'b1), .D(OPC_d));
  ROM #(.AddrBits(9), .Bits(4)) CON (.A(A_CTRL_U[9:1]), .sel(1'b1), .D(CONS));
  or or_7 (or_7_out, CABT, INTQ);
  and and_11 (and_11_out, SKIP, ~or_7_out);  // And
  or or_8 (or_8_out, IRQ, NMI, AA_U, RES);
  Multiplexer #(.Selector_Bits(4)) multiplexer_1 (
    .sel(CONS), .in_0(1'b1), .in_1(1'b0), .in_2(BY_U), .in_3(1'b0), .in_4(FLI_U[0]), .in_5(FLI_U[1]),
    .in_6(FLI_U[3]), .in_7(FLI_U[4]), .in_8(DI_U[0]), .in_9(DI_U[1]), .in_10(DI_U[2]), .in_11(DI_U[3]),
    .in_12(DI_U[4]), .in_13(DI_U[5]), .in_14(DI_U[6]), .in_15(DI_U[7]), .out(multiplexer_1_out));
  Multiplexer #(.Bits(4)) multiplexer_2 (.sel(and_16_out), .in_0(4'b1111), .in_1(4'b0101), .out(multiplexer_2_out));
  and and_12 (and_12_out, and_11_out, ~WAI_U);  // And
  and and_13 (ACY0, CY0, ~or_8_out);  // And
  and and_14 (WAI_U, CONS[0], CONS[1], ~CONS[2], ~CONS[3]);  // And
  and and_15 (COND, ~WAI_U, CONE, multiplexer_1_out);  // And
  or or_9 (or_9_out, CABT, INTQ);
  and and_16 (and_16_out, ~or_9_out, COND);  // And
  Multiplexer #(.Bits(4)) multiplexer_3 (
    .sel(and_12_out), .in_0(multiplexer_2_out), .in_1(4'b0000), .out(multiplexer_3_out));
  ROM #(.AddrBits(10), .Bits(8)) INST0 (.A({OPC_d[6:0], CY}), .sel(1'b1), .D(INST0_d));
  ROM #(.AddrBits(7), .Bits(8)) INST1 (.A({OPC_d[3:0], CY}), .sel(1'b1), .D(INST1_d));
  or or_10 (LDIR_U, and_12_out, ACY0);
  Multiplexer #(.Bits(8)) multiplexer_4 (.sel(OPC_d[7]), .in_0(INST0_d), .in_1(INST1_d), .out(multiplexer_4_out));
  ROM #(.AddrBits(3), .Bits(8)) INA (.A(CY), .sel(1'b1), .D(INA_d));
  ROM #(.AddrBits(1), .Bits(8)) u_RES (.A(CY[0]), .sel(1'b1), .D(RES_d));
  or or_11 (or_11_out, CABT, COND, END);
  CE_STATE CYCLE (.R(R_U), .C(nC_U), .L(or_11_out), .IN(multiplexer_3_out), .RES(RES), .OUT({CY0, CY}));
  Register #(.Bits(8)) IR (.D(DI_U), .C(nC_U), .en(LDIR_U), .Q(A_CTRL_U[8:1]));
  Multiplexer #(.Bits(8)) multiplexer_5 (
    .sel(or_12_out), .in_0(multiplexer_4_out), .in_1(INA_d), .out(multiplexer_5_out));
  or or_12 (or_12_out, IRQ, NMI, AA_U);
  Multiplexer #(.Bits(8)) multiplexer_6 (.sel(RES), .in_0(multiplexer_5_out), .in_1(RES_d), .out(multiplexer_6_out));
  Multiplexer #(.Bits(8)) multiplexer_7 (
    .sel(ACY0), .in_0(multiplexer_6_out), .in_1({8{1'b1}}), .out(multiplexer_7_out));
  Multiplexer #(.Bits(8)) multiplexer_8 (.sel(LDIR_U), .in_0(A_CTRL_U[8:1]), .in_1(DI_U), .out(multiplexer_8_out));
  Multiplexer multiplexer_9 (.sel(LDIR_U), .in_0(A_CTRL_U[9]), .in_1(O2C), .out(multiplexer_9_out[8]));
  ROM #(.AddrBits(8), .Bits(32)) ROM32 (.A(multiplexer_7_out), .sel(1'b1), .D(ROM32_d));
  ROM #(.AddrBits(8), .Bits(12)) ROM12 (.A(multiplexer_7_out), .sel(1'b1), .D(ROM12_d));
  ROM #(.AddrBits(9), .Bits(3)) PCO (.A({multiplexer_9_out[8], multiplexer_8_out}), .sel(1'b1), .D(PCO_d));
  or or_13 (or_13_out, CY0, ROM12_d[10]);
  Multiplexer #(.Bits(32)) multiplexer_10 (
    .sel(and_18_out), .in_0(ROM32_d), .in_1({32{1'b0}}), .out({multiplexer_10_out, R_CTRL_U[28:0]}));
  Multiplexer #(.Bits(12)) multiplexer_11 (
    .sel(and_18_out), .in_0(ROM12_d), .in_1({12{1'b0}}),
    .out({END, SKIP, multiplexer_11_out[9], CONE, A_CTRL_U[0], M_CTRL_U, SPO_U}));
  Add #(.Bits(3)) add_1 (.a(3'b000), .b(PCO_d), .c_i(O2C), .s(add_1_s));  // open: c_o
  Multiplexer #(.Bits(3)) multiplexer_12 (.sel(and_17_out), .in_0(PCO_d), .in_1(3'b000), .out(PCO_U));
  and and_17 (and_17_out, INTQ, SKIP);
  and and_18 (and_18_out, CABT, ~or_13_out);  // And
  Neg #(.Bits(3)) neg_1 (.in(add_1_s), .out(neg_1_out));
  or or_14 (or_14_out, nor_1_out, IRQ);
  nor nor_1 (nor_1_out, A_CTRL_U[1], A_CTRL_U[2], A_CTRL_U[3], A_CTRL_U[4], A_CTRL_U[5], A_CTRL_U[6], A_CTRL_U[7], A_CTRL_U[8]);
  Multiplexer #(.Bits(3)) multiplexer_13 (
    .sel(AA_U), .in_0(multiplexer_10_out), .in_1(neg_1_out), .out(R_CTRL_U[31:29]));
  PriorityEncoder #(.Selector_Bits(2)) priorityencoder_1 (
    .in0(or_14_out), .in1(NMI), .in2(AA_U), .in3(RES), .num(priorityencoder_1_num), .any(INT_U));
  or or_15 (CLR, multiplexer_11_out[9], R_U);
  ROM #(.AddrBits(3), .Bits(2)) PRI (.A({INT_U, priorityencoder_1_num}), .sel(1'b1), .D(ANRI_U));

  // Other names for the same wires on the sheet: ABT = AA_U; BY = BY_U; C = C_U; DI[7:0] = DI_U;
  //   FL[5:0] = {FLI_U[6:3], FLI_U[1:0]}; LDIR = LDIR_U; nC = nC_U; OP2 = A_CTRL_U[9]; OPC[7:0] = A_CTRL_U[8:1];
  //   R = R_U; WAIT = WAI_U

  // Notes on the sheet:
  //   R_U: Reset
  //   DI_U: Data Input
  //   FLI_U: Flags Input
  //   IRQ_U: Interrupt Request
  //   NMI_U: Non-Maskable Interrupt
  //   ABT_U: Abort
  //   INT_U: Interrupt
  //   LDIR_U: Load IR
  //   A_CTRL_U: ALU Control
  //   R_CTRL_U: Register Control
  //   SPO_U: SP Offset
  //   M_CTRL_U: Memory Control
  //   PCO_U: PC Offset
  //   BY_U: DIV State Machine Busy flag
  //   WAI_U: Wait
  //   AA_U: Active Abort
  //   contents of OPC (hex, n*v repeats v):
  //   0,1c,2,2,55,17,55,55,5b,16,54,78,57,19,57,13,f,1d,1e,11,55,18,56,55,2,1b,54,69,57,
  //   1a,58,13,3,1c,4,5,43,17,55,55,62,16,54,76,45,19,57,13,10,1d,1e,12,44,18,56,55,2,1b,
  //   54,6c,46,1a,58,13,7,1c,15,54,55,17,55,55,5c,16,54,70,a,19,57,13,f,1d,1e,11,56,18,
  //   56,55,2,1b,5e,6d,79,1a,58,13,8,1c,9,6,34,17,55,55,63,16,54,74,b,19,57,13,10,1d,1e,
  //   12,38,18,56,55,2,1b,65,71,c,1a,58,13,d,2e,2d,e,33,31,32,55,6b,42,72,3e,3b,39,3a,14,
  //   f,2f,30,11,37,35,36,55,73,40,75,41,3c,3d,3f,14,21,1c,20,22,24,17,23,55,6f,16,6e,29,
  //   28,19,27,14,10,1d,1e,12,26,18,25,55,2,1b,77,2c,2b,1a,2a,14,4c,48,4d,59,4f,43,55,55,
  //   68,42,6a,5a,52,45,57,14,f,49,4a,11,50,44,56,55,2,47,5d,5f,53,46,58,14,4b,1c,1f,59,
  //   4e,17,55,55,67,16,1,5a,51,19,57,14,10,1d,1e,12,60,18,56,55,2,1b,64,66,61,1a,58,14,
  //   0,0,0,0,0,17,0,0,0,16,0,0,0,19,0,0,0,0,0,0,0,18,0,0,0,1b,0,0,0,1a,0,0,0,0,0,0,0,17,
  //   0,0,0,16,0,0,0,19,0,0,0,0,0,0,0,18,0,0,0,1b,0,7a,0,1a,0,0,0,0,0,0,0,8a,0,0,81,89,
  //   0,7b,0,8c,0,0,0,0,0,0,0,8b,0,0,0,8e,0,7c,0,8d,0,0,0,0,0,0,0,8a,0,0,82,89,0,7d,0,8c,
  //   0,0,0,0,0,0,0,8b,0,0,0,8e,0,7e,0,8d,0,0,0,85,80,0,0,0,0,0,0,0,0,0,0,0,0,0,0,87,0,
  //   0,0,0,0,0,0,0,0,0,0,0,0,0,0,0,0,0,0,0,0,0,0,0,0,0,0,0,0,0,0,0,0,0,0,0,0,0,0,0,0,0,
  //   0,0,0,0,0,0,0,0,0,0,55,0,54,0,5a,5a,0,0,57,0,0,0,0,0,0,0,56,0,0,0,0,0,0,0,58,0,0,
  //   86,7f,0,0,0,55,0,54,0,1,5a,0,0,57,83,0,86,0,0,0,0,56,0,0,0,0,0,0,0,58,84
  //   contents of CON (hex, n*v repeats v):
  //   0,0,0,0,0,0,0,0,0,0,0,0,0,0,0,8,7,0,0,7,0,0,0,0,0,0,0,0,0,0,0,9,0,0,0,0,0,0,0,0,0,
  //   0,0,0,0,0,0,a,7,0,0,7,0,0,0,0,0,0,0,0,0,0,0,b,0,0,0,0,0,0,0,0,0,0,0,0,0,0,0,c,6,0,
  //   0,6,0,0,0,0,0,0,0,0,0,0,0,d,0,0,0,0,0,0,0,0,0,0,0,0,0,0,0,e,6,0,0,6,0,0,0,0,0,0,0,
  //   0,0,0,0,f,0,0,0,0,0,0,0,0,0,0,0,0,0,0,0,8,4,0,0,4,0,0,0,0,0,0,0,0,0,0,0,9,0,0,0,0,
  //   0,0,0,0,0,0,0,0,0,0,0,a,4,0,0,4,0,0,0,0,0,0,0,0,0,0,0,b,0,0,0,0,0,0,0,0,0,0,0,0,0,
  //   0,0,c,5,0,0,5,0,0,0,0,0,0,0,0,0,0,0,d,0,0,0,0,0,0,0,0,0,0,0,0,0,0,0,e,5,0,0,5,0,0,
  //   0,0,0,0,0,0,0,0,0,f,0,0,0,0,0,0,0,0,0,0,0,0,0,0,0,0,0,0,0,0,0,0,0,0,0,0,0,0,0,0,0,
  //   0,0,0,0,0,0,0,0,0,0,0,0,0,0,0,0,0,0,0,0,0,0,0,0,0,0,0,0,0,0,0,0,0,0,0,0,0,0,2,0,0,
  //   0,2,0,0,0,2,0,0,0,0,0,0,0,2,0,0,0,2,0,0,0,2,0,0,0,0,0,0,0,2,0,0,0,2,0,0,0,2,0,0,0,
  //   0,0,0,0,2,0,0,0,2,0,0,0,2,0,0,0,0,0,0,0,0,0,0,0,0,0,0,0,0,0,0,0,0,0,0,0,0,0,0,0,0,
  //   0,0,0,0,0,0,0,0,0,0,0,0,0,0,0,0,0,0,0,0,0,0,0,0,0,0,0,0,0,0,0,0,0,0,0,0,0,0,0,0,0,
  //   0,0,0,0,0,0,0,0,0,0,0,0,0,0,0,0,0,0,0,0,0,0,0,0,0,0,0,0,0,0,0,0,0,0,0,0,0,0,0,0,0,
  //   0,0,0,3
  //   contents of INST0 (hex, n*v repeats v):
  //   93,89,8d,79,32,0,0,0,6f,0,0,0,0,0,0,0,e,0,0,0,0,0,0,0,94,8a,76,2c,0,0,0,0,3c,37,94,
  //   8a,77,30,0,0,3c,37,94,8a,78,31,0,0,94,8a,76,1,0,0,0,0,8,44,2e,72,0,0,0,0,43,2d,71,
  //   0,0,0,0,0,3b,45,2f,7b,0,0,0,0,42,2c,0,0,0,0,0,0,3c,37,46,30,0,0,0,0,3c,37,48,31,0,
  //   0,0,0,2,0,0,0,0,0,0,0,42,1,0,0,0,0,0,0,4,2,0,0,0,6f,0,0,4,6f,0,0,0,2,0,0,4,42,1,0,
  //   0,6f,0,0,4,6f,0,0,0,42,1,0,42,3,2,6f,0,0,0,0,42,3,6f,2,0,0,0,0,f,0,0,0,0,0,0,0,1e,
  //   0,0,0,0,0,0,0,41,1c,0,0,0,0,0,0,41,1d,0,0,0,0,0,0,3c,37,21,0,0,0,0,0,3c,37,22,0,0,
  //   0,0,0,3c,37,23,0,0,0,0,0,41,3a,36,21,0,0,0,0,41,39,35,23,0,0,0,0,41,39,35,24,0,0,
  //   0,0,41,3d,38,23,0,0,0,0,52,0,0,0,0,0,0,0,5d,0,0,0,0,0,0,0,67,0,0,0,0,0,0,0,41,50,
  //   0,0,0,0,0,0,41,5b,0,0,0,0,0,0,41,51,0,0,0,0,0,0,41,5c,0,0,0,0,0,0,3c,37,54,0,0,0,
  //   0,0,3c,37,5f,0,0,0,0,0,3c,37,69,0,0,0,0,0,3c,37,55,0,0,0,0,0,3c,37,60,0,0,0,0,0,3c,
  //   37,6a,0,0,0,0,0,41,3d,38,a5,0,0,0,0,41,3a,36,9b,0,0,0,0,41,39,35,a5,0,0,0,0,41,39,
  //   35,a7,0,0,0,0,41,81,0,0,0,0,0,0,41,82,0,0,0,0,0,0,41,83,0,0,0,0,0,0,41,84,0,0,0,0,
  //   0,0,41,85,0,0,0,0,0,0,41,88,0,0,0,0,0,0,41,86,0,0,0,0,0,0,41,87,0,0,0,0,0,0,3c,37,
  //   9b,0,0,0,0,0,3c,37,9e,0,0,0,0,0,3c,37,9f,0,0,0,0,0,3c,37,a0,0,0,0,0,0,3c,37,a1,0,
  //   0,0,0,0,3c,37,a3,0,0,0,0,0,3c,37,a4,0,0,0,0,0,3c,37,a5,0,0,0,0,0,3c,37,a6,0,0,0,0,
  //   0,7,0,0,0,0,0,0,0,41,5,0,0,0,0,0,0,41,6,0,0,0,0,0,0,3c,37,a,0,0,0,0,0,3c,37,b,0,0,
  //   0,0,0,3c,37,c,0,0,0,0,0,41,3a,36,a,0,0,0,0,41,39,35,c,0,0,0,0,41,39,35,d,0,0,0,0,
  //   13,0,0,0,0,0,0,0,16,0,0,0,0,0,0,0,19,0,0,0,0,0,0,0,41,12,0,0,0,0,0,0,41,15,0,0,0,
  //   0,0,0,41,18,0,0,0,0,0,0,3c,37,14,0,0,0,0,0,3c,37,17,0,0,0,0,0,3c,37,1a,0,0,0,0,0,
  //   25,0,0,0,0,0,0,0,3b,49,7f,0,0,0,0,0,3b,4a,80,0,0,0,0,0,3c,37,4b,9d,0,0,0,0,3c,37,
  //   4c,a2,0,0,0,0,3b,40,4d,7e,7d,0,0,0,3c,37,47,4e,9c,9a,0,0,92,74,0,0,0,0,0,0,91,74,
  //   0,0,0,0,0,0,96,74,0,0,0,0,0,0,97,74,0,0,0,0,0,0,98,74,0,0,0,0,0,0,42,3e,95,8b,75,
  //   0,0,0,3c,37,46,3f,95,8b,75,0,8,70,0,0,0,0,0,0,1f,70,0,0,0,0,0,0,53,70,0,0,0,0,0,0,
  //   5e,70,0,0,0,0,0,0,68,70,0,0,0,0,0,0,58,0,0,0,0,0,0,0,63,0,0,0,0,0,0,0,6c,0,0,0,0,
  //   0,0,0,58,0,0,0,0,0,0,0,63,0,0,0,0,0,0,0,6c,0,0,0,0,0,0,0,2b,0,0,0,0,0,0,0,56,0,0,
  //   0,0,0,0,0,61,0,0,0,0,0,0,0,6b,0,0,0,0,0,0,0,26,0,0,0,0,0,0,0,27,0,0,0,0,0,0,0,28,
  //   0,0,0,0,0,0,0,29,0,0,0,0,0,0,0,34,0,0,0,0,0,0,0,33,0,0,0,0,0,0,0,57,0,0,0,0,0,0,0,
  //   62,0,0,0,0,0,0,0,6f,0,0,0,0,0,0,0,10,0,0,0,0,0,0,0,11,0,0,0,0,0,0,0,65,59,0,0,0,0,
  //   0,0,6d,59,0,0,0,0,0,0,6e,64,0,0,0,0,0,0,20
  //   contents of INST1 (hex, n*v repeats v):
  //   99,0,0,0,0,0,0,0,98,8c,8e,8f,90,7a,0,0,1b,2a,4f,5a,66,73,0,0,7c,0,0,0,0,0,0,0,4,0,
  //   0,0,0,4,0,0,41,3a,36,23,0,0,0,0,41,3a,36,9b,0,0,0,0,aa,0,0,0,0,0,0,0,ab,0,0,0,0,0,
  //   0,0,ad,0,0,0,0,4,ac,0,41,ae,0,0,0,4,ac,0,41,af,0,0,0,4,ac,0,3c,37,b0,0,0,4,ac,0,3c,
  //   37,b1,0,0,4,ac,0,3c,37,b2,0,0,4,ac
  //   contents of INA (hex, n*v repeats v):
  //   93,89,8d,79,a9
  //   contents of RES (hex, n*v repeats v):
  //   79,a9
  //   contents of ROM32 (hex, n*v repeats v):
  //   0,e6000000,e5000000,5000,1000,5018,6018,e0000018,b018,b018,1018,2018,3018,4018,4000000,
  //   4800c1c,4800e1c,4800a1c,5019,e0000019,1019,501a,e000001a,101a,501b,e000001b,101b,
  //   80b000,805218,806218,e0800218,80b218,80c218,801218,802218,803218,804218,4800200,4800204,
  //   4800208,480020c,4800210,90b000,4900200,e7000000,7f0b000,700b000,7f0e000,27001000,
  //   27002000,700f000,14f00000,cf00000,20d05000,20d06000,e0d00000,d0d000,e05000,e06000,
  //   e0e00000,c0e00000,e0d000,e0080000,20081000,48000,e0040000,c0040000,4b000,4b000,4e000,
  //   41000,41000,42000,58018,59018,51018,52018,200d8018,200d1018,a0b000,a05218,a07218,
  //   e0a00218,a0b218,a01218,a03218,4a00200,4a00214,4a00208,4a00400,b0b000,b05218,b06218,
  //   e0b00218,b0b218,b01218,b02218,4b00200,4b00214,4b0020c,4b00400,b60600,c0b000,e0c00218,
  //   c0b218,c01218,c02218,4c00200,4c00210,c70600,c70800,4000000,1c000000,1c000000,1c000000,
  //   1c000000,1c000000,1c000000,d8040000,18041000,18042000,1804f000,1c000000,1c000200,
  //   0,200080e0,80c0,80c0,90c0,5000,5040,5060,5080,6000,6060,6080,7040,b100,e000b100,b0c0,
  //   b060,b0a0,b040,b020,b000,b000,b0a0,b120,e000b120,b0e0,b040,b060,b080,c000,200010e0,
  //   1000,10c0,10c0,1040,1060,1080,2000,20c0,2060,2080,3000,3040,4000,b0a0,700f000,80a218,
  //   a000,800200,e0000018,5018,6018,1018,2018,3018,0,0,0,0,0,0,0,0,0,0,0,0,0,0,0,0,0,0,
  //   0,0,0,0,0,0,0,0,0,0,0,0,0,0,0,0,0,0,0,0,0,0,0,0,0,0,0,0,0,0,0,0,0,0,0,0,0,0,0,0,0,
  //   0,0,0,0,0,0,0,0,0,0,0,0,0,0,0,0,0,4000000
  //   contents of ROM12 (hex, n*v repeats v):
  //   0,800,800,100,100,880,880,880,81,881,880,880,880,880,c80,c80,c80,c80,880,880,880,
  //   880,880,880,880,880,880,1,880,880,880,81,880,880,880,880,880,c80,c80,c80,c80,c80,
  //   2,c00,800,2,3,2,800,800,800,c00,c00,0,0,0,2,0,0,0,0,1,0,0,20,0,0,1,2,1,0,20,0,a0,
  //   a0,a0,a0,a0,a0,3,880,880,880,81,880,880,c80,c80,c80,c00,4,880,880,880,881,880,880,
  //   c80,c80,c80,c00,0,5,880,81,880,880,c80,c80,0,0,c00,c01,c02,c03,c05,c0f,c0e,e,e,e,
  //   d,c0b,c02,100,830,30,830,830,810,810,810,810,810,810,810,810,1f,1f,1f,1f,1e,1e,1d,
  //   1c,10,10,10,10,10,10,10,10,810,830,810,30,830,810,810,810,810,830,810,810,810,810,
  //   810,5e,a00,880,810,c00,80,80,80,80,80,80
  //   contents of PCO (hex, n*v repeats v):
  //   2,2,1,1,2,2,2,2,1,2,1,1,3,3,3,3,2,2,2,3,2,2,2,2,1,3,1,1,3,3,3,3,3,2,3,3,2,2,2,2,1,
  //   2,1,1,3,3,3,3,2,2,2,3,2,2,2,2,1,3,1,1,3,3,3,3,1,2,1,1,2,2,2,2,1,2,1,1,3,3,3,3,2,2,
  //   2,3,2,2,2,2,1,3,1,1,1,3,3,3,1,2,2,3,2,2,2,2,1,2,1,1,3,3,3,3,2,2,2,3,2,2,2,2,1,3,1,
  //   1,3,3,3,3,2,2,2,3,2,2,2,2,1,2,1,3,3,3,3,3,2,2,2,3,2,2,2,2,1,3,1,3,3,3,3,3,2,2,2,2,
  //   2,2,2,2,1,2,1,3,3,3,3,3,2,2,2,3,2,2,2,2,1,3,1,3,3,3,3,3,2,2,2,2,2,2,2,2,1,2,1,3,3,
  //   3,3,3,2,2,2,3,2,2,2,2,1,3,1,1,3,3,3,3,2,2,2,2,2,2,2,2,1,2,1,3,3,3,3,3,2,2,2,3,3,2,
  //   2,2,1,3,1,1,3,3,3,3,0,0,0,0,0,2,0,0,0,2,0,0,0,3,0,0,0,0,0,0,0,2,0,0,0,3,0,0,0,3,0,
  //   0,0,0,0,0,0,2,0,0,0,2,0,0,0,3,0,0,0,0,0,0,0,2,0,0,0,3,0,1,0,3,0,0,0,0,0,0,0,2,0,0,
  //   1,2,0,1,0,3,0,0,0,0,0,0,0,2,0,0,0,3,0,1,0,3,0,0,0,0,0,0,0,2,0,0,1,2,0,1,0,3,0,0,0,
  //   0,0,0,0,2,0,0,0,3,0,1,0,3,0,0,0,2,1,0,0,0,0,0,0,0,0,0,0,0,0,0,0,1,0,0,0,0,0,0,0,0,
  //   0,0,0,0,0,0,0,0,0,0,0,0,0,0,0,0,0,0,0,0,0,0,0,0,0,0,0,0,0,0,0,0,0,0,0,0,0,0,0,0,0,
  //   0,0,0,2,0,1,0,3,3,0,0,3,0,0,0,0,0,0,0,2,0,0,0,0,0,0,0,3,0,0,2,1,0,0,0,2,0,1,0,0,3,
  //   0,0,3,1,0,1,0,0,0,0,2,0,0,0,0,0,0,0,3,1
  //   contents of PRI (hex, n*v repeats v):
  //   0,3,0,1,0,0,0,2
endmodule
