// Digital circuit CE_M_REGS.dig as structural Verilog
module CE_M_REGS (
  input  R_R,
  input  nC_R,
  input  [7:0] DI_R,
  input  [15:0] ALUI_R,
  input  [7:0] RNDI_R,
  input  [7:0] FLI_R,
  input  [1:0] ANRI_R,
  input  [31:0] R_CTRL_R,
  input  [2:0] PCO_R,
  input  [3:0] SPO_R,
  output [7:0] ALA_R,
  output [15:0] ALB_R,
  output [7:0] DO_R,
  output VPA_R,
  output VBA_R,
  output VSA_R,
  output VVA_R,
  output [15:0] AO_R
);

  wire and_1_out, and_2_out, and_4_out, decoder_1_out_0, demultiplexer_1_out_0, demultiplexer_1_out_1,
       demultiplexer_1_out_2, demultiplexer_1_out_4, demultiplexer_1_out_5, demultiplexer_1_out_6, SPS, YEN;
  wire [1:0] or_1_out;
  wire [1:1] and_3_out;
  wire [4:0] AOS_d;
  wire [7:0] A, add_3_s, add_4_s, B, multiplexer_1_out, multiplexer_5_out, multiplexer_6_out,
       multiplexer_7_out, multiplexer_8_out, multiplexer_9_out, multiplexer_10_out, multiplexer_11_out,
       multiplexer_12_out, multiplexer_13_out, multiplexer_14_out, multiplexer_15_out, multiplexer_17_out,
       multiplexer_18_out, multiplexer_19_out, neg_1_out, REG, TBH, TBL, X, Y, Z;
  wire [15:0] add_1_s, add_2_s, add_5_s, add_6_s, add_7_s, add_8_s, bitextender_3_out, bitextender_4_out,
       multiplexer_2_out, multiplexer_4_out, multiplexer_16_out, multiplexer_21_out, OFS, PC, SP, SPN, SPO,
       TA;

  BitExtender #(.inputBits(4)) bitextender_1 (.in(SPO_R), .out(SPO));
  BitExtender #(.inputBits(3)) bitextender_2 (.in(R_CTRL_R[31:29]), .out(OFS));
  Neg #(.Bits(8)) neg_1 (.in(A), .out(neg_1_out));
  Multiplexer #(.Bits(8)) multiplexer_1 (
    .sel(R_CTRL_R[24]), .in_0({{5{1'b0}}, PCO_R}), .in_1(DI_R), .out(multiplexer_1_out));
  Multiplexer #(.Bits(16)) multiplexer_2 (.sel(and_1_out), .in_0(PC), .in_1({16{1'b0}}), .out(multiplexer_2_out));
  BitExtender bitextender_3 (.in(multiplexer_1_out), .out(bitextender_3_out));
  Multiplexer #(.Selector_Bits(3), .Bits(8)) multiplexer_3 (
    .sel(R_CTRL_R[11:9]), .in_0(DI_R), .in_1(ALUI_R[7:0]), .in_2(TBL), .in_3(X), .in_4(Y),
    .in_5({A[3:0], A[7:4]}), .in_6(neg_1_out), .in_7(RNDI_R), .out(REG));
  Demultiplexer #(.Selector_Bits(3)) demultiplexer_1 (
    .sel(R_CTRL_R[22:20]), .in(R_CTRL_R[23]), .out_0(demultiplexer_1_out_0), .out_1(demultiplexer_1_out_1),
    .out_2(demultiplexer_1_out_2), .out_3(YEN), .out_4(demultiplexer_1_out_4), .out_5(demultiplexer_1_out_5),
    .out_6(demultiplexer_1_out_6), .out_7(SPS));
  and and_1 (and_1_out, R_CTRL_R[25], R_CTRL_R[24]);
  Multiplexer #(.Bits(16)) multiplexer_4 (
    .sel(R_CTRL_R[25]), .in_0(bitextender_3_out), .in_1({DI_R, TBL}), .out(multiplexer_4_out));
  and and_2 (and_2_out, SPS, R_CTRL_R[24], R_CTRL_R[25]);
  Add #(.Bits(16)) add_1 (.a(multiplexer_2_out), .b(multiplexer_4_out), .c_i(and_2_out), .s(add_1_s));  // open: c_o
  Multiplexer #(.Bits(8)) multiplexer_5 (.sel(R_CTRL_R[9]), .in_0(DI_R), .in_1(A), .out(multiplexer_5_out));
  Multiplexer #(.Bits(8)) multiplexer_6 (.sel(R_CTRL_R[16]), .in_0(DI_R), .in_1(ALUI_R[15:8]), .out(multiplexer_6_out));
  Multiplexer #(.Selector_Bits(2), .Bits(8)) multiplexer_7 (
    .sel(R_CTRL_R[17:16]), .in_0(DI_R), .in_1(ALUI_R[7:0]), .in_2(Y), .in_3(Z), .out(multiplexer_7_out));
  Multiplexer #(.Bits(8)) multiplexer_8 (.sel(SPS), .in_0(SPN[15:8]), .in_1(Y), .out(multiplexer_8_out));
  Multiplexer #(.Bits(8)) multiplexer_9 (.sel(SPS), .in_0(SPN[7:0]), .in_1(X), .out(multiplexer_9_out));
  CE_PRE u_A (.R(R_R), .C(nC_R), .L(demultiplexer_1_out_0), .IN(REG), .PR({8{1'b0}}), .Q(A));
  CE_PRE u_B (.R(R_R), .C(nC_R), .L(demultiplexer_1_out_1), .IN(multiplexer_5_out), .PR({8{1'b0}}), .Q(B));
  CE_PRE u_X (.R(R_R), .C(nC_R), .L(demultiplexer_1_out_2), .IN(REG), .PR({8{1'b0}}), .Q(X));
  CE_PRE u_Y (.R(R_R), .C(nC_R), .L(YEN), .IN(REG), .PR({8{1'b0}}), .Q(Y));
  CE_PRE u_Z (.R(R_R), .C(nC_R), .L(demultiplexer_1_out_4), .IN(REG), .PR({8{1'b0}}), .Q(Z));
  CE_PRE TAH (.R(R_R), .C(nC_R), .L(demultiplexer_1_out_5), .IN(DI_R), .PR({8{1'b0}}), .Q(TA[15:8]));
  CE_PRE TAL (.R(R_R), .C(nC_R), .L(demultiplexer_1_out_6), .IN(DI_R), .PR({8{1'b0}}), .Q(TA[7:0]));
  CE_PRE u_TBH (.R(R_R), .C(nC_R), .L(R_CTRL_R[19]), .IN(multiplexer_6_out), .PR({8{1'b0}}), .Q(TBH));
  CE_PRE u_TBL (.R(R_R), .C(nC_R), .L(R_CTRL_R[18]), .IN(multiplexer_7_out), .PR({8{1'b0}}), .Q(TBL));
  CE_PRE SPH (.R(R_R), .C(nC_R), .L(R_CTRL_R[28]), .IN(multiplexer_8_out), .PR(8'h1), .Q(SP[15:8]));
  CE_PRE SPL (.R(R_R), .C(nC_R), .L(R_CTRL_R[27]), .IN(multiplexer_9_out), .PR({8{1'b0}}), .Q(SP[7:0]));
  Register #(.Bits(16), .isProgramCounter("true")) u_PC (.D(add_1_s), .C(nC_R), .en(R_CTRL_R[26]), .Q(PC));
  ROM #(.AddrBits(4), .Bits(5)) AOS (.A(R_CTRL_R[15:12]), .sel(1'b1), .D(AOS_d));
  and and_3 (and_3_out[1], R_CTRL_R[28], R_CTRL_R[9], R_CTRL_R[27]);
  Multiplexer #(.Selector_Bits(2), .Bits(8)) multiplexer_10 (
    .sel(or_1_out), .in_0({8{1'b0}}), .in_1(X), .in_2(Y), .in_3(Z), .out(multiplexer_10_out));
  assign or_1_out = {2{and_3_out[1]}} | AOS_d[4:3];  // Or or_1, 2 bits wide
  Multiplexer #(.Selector_Bits(2), .Bits(8)) multiplexer_11 (
    .sel(or_1_out), .in_0({8{1'b0}}), .in_1(Y), .in_2(TBL), .in_3(TA[7:0]), .out(multiplexer_11_out));
  Multiplexer #(.Bits(8)) multiplexer_12 (.sel(AOS_d[2]), .in_0(TBL), .in_1(TA[7:0]), .out(multiplexer_12_out));
  Multiplexer #(.Bits(8)) multiplexer_13 (
    .sel(and_4_out), .in_0(SP[7:0]), .in_1(multiplexer_10_out), .out(multiplexer_13_out));
  Multiplexer #(.Bits(8)) multiplexer_14 (
    .sel(and_4_out), .in_0(multiplexer_11_out), .in_1(multiplexer_12_out), .out(multiplexer_14_out));
  and and_4 (and_4_out, AOS_d[0], ~AOS_d[1]);  // And
  BitExtender bitextender_4 (.in(multiplexer_10_out), .out(bitextender_4_out));
  Add #(.Bits(16)) add_2 (.a(TA), .b(bitextender_4_out), .c_i(1'b0), .s(add_2_s));  // open: c_o
  Multiplexer #(.Bits(8)) multiplexer_15 (.sel(and_4_out), .in_0(SPO[7:0]), .in_1(OFS[7:0]), .out(multiplexer_15_out));
  Add #(.Bits(8)) add_3 (.a(multiplexer_13_out), .b(multiplexer_14_out), .c_i(1'b0), .s(add_3_s));  // open: c_o
  Multiplexer #(.Bits(16)) multiplexer_16 (.sel(AOS_d[2]), .in_0(PC), .in_1(add_2_s), .out(multiplexer_16_out));
  Multiplexer #(.Bits(8)) multiplexer_17 (.sel(and_4_out), .in_0(SP[15:8]), .in_1(B), .out(multiplexer_17_out));
  Add #(.Bits(8)) add_4 (.a(multiplexer_15_out), .b(add_3_s), .c_i(1'b0), .s(add_4_s));  // open: c_o
  Add #(.Bits(16)) add_5 (.a({{8{1'b0}}, multiplexer_14_out}), .b(SPO), .c_i(1'b0), .s(add_5_s));  // open: c_o
  Add #(.Bits(16)) add_6 (.a(16'hfff8), .b({{13{1'b0}}, ANRI_R, 1'b0}), .c_i(R_CTRL_R[26]), .s(add_6_s));  // open: c_o
  Add #(.Bits(16)) add_7 (.a(PC), .b({X, Y}), .c_i(1'b0), .s(add_7_s));  // open: c_o
  Add #(.Bits(16)) add_8 (.a(multiplexer_16_out), .b(OFS), .c_i(1'b0), .s(add_8_s));  // open: c_o
  Multiplexer #(.Bits(8)) multiplexer_18 (.sel(YEN), .in_0(SP[7:0]), .in_1(SP[15:8]), .out(multiplexer_18_out));
  Multiplexer #(.Bits(8)) multiplexer_19 (.sel(R_CTRL_R[19]), .in_0(DI_R), .in_1(TBL), .out(multiplexer_19_out));
  Multiplexer #(.Bits(16)) multiplexer_20 (
    .sel(FLI_R[5]), .in_0(add_5_s), .in_1({multiplexer_17_out, add_4_s}), .out(SPN));
  Multiplexer #(.Bits(16)) multiplexer_21 (.sel(AOS_d[2]), .in_0(add_6_s), .in_1(add_7_s), .out(multiplexer_21_out));
  Decoder #(.Selector_Bits(2)) decoder_1 (
    .sel(AOS_d[1:0]), .out_0(decoder_1_out_0), .out_1(VBA_R), .out_2(VSA_R), .out_3(VVA_R));
  Multiplexer #(.Selector_Bits(2), .Bits(16)) multiplexer_22 (
    .sel(AOS_d[1:0]), .in_0(add_8_s), .in_1({multiplexer_17_out, add_4_s}), .in_2(SPN),
    .in_3(multiplexer_21_out), .out(AO_R));
  Multiplexer #(.Selector_Bits(2), .Bits(8)) multiplexer_23 (
    .sel(R_CTRL_R[1:0]), .in_0(A), .in_1(X), .in_2(Y), .in_3(Z), .out(ALA_R));
  Multiplexer #(.Selector_Bits(3), .Bits(8)) multiplexer_24 (
    .sel(R_CTRL_R[4:2]), .in_0(A), .in_1(B), .in_2(X), .in_3(Y), .in_4(Z), .in_5(multiplexer_18_out),
    .in_6(multiplexer_19_out), .in_7(REG), .out(ALB_R[7:0]));
  Multiplexer #(.Selector_Bits(4), .Bits(8)) multiplexer_25 (
    .sel(R_CTRL_R[8:5]), .in_0(A), .in_1(B), .in_2(X), .in_3(Y), .in_4(Z), .in_5(FLI_R), .in_6(TBL),
    .in_7(TBH), .in_8(add_8_s[7:0]), .in_9(add_8_s[15:8]), .in_10({8{1'b0}}), .in_11({8{1'b0}}),
    .in_12({8{1'b0}}), .in_13({8{1'b0}}), .in_14({8{1'b0}}), .in_15({8{1'b0}}), .out(DO_R));
  and and_5 (VPA_R, ~AOS_d[2], decoder_1_out_0);  // And

  assign ALB_R[15:8] = DI_R;

  // Other names for the same wires on the sheet: ALIL[7:0] = ALUI_R[7:0]; ALIH[7:0] = ALUI_R[15:8];
  //   ANRI[1:0] = ANRI_R; DI[7:0] = DI_R; FL[7:0] = FLI_R; nEF = FLI_R[5]; nC = nC_R; OFS8[7:0] = OFS[7:0];
  //   PCO[2:0] = PCO_R; R = R_R; ALAS[1:0] = R_CTRL_R[1:0]; ALBS[2:0] = R_CTRL_R[4:2]; DOS[3:0] = R_CTRL_R[8:5];
  //   RGS[2:0] = R_CTRL_R[11:9]; AOS[3:0] = R_CTRL_R[15:12]; TBS[1:0] = R_CTRL_R[17:16]; LBL = R_CTRL_R[18];
  //   LBH = R_CTRL_R[19]; LRS[2:0] = R_CTRL_R[22:20]; LRE = R_CTRL_R[23]; PCS[1:0] = R_CTRL_R[25:24];
  //   LPC = R_CTRL_R[26]; LSL = R_CTRL_R[27]; LSH = R_CTRL_R[28]; RND[7:0] = RNDI_R; SPH[7:0] = SP[15:8];
  //   SPL[7:0] = SP[7:0]; SPO8[7:0] = SPO[7:0]; TAL[7:0] = TA[7:0]

  // Notes on the sheet:
  //   R_R: Reset
  //   DI_R: Data Input
  //   ALUI_R: ALU Input
  //   RNDI_R: LSFR Input
  //   FLI_R: Flag/Status Input
  //   ALA_R: ALU A Output
  //   ALB_R: ALU B Output
  //   DO_R: Data Output
  //   VPA_R: Valid Program Address
  //   VBA_R: Valid Base Page Address
  //   VSA_R: Valid Stack Address
  //   VVA_R: Valid Vector Address
  //   AO_R: Address Output
  //   ANRI_R: ABT/NMI/RES/IRQ Input
  //   R_CTRL_R: Rregister Control Input
  //   PCO_R: PC Offset Input
  //   SPO_R: SP Offset Input
  //   contents of AOS (hex, n*v repeats v):
  //   0,4,c,14,1c,1,9,11,5,d,7,2,a,12,1a,3
endmodule
