// Digital circuit CE_NZ.dig as structural Verilog
module CE_NZ (
  input  [7:0] IN,
  output Q
);

  or or_1 (Q, IN[0], IN[1], IN[2], IN[3], IN[4], IN[5], IN[6], IN[7]);

  // Notes on the sheet:
  //   IN: Input
  //   Q: Output
endmodule
