// Digital circuit CE_PRE.dig as structural Verilog
module CE_PRE (
  input  R,
  input  C,
  input  L,
  input  [7:0] IN,
  input  [7:0] PR,
  output [7:0] Q
);

  wire d_ff_1_nq, multiplexer_1_out, multiplexer_2_out, or_1_out;
  wire [7:0] REG_q;

  or or_1 (or_1_out, L, R);
  Multiplexer multiplexer_1 (.sel(d_ff_1_nq), .in_0(1'b1), .in_1(L), .out(multiplexer_1_out));
  Multiplexer multiplexer_2 (.sel(R), .in_0(multiplexer_1_out), .in_1(1'b0), .out(multiplexer_2_out));
  Register #(.Bits(8)) REG (.D(IN), .C(C), .en(or_1_out), .Q(REG_q));
  D_FF d_ff_1 (.D(multiplexer_2_out), .C(C), .nQ(d_ff_1_nq));  // open: Q
  Multiplexer #(.Bits(8)) multiplexer_3 (.sel(d_ff_1_nq), .in_0(REG_q), .in_1(PR), .out(Q));
endmodule
