// Digital circuit CE_SRL.dig as structural Verilog
module CE_SRL (
  input  C_i,
  input  [15:0] IN,
  input  SEL,
  output C_o,
  output [7:0] Q,
  output [7:0] QH
);

  Multiplexer multiplexer_1 (.sel(SEL), .in_0(IN[7]), .in_1(IN[15]), .out(C_o));

  assign Q = {IN[6:0], C_i};
  assign QH = IN[14:7];

  // Notes on the sheet:
  //   C_i: Carry In
  //   C_o: Carry Out
  //   IN: Input
  //   Q: Output Low
  //   QH: Output High
  //   SEL: 8/16 bit Select
endmodule
