// Digital circuit CE_SRR.dig as structural Verilog
module CE_SRR (
  input  C_i,
  input  [15:0] IN,
  input  SEL,
  output C_o,
  output [7:0] Q,
  output [7:0] QH
);

  Multiplexer multiplexer_1 (.sel(SEL), .in_0(C_i), .in_1(IN[8]), .out(Q[7]));
  // Probe on {C_i, IN[15:9], Q[7], IN[7:1]}

  assign C_o = IN[0];
  assign Q[6:0] = IN[7:1];
  assign QH = {C_i, IN[15:9]};

  // Notes on the sheet:
  //   C_i: Carry In
  //   C_o: Carry Out
  //   IN: Input
  //   Q: Output Low
  //   QH: Output High
  //   SEL: 8/16 bit Select
endmodule
