// Digital circuit CE_STATE.dig as structural Verilog
module CE_STATE (
  input  R,
  input  C,
  input  L,
  input  [3:0] IN,
  output RES,
  output [3:0] OUT
);

  wire and_1_out;

  and and_1 (and_1_out, L, ~R);  // And
  JK_FF jk_ff_1 (.J(and_1_out), .C(C), .K(R), .nQ(RES));  // open: Q
  CounterPreset #(.Bits(4)) counterpreset_1 (
    .en(1'b1), .C(C), .dir(1'b0), .in(IN), .ld(L), .clr(R), .out(OUT));  // open: ovf
endmodule
