// Digital circuit CE_4t5.dig as structural Verilog
module CE_4t5 (
  input  N_0,
  input  N_1,
  input  N_2,
  input  N_3,
  output O_0,
  output O_1,
  output O_2,
  output O_3,
  output O_4
);

  wire and_1_out, multiplexer_2_out, or_1_out, or_2_out, or_3_out, xnor_1_out, xnor_2_out, xor_2_out,
       xor_3_out;

  xor xor_1 (O_0, O_3, N_0);
  xor xor_2 (xor_2_out, O_4, N_1);
  xnor xnor_1 (xnor_1_out, N_1, N_0);
  xnor xnor_2 (xnor_2_out, N_2, N_1);
  or or_1 (or_1_out, N_0, N_1);
  or or_2 (or_2_out, N_1, N_2);
  Multiplexer multiplexer_1 (.sel(O_3), .in_0(xor_2_out), .in_1(xnor_1_out), .out(O_1));
  Multiplexer multiplexer_2 (.sel(O_4), .in_0(N_2), .in_1(xnor_2_out), .out(multiplexer_2_out));
  xor xor_3 (xor_3_out, multiplexer_2_out, or_1_out);
  and and_1 (and_1_out, or_1_out, N_2);
  and and_2 (O_4, or_2_out, N_3);
  Multiplexer multiplexer_3 (.sel(O_3), .in_0(multiplexer_2_out), .in_1(xor_3_out), .out(O_2));
  or or_3 (or_3_out, N_3, and_1_out);
  xor xor_4 (O_3, or_3_out, O_4);

  // Other names for the same wires on the sheet: F = O_3; X = O_4
endmodule
