// Digital circuit CE_5t5.dig as structural Verilog
module CE_5t5 (
  input  N_0,
  input  N_1,
  input  N_2,
  input  N_3,
  input  N_4,
  output O_0,
  output O_1,
  output O_2,
  output O_3,
  output O_4
);

  wire and_1_out, and_2_out, and_3_out, and_4_out, and_5_out, multiplexer_1_out, multiplexer_3_out,
       multiplexer_4_out, not_1_out, or_1_out, or_2_out, or_3_out, S, xnor_1_out, xnor_2_out, xor_2_out,
       xor_3_out, xor_4_out, xor_5_out;

  xnor xnor_1 (xnor_1_out, N_2, N_1);
  or or_1 (or_1_out, N_0, N_1);
  and and_1 (and_1_out, N_0, N_1);
  or or_2 (or_2_out, N_1, N_2);
  xor xor_1 (O_0, O_3, N_0);
  xor xor_2 (xor_2_out, O_4, N_1);
  xnor xnor_2 (xnor_2_out, N_1, N_0);
  and and_2 (and_2_out, or_1_out, N_2);
  and and_3 (and_3_out, or_2_out, N_3);
  Multiplexer multiplexer_1 (.sel(O_3), .in_0(xor_2_out), .in_1(xnor_2_out), .out(multiplexer_1_out));
  not not_1 (not_1_out, xnor_2_out);
  xor xor_3 (xor_3_out, N_2, or_1_out);
  xor xor_4 (xor_4_out, N_2, and_1_out);
  and and_4 (and_4_out, and_1_out, N_2);
  or or_3 (or_3_out, and_2_out, N_3);
  or or_4 (O_4, and_3_out, N_4);
  Multiplexer multiplexer_2 (.sel(S), .in_0(multiplexer_1_out), .in_1(not_1_out), .out(O_1));
  Multiplexer multiplexer_3 (.sel(O_4), .in_0(N_2), .in_1(xnor_1_out), .out(multiplexer_3_out));
  Multiplexer multiplexer_4 (.sel(O_3), .in_0(multiplexer_3_out), .in_1(xor_3_out), .out(multiplexer_4_out));
  and and_5 (and_5_out, and_4_out, N_3);
  Multiplexer multiplexer_5 (.sel(S), .in_0(multiplexer_4_out), .in_1(xor_4_out), .out(O_2));
  xor xor_5 (xor_5_out, or_3_out, O_4);
  or or_5 (S, and_5_out, N_4);
  or or_6 (O_3, and_5_out, xor_5_out);

  // Other names for the same wires on the sheet: T = O_3; X = O_4
endmodule
