// Digital circuit CE_CBH.dig as structural Verilog
module CE_CBH (
  input  [7:0] I,
  output [7:0] Q,
  output C_O
);

  wire comparator_1_lt, comparator_2_gt;
  wire [7:0] add_1_s;

  Comparator #(.Bits(4)) comparator_1 (.a(4'b1001), .b(I[3:0]), .lt(comparator_1_lt));  // open: gt, eq
  Comparator #(.Bits(4)) comparator_2 (.a(I[7:4]), .b(4'b1001), .gt(comparator_2_gt));  // open: eq, lt
  or or_1 (C_O, comparator_1_lt, comparator_2_gt);
  Add #(.Bits(8)) add_1 (.a({3'b000, I[7:4], 1'b0}), .b({1'b0, I[7:4], 3'b000}), .c_i(1'b0), .s(add_1_s));  // open: c_o
  Add #(.Bits(8)) add_2 (.a({4'b0000, I[3:0]}), .b(add_1_s), .c_i(1'b0), .s(Q));  // open: c_o

  // Notes on the sheet:
  //   I: Input
  //   Q: Output
  //   C_O: Carry Output
endmodule
