// Digital circuit CE_CHB.dig as structural Verilog
module CE_CHB (
  input  [7:0] I,
  output [7:0] Q,
  output C_O
);

  wire ce_4t5_1_o_0, ce_4t5_1_o_1, ce_4t5_1_o_2;

  Comparator #(.Bits(8)) comparator_1 (.a(8'h63), .b(I), .lt(C_O));  // open: gt, eq
  CE_4t5 ce_4t5_1 (
    .N_0(I[3]), .N_1(I[4]), .N_2(I[5]), .N_3(I[6]), .O_0(ce_4t5_1_o_0), .O_1(ce_4t5_1_o_1),
    .O_2(ce_4t5_1_o_2), .O_3(Q[6]), .O_4(Q[7]));
  CE_5t5 ce_5t5_1 (
    .N_0(I[1]), .N_1(I[2]), .N_2(ce_4t5_1_o_0), .N_3(ce_4t5_1_o_1), .N_4(ce_4t5_1_o_2), .O_0(Q[1]),
    .O_1(Q[2]), .O_2(Q[3]), .O_3(Q[4]), .O_4(Q[5]));

  assign Q[0] = I[0];

  // Notes on the sheet:
  //   I: Input
  //   Q: Output
  //   C_O: Carry Output
endmodule
