// Digital circuit DIG_Div_unsigned.dig as structural Verilog
module DIG_Div_unsigned (
  input  [7:0] AI_UD,
  input  [7:0] BI_UD,
  input  C_UD,
  input  nC_UD,
  input  EN_UD,
  input  R_UD,
  output [7:0] QO_UD,
  output [7:0] RO_UD,
  output BY_UD,
  output DONE_UD
);

  wire and_1_out, d_ff_1_q, DIS, nRUN, or_1_out, RUN, sub_1_c_o;
  wire [0:0] not_1_out;
  wire [2:0] DIV_C_out;
  wire [7:0] B_DIV_q, multiplexer_1_out, multiplexer_2_out, multiplexer_3_out, multiplexer_4_out, sub_1_s, X;

  and and_1 (and_1_out, EN_UD, ~DIS);  // And
  Register #(.Bits(8)) B_DIV (.D(BI_UD), .C(nC_UD), .en(EN_UD), .Q(B_DIV_q));
  Sub #(.Bits(8)) sub_1 (.a({RO_UD[6:0], X[7]}), .b(B_DIV_q), .c_i(1'b0), .s(sub_1_s), .c_o(sub_1_c_o));
  JK_FF u_RUN (.J(and_1_out), .C(nC_UD), .K(DIS), .Q(RUN), .nQ(nRUN));
  not not_1 (not_1_out[0], sub_1_c_o);
  Multiplexer #(.Bits(8)) multiplexer_1 (
    .sel(not_1_out[0]), .in_0({RO_UD[6:0], X[7]}), .in_1(sub_1_s), .out(multiplexer_1_out));
  Multiplexer #(.Bits(8)) multiplexer_2 (
    .sel(RUN), .in_0({8{1'b0}}), .in_1(multiplexer_1_out), .out(multiplexer_2_out));
  Multiplexer #(.Bits(8)) multiplexer_3 (.sel(RUN), .in_0(AI_UD), .in_1({X[6:0], 1'b0}), .out(multiplexer_3_out));
  Multiplexer #(.Bits(8)) multiplexer_4 (
    .sel(RUN), .in_0({8{1'b0}}), .in_1({QO_UD[6:0], not_1_out[0]}), .out(multiplexer_4_out));
  Counter #(.Bits(3)) DIV_C (.en(RUN), .C(nC_UD), .clr(DIS), .out(DIV_C_out));  // open: ovf
  and and_2 (DONE_UD, DIV_C_out[0], DIV_C_out[1], DIV_C_out[2]);
  or or_1 (or_1_out, EN_UD, RUN);
  or or_2 (DIS, R_UD, DONE_UD);
  Register #(.Bits(8)) R_DIV (.D(multiplexer_2_out), .C(nC_UD), .en(or_1_out), .Q(RO_UD));
  Register #(.Bits(8)) X_DIV (.D(multiplexer_3_out), .C(nC_UD), .en(or_1_out), .Q(X));
  Register #(.Bits(8)) Q_DIV (.D(multiplexer_4_out), .C(nC_UD), .en(or_1_out), .Q(QO_UD));
  D_FF d_ff_1 (.D(or_1_out), .C(C_UD), .Q(d_ff_1_q));  // open: nQ
  or or_3 (BY_UD, or_1_out, d_ff_1_q);

  // Other names for the same wires on the sheet: A[7:0] = AI_UD; C = C_UD; EN = EN_UD; nC = nC_UD; Q[7:0] = QO_UD;
  //   R[7:0] = RO_UD; RES = R_UD

  // Notes on the sheet:
  //   AI_UD: Dividend
  //   BI_UD: Divisor
  //   QO_UD: Quotient
  //   RO_UD: Remainder
  //   BY_UD: Busy (ie State Machine is still running)
  //   EN_UD: Enable
  //   R_UD: Reset
  //   DONE_UD: Used to Update Flags
endmodule
