// Logisim project 65CE02.circ as structural Verilog: 16 circuits, main circuit main
module main (
  input  [7:0] in_1,
  input  [7:0] in_2
);

  wire and_1_out, and_2_out, and_3_out, and_4_out, and_5_out, and_6_out, and_7_out, button_1_out,
       button_2_out, button_3_out, C, comparator_1_eq, comparator_2_eq, comparator_3_eq, d_ff_1_q, IO,
       not_1_out, not_3_out, not_4_out, not_5_out, pull_resistor_4_node, pull_resistor_5_node, R, RAM, RD,
       ROM, RST_out, WR;
  wire [7:0] db8_1_do, db8_2_do, db8_3_do, db8_4_do, DI, divider_1_out, divider_1_rem, DO, KEYBOARD_avail,
       KEYBOARD_data, multiplexer_1_out, ram_1_dout, rom_1_data;
  wire [15:0] A, buffer_1_out;

  Clock clock_1 (.out(C));
  not not_1 (not_1_out, RST_out);
  Button RST (.out(RST_out));
  not not_2 (R, d_ff_1_q);
  D_Flip_Flop #(.trigger("falling")) d_ff_1 (.clk(C), .D(not_1_out), .Q(d_ff_1_q));  // open: Qn, preset, reset
  not not_3 (not_3_out, button_1_out);
  Button button_1 (.out(button_1_out));
  not not_4 (not_4_out, button_2_out);
  Button button_2 (.out(button_2_out));
  not not_5 (not_5_out, button_3_out);
  Button button_3 (.out(button_3_out));
  // FileViewer #(.addrWidth(9), .cols(19), .lines(1)) fileviewer_1: pin names not known
  assign buffer_1_out = A;  // Buffer buffer_1, 16 bits wide
  Pull_Resistor pull_resistor_1 (.node(buffer_1_out));
  CPU cpu_1 (
    .DO(DO), .AO(A), .RW(RD), .R(d_ff_1_q), .C(C), .DI(DI), .IRQ(not_3_out), .NMI(not_4_out),
    .ABT(not_5_out), .SOB(1'b1), .RDY(1'b1), .BE(1'b1));  // open: MLB, VDA, VPA, VBA, VSA, VVA, DEBUG
  // Probe on divider_1_out
  Divider #(.mode("unsigned")) divider_1 (.a(in_1), .b(in_2), .out(divider_1_out), .rem(divider_1_rem));  // open: upper
  // Probe on divider_1_rem
  and and_1 (and_1_out, buffer_1_out[10], buffer_1_out[11], buffer_1_out[12], buffer_1_out[13], buffer_1_out[14], buffer_1_out[15]);
  and and_2 (and_2_out, C, IO);
  Demultiplexer demultiplexer_1 (.out0(RAM), .out1(ROM), .in(RD), .sel(and_1_out), .en(and_2_out));
  not not_6 (WR, RD);
  // Probe on DI
  // Probe on DO
  // Probe on A
  Comparator #(.mode("unsigned"), .width(16)) comparator_1 (.a(A), .b(16'hdf00), .eq(comparator_1_eq));  // open: gt, lt
  Pull_Resistor pull_resistor_2 (.node(comparator_1_eq));
  and and_3 (and_3_out, comparator_1_eq, WR);
  Comparator #(.mode("unsigned"), .width(16)) comparator_2 (.a(A), .b(16'hdf01), .eq(comparator_2_eq));  // open: gt, lt
  Pull_Resistor pull_resistor_3 (.node(comparator_2_eq));
  and and_4 (and_4_out, comparator_2_eq, WR);
  Pull_Resistor pull_resistor_4 (.node(pull_resistor_4_node));
  Pull_Resistor pull_resistor_5 (.node(pull_resistor_5_node));
  Register #(.trigger("falling")) MOD (.D(DO), .en(and_3_out), .clk(C), .clr(R));  // open: Q
  Register #(.trigger("falling")) DIV (.D(DO), .en(and_4_out), .clk(C), .clr(R));  // open: Q
  RAM #(.addrWidth(16), .trigger("falling")) ram_1 (.addr(A), .we(WR), .clk(C), .din(DO), .dout(ram_1_dout));
  ROM #(.addrWidth(10)) rom_1 (.addr(A[9:0]), .data(rom_1_data));
  TTY #(.asciiwidth(8), .cols(40), .rows(10), .trigger("falling")) TERMINAL (
    .data(DO[6:0]), .clk(C), .we(and_5_out), .clr(1'b0));
  and and_5 (and_5_out, pull_resistor_4_node, WR);
  Keyboard #(.asciiwidth(8), .trigger("falling")) KEYBOARD (
    .clk(C), .re(and_6_out), .clr(1'b0), .avail(KEYBOARD_avail[0]), .data(KEYBOARD_data[6:0]));
  and and_6 (and_6_out, pull_resistor_4_node, RD);
  and and_7 (and_7_out, pull_resistor_5_node, RD);
  nor nor_1 (IO, and_7_out, and_6_out);
  Pull_Resistor pull_resistor_6 (.node(KEYBOARD_avail));
  Comparator #(.mode("unsigned")) comparator_3 (.a(KEYBOARD_data), .b(8'ha), .eq(comparator_3_eq));  // open: gt, lt
  DB8 db8_1 (.DO(db8_1_do), .SE(RAM), .DI(ram_1_dout));
  DB8 db8_2 (.DO(db8_2_do), .SE(ROM), .DI(rom_1_data));
  Multiplexer #(.enable("false"), .width(8)) multiplexer_1 (
    .in0(KEYBOARD_data), .in1(8'hd), .out(multiplexer_1_out), .sel(comparator_3_eq));
  DB8 db8_3 (.DO(db8_3_do), .SE(and_6_out), .DI(multiplexer_1_out));
  DB8 db8_4 (.DO(db8_4_do), .SE(and_7_out), .DI(KEYBOARD_avail));
  assign DI = db8_1_do | db8_2_do | db8_3_do | db8_4_do;  // OR_Gate or_1, 8 bits wide
  // Probe on nothing
  // Pins of 7 and 8 bits meet at DO
  // Pins of 7 and 8 bits meet at KEYBOARD_data

  // Notes on the sheet:
  //   Simulated Memory Map:
  //   0x0000 - 0xDEFF - RAM
  //   0xDF00 - Terminal/Keyboard
  //   0xDF01 - Keyboard Status (1 = Data in Keyboard)
  //   0xFC00 - 0xFFFF - ROM
  //   contents of fileviewer_1 (hex, n*v repeats v):
  //   ORA (bp,x) CLE SEE TSB bp ORA bp ASL bp RMB0 bp PHP ORA # ASL A TSY TSB a ORA a ASL a BBR0 bp,r
  //   BPL/BNC r ORA (bp),y ORA (bp),z BPL/BNC rr TRB bp ORA bp,x ASL bp,x RMB1 bp CLC ORA a,y INA/INC A
  //   INZ/INC Z TRB a ORA a,x ASL a,x BBR1 bp,r JSR a AND (bp,x) JSR (a) JSR (a,x) BIT bp AND bp ROL bp
  //   RMB2 bp PLP AND # ROL A TYS BIT a AND a ROL a BBR2 bp,r BMI/BNS r AND (bp),y AND (bp),z BMI/BNS rr
  //   BIT bp,x AND bp,x ROL bp,x RMB3 bp SEC AND a,y DEC A DEZ/DEC Z BIT a,x AND a,x ROL a,x BBR3 bp,r RTI
  //   XOR (bp,x) NEG A ASR A ASR bp XOR bp LSR bp RMB4 bp PHA XOR # LSR A TAZ JMP a XOR a LSR a BBR4 bp,r
  //   BVC r XOR (bp),y XOR (bp),z BVC rr ASR bp,x XOR bp,x LSR bp,x RMB5 bp CLI XOR a,y PHY TAB EXTENDED
  //   XOR a,x LSR a,x BBR5 bp,r RTS ADC (bp,x) RTN # BSR rr STZ bp ADC bp ROR bp RMB6 bp PLA ADC # ROR A
  //   TZA JMP (a) ADC a ROR a BBR6 bp,r BVS r ADC (bp),y ADC (bp),z BVS rr STZ bp,x ADC bp,x ROR bp,x RMB7
  //   bp SEI ADC a,y PLY TBA JMP (a,x) ADC a,x ROR a,x BBR7 bp,r BRA r STA (bp,x) STA (d,sp),y BRA rr STY
  //   bp STA bp STX bp SMB0 bp DEY/DEC Y BIT # TXA STY a,x STY a STA a STX a BBS0 bp,r BCC r STA (bp),y
  //   STA (bp),z BCC rr STY bp,x STA bp,x STX bp,y SMB1 bp TYA STA a,y TXS STX a,y STZ a STA a,x STZ a,x
  //   BBS1 bp,r LDY # LDA (bp,x) LDX # LDZ # LDY bp LDA bp LDX bp SMB2 bp TAY LDA # TAX LDZ a LDY a LDA a
  //   LDX a BBS2 bp,r BCS r LDA (bp),y LDA (bp),z BCS rr LDY bp,x LDA bp,x LDX bp,y SMB3 bp CLV LDA a,y
  //   TSX LDZ a,x LDY a,x LDA a,x LDX a,y BBS3 bp,r CPY # CMP (bp,x) CPZ # DEW bp CPY bp CMP bp DEC bp
  //   SMB4 bp INY/INC Y CMP # DEX/DEC X ASW/ALW a CPY a CMP a DEC a BBS4 bp,r BNE/BZC r CMP (bp),y CMP
  //   (bp),z BNE/BZC rr CPZ bp CMP bp,x DEC bp,x SMB5 bp CLD CMP a,y PHX PHZ CPZ a CMP a,x DEC a,x BBS5
  //   bp,r CPX # SBC (bp,x) LDA (d,sp),y INW bp CPX bp SBC bp INC bp SMB6 bp INX/INC X SBC # NOP ROW/RLW a
  //   CPX a SBC a INC a BBS6 bp,r BEQ/BZS r SBC (bp),y SBC (bp),z BEQ/BZS rr PHW ## SBC bp,x INC bp,x SMB7
  //   bp SED SBC a,y PLX PLZ PHW a SBC a,x INC a,x BBS7 bp,r      MUL bp    MUL #    MUL a        MUL bp,x
  //   MUL a,y    MUL a,x        MLH bp    MLH #    MLH a        MLH bp,x    MLH a,y  RND  MLH a,x
  //   MOD bp   PHR MOD #  SWP  MOD a        MOD bp,x    MOD a,y  SXY ??? MOD a,x        DIV bp   PLR DIV #
  //   SXZ  DIV a        DIV bp,x    DIV a,y  SYZ  DIV a,x     STA sp,y
  //   DCC bp  CBH  LRW a ARW a   DCC a        DCC bp,x        DCC a,x    LDA sp,y    ICC bp  CHB   RRW a
  //   ICC a WAI       ICC bp,x        ICC a,x STP
  //   contents of rom_1 (hex, n*v repeats v):
  //   ea 40 ea 40 ea 40 a2 ff 9a a5 0 5c 45 1 8d 0 df a5 0 5c 65 1 8d 1 df 38 5c e6 0 5c e6 1 80 e7 38 5c
  //   e6 2 5c e6 3 b0 2 80 f5 60 970*0 4 fc 2 fc 6 fc 0 fc
endmodule

module CPU (
  input  R,
  input  C,
  input  [7:0] DI,
  input  IRQ,
  input  NMI,
  input  ABT,
  input  SOB,
  input  RDY,
  input  BE,
  output [7:0] DO,
  output [15:0] AO,
  output RW,
  output MLB,
  output VDA,
  output VPA,
  output VBA,
  output VSA,
  output VVA,
  output [8:0] DEBUG
);

  wire ABT_t, and_5_out, and_6_out, and_7_out, C_t, CIB, cu_1_ldir, IRQ_t, NMI_t, not_2_out, not_4_out,
       or_1_out, R_t, RDY_t, SOB_t;
  wire [0:0] cu_1_a_ctrl;
  wire [1:0] cu_1_anri, not_3_out;
  wire [2:0] cu_1_m_ctrl, cu_1_pco;
  wire [3:0] cu_1_spo, regs_1_vpa;
  wire [7:0] alu_1_fl, lfsr_1_o_8, regs_1_ala, regs_1_do;
  wire [15:0] alu_1_q, regs_1_alb, regs_1_ao;
  wire [31:0] cu_1_r_ctrl;

  not not_1 (R_t, R);
  Multiplexer #(.enable("false")) multiplexer_1 (.in0(C), .in1(1'b1), .out(C_t), .sel(RDY_t));
  and and_1 (IRQ_t, BE, ~IRQ);  // AND_Gate
  and and_2 (NMI_t, BE, ~NMI);  // AND_Gate
  and and_3 (ABT_t, BE, ~ABT);  // AND_Gate
  and and_4 (SOB_t, BE, ~SOB);  // AND_Gate
  D_Flip_Flop d_ff_1 (.clk(C), .D(not_2_out), .Q(RDY_t));  // open: Qn, preset, reset
  not not_2 (not_2_out, RDY);
  LFSR lfsr_1 (.O_8(lfsr_1_o_8), .C(C));
  CU cu_1 (
    .ANRI(cu_1_anri), .INT(CIB), .LDIR(cu_1_ldir), .A_CTRL({DEBUG, cu_1_a_ctrl[0]}), .R_CTRL(cu_1_r_ctrl),
    .SPO(cu_1_spo), .M_CTRL(cu_1_m_ctrl), .PCO(cu_1_pco), .R(R_t), .C(C_t), .DI(DI),
    .FL({alu_1_fl[7:4], alu_1_fl[2:0]}), .IRQ(IRQ_t), .NMI(NMI_t), .ABT(ABT_t));
  REGS regs_1 (
    .ALA(regs_1_ala), .ALB(regs_1_alb), .DO(regs_1_do), .VPA(regs_1_vpa[0]), .VBA(regs_1_vpa[1]),
    .VSA(regs_1_vpa[2]), .VVA(regs_1_vpa[3]), .AO(regs_1_ao), .SPO(cu_1_spo), .R(R_t), .C(C_t),
    .ANRI(cu_1_anri), .DI(DI), .ALUI(alu_1_q), .RND(lfsr_1_o_8), .FL(alu_1_fl), .R_CTRL(cu_1_r_ctrl),
    .PCO(cu_1_pco));
  assign {alu_1_fl[3], not_3_out} = ~cu_1_m_ctrl;  // NOT_Gate not_3, 3 bits wide
  ALU alu_1 (
    .FL({alu_1_fl[7:4], alu_1_fl[2:0]}), .Q(alu_1_q), .R(R_t), .C(C_t), .A(regs_1_ala), .B(regs_1_alb),
    .A_CTRL({DEBUG, cu_1_a_ctrl[0]}), .SOB(SOB_t), .CIB(CIB));
  and and_5 (and_5_out, cu_1_m_ctrl[0], BE, C_t);
  and and_6 (and_6_out, C_t, BE);
  assign DO = and_5_out ? regs_1_do : 8'bz;  // Controlled_Buffer controlled_buffer_1
  assign AO = and_6_out ? regs_1_ao : 16'bz;  // Controlled_Buffer controlled_buffer_2
  not not_4 (not_4_out, cu_1_ldir);
  or or_1 (or_1_out, regs_1_vpa[3], and_7_out);
  and and_7 (and_7_out, regs_1_vpa[2], CIB);
  assign RW = BE ? not_3_out[0] : 1'bz;  // Controlled_Buffer controlled_buffer_3
  assign MLB = BE ? not_3_out[1] : 1'bz;  // Controlled_Buffer controlled_buffer_4
  assign VDA = BE ? not_4_out : 1'bz;  // Controlled_Buffer controlled_buffer_5
  assign VPA = BE ? regs_1_vpa[0] : 1'bz;  // Controlled_Buffer controlled_buffer_6
  assign VBA = BE ? regs_1_vpa[1] : 1'bz;  // Controlled_Buffer controlled_buffer_7
  assign VSA = BE ? regs_1_vpa[2] : 1'bz;  // Controlled_Buffer controlled_buffer_8
  assign VVA = BE ? or_1_out : 1'bz;  // Controlled_Buffer controlled_buffer_9
  // Probe on nothing

  // Other names for the same wires on the sheet: CB = C; RC[1:0] = {C_t, R_t}
endmodule

module REGS (
  input  R,
  input  C,
  input  [1:0] ANRI,
  input  [7:0] DI,
  input  [15:0] ALUI,
  input  [7:0] RND,
  input  [7:0] FL,
  input  [31:0] R_CTRL,
  input  [2:0] PCO,
  input  [3:0] SPO,
  output [7:0] ALA,
  output [15:0] ALB,
  output [7:0] DO,
  output VPA,
  output VBA,
  output VSA,
  output VVA,
  output [15:0] AO
);

  wire and_1_out, and_2_out, and_4_out, decoder_1_out0, decoder_1_out1, decoder_1_out2, decoder_1_out4,
       decoder_1_out5, decoder_1_out6, decoder_2_out0, decoder_2_out3, SPS, YEN;
  wire [1:0] or_1_out;
  wire [1:1] and_3_out;
  wire [4:0] AOS_out;
  wire [7:0] A, adder_3_out, adder_6_out, B, multiplexer_1_out, multiplexer_5_out, multiplexer_6_out,
       multiplexer_7_out, multiplexer_8_out, multiplexer_9_out, multiplexer_10_p5, multiplexer_11_out,
       multiplexer_12_out, multiplexer_13_out, multiplexer_14_out, multiplexer_15_out, multiplexer_16_out,
       multiplexer_17_out, multiplexer_19_out, negator_1_out, PCO_t, REG, TBH, TBL, X, Y, Z;
  wire [15:0] adder_1_out, adder_2_out, adder_4_out, adder_5_out, adder_7_out, adder_8_out, adder_9_out,
       bit_extender_4_out, bit_extender_5_out, bit_extender_6_out, multiplexer_2_out, multiplexer_3_out,
       multiplexer_18_out, multiplexer_20_out, OFS, OSP, PC, SP, SPN, TA;

  assign OFS = {{13{R_CTRL[31]}}, R_CTRL[31:29]};  // Bit_Extender bit_extender_1
  assign PCO_t = {{5{1'b0}}, PCO};  // Bit_Extender bit_extender_2
  assign OSP = {{12{SPO[3]}}, SPO};  // Bit_Extender bit_extender_3
  // Probe on OFS
  Multiplexer #(.enable("false"), .width(8)) multiplexer_1 (
    .in0(PCO_t), .in1(DI), .out(multiplexer_1_out), .sel(R_CTRL[24]));
  // Probe on DI
  Decoder #(.select(3)) decoder_1 (
    .out0(decoder_1_out0), .out1(decoder_1_out1), .out2(decoder_1_out2), .out3(YEN), .out4(decoder_1_out4),
    .out5(decoder_1_out5), .out6(decoder_1_out6), .out7(SPS), .sel(R_CTRL[22:20]), .en(R_CTRL[23]));
  and and_1 (and_1_out, R_CTRL[25], R_CTRL[24]);
  Multiplexer #(.enable("false"), .width(16)) multiplexer_2 (
    .in0(PC), .in1({16{1'b0}}), .out(multiplexer_2_out), .sel(and_1_out));
  assign bit_extender_4_out = {{8{multiplexer_1_out[7]}}, multiplexer_1_out};  // Bit_Extender bit_extender_4
  Multiplexer #(.enable("false"), .width(16)) multiplexer_3 (
    .in0(bit_extender_4_out), .in1({DI, TBL}), .out(multiplexer_3_out), .sel(R_CTRL[25]));
  Multiplexer #(.enable("false"), .select(3), .width(8)) multiplexer_4 (
    .in0(DI), .in1(ALUI[7:0]), .in2(TBL), .in3(X), .in4(Y), .in5({A[3:0], A[7:4]}), .in6(negator_1_out),
    .in7(RND), .out(REG));  // open: sel
  Negator negator_1 (.in(A), .out(negator_1_out));
  Multiplexer #(.enable("false"), .width(8)) multiplexer_5 (
    .in0(DI), .in1(A), .out(multiplexer_5_out), .sel(R_CTRL[9]));
  Multiplexer #(.enable("false"), .width(8)) multiplexer_6 (
    .in0(DI), .in1(ALUI[15:8]), .out(multiplexer_6_out), .sel(R_CTRL[16]));
  Multiplexer #(.enable("false"), .select(2), .width(8)) multiplexer_7 (
    .in0(DI), .in1(ALUI[7:0]), .in2(Y), .in3(Z), .out(multiplexer_7_out), .sel(R_CTRL[17:16]));
  Multiplexer #(.enable("false"), .width(8)) multiplexer_8 (
    .in0(SPN[15:8]), .in1(Y), .out(multiplexer_8_out), .sel(SPS));
  Multiplexer #(.enable("false"), .width(8)) multiplexer_9 (
    .in0(SPN[7:0]), .in1(X), .out(multiplexer_9_out), .sel(SPS));
  and and_2 (and_2_out, SPS, R_CTRL[24], R_CTRL[25]);
  Adder #(.width(16)) adder_1 (
    .a(multiplexer_2_out), .b(multiplexer_3_out), .out(adder_1_out), .cin(and_2_out));  // open: cout
  Register #(.trigger("falling")) u_A (.D(REG), .en(decoder_1_out0), .Q(A), .clk(C), .clr(R));
  Register #(.trigger("falling")) u_B (.D(multiplexer_5_out), .en(decoder_1_out1), .Q(B), .clk(C), .clr(R));
  Register #(.trigger("falling")) u_X (.D(REG), .en(decoder_1_out2), .Q(X), .clk(C), .clr(R));
  Register #(.trigger("falling")) u_Y (.D(REG), .en(YEN), .Q(Y), .clk(C), .clr(R));
  Register #(.trigger("falling")) u_Z (.D(REG), .en(decoder_1_out4), .Q(Z), .clk(C), .clr(R));
  Register #(.trigger("falling")) TAH (.D(DI), .en(decoder_1_out5), .Q(TA[15:8]), .clk(C), .clr(R));
  Register #(.trigger("falling")) TAL (.D(DI), .en(decoder_1_out6), .Q(TA[7:0]), .clk(C), .clr(R));
  Register #(.trigger("falling")) u_TBH (.D(multiplexer_6_out), .en(R_CTRL[19]), .Q(TBH), .clk(C), .clr(R));
  Register #(.trigger("falling")) u_TBL (.D(multiplexer_7_out), .en(R_CTRL[18]), .Q(TBL), .clk(C), .clr(R));
  PSREG SPH (.O(SP[15:8]), .R(R), .C(C), .L(R_CTRL[28]), .I(multiplexer_8_out), .S(8'h1));
  Register #(.trigger("falling")) SPL (.D(multiplexer_9_out), .en(R_CTRL[27]), .Q(SP[7:0]), .clk(C), .clr(R));
  Register #(.trigger("falling"), .width(16)) u_PC (.D(adder_1_out), .en(R_CTRL[26]), .Q(PC), .clk(C), .clr(R));
  PLA #(.in_width(4), .out_width(5), .\table ("0000 00000 # PC\n0001 00100 # TA\n0010 01100 # TA+X\n0011 10100 # TA+Y\n0100 11100 # TA+Z\n0101 00001 # BP/TBL\n0110 01001 # BP/TBL+X\n0111 10001 # BP/TBL+Y\n1000 00101 # BP/TAL\n1001 01101 # BP/TAL+X\n1010 00111 # PC+XY\n1011 00010 # SP\n1100 01010 # SP+Y\n1101 10010 # SP+TBL\n1110 11010 # SP+TAL\n1111 00011 # VP")) AOS (
    .in(R_CTRL[15:12]), .out(AOS_out));
  assign or_1_out = {2{and_3_out[1]}} | AOS_out[4:3];  // OR_Gate or_1, 2 bits wide
  // Multiplexer #(.enable("false"), .select(2), .width(8)) multiplexer_10: pin names not known; wires that end beside it: {8{1'b0}}, X, Y, Z, multiplexer_10_p5
  Multiplexer #(.enable("false"), .select(2), .width(8)) multiplexer_11 (
    .in0({8{1'b0}}), .in1(Y), .in2(TBL), .in3(TA[7:0]), .out(multiplexer_11_out));  // open: sel
  Multiplexer #(.enable("false"), .width(8)) multiplexer_12 (
    .in0(TBL), .in1(TA[7:0]), .out(multiplexer_12_out), .sel(AOS_out[2]));
  and and_3 (and_3_out[1], R_CTRL[28], R_CTRL[9], R_CTRL[27]);
  assign bit_extender_5_out = {{8{multiplexer_10_p5[7]}}, multiplexer_10_p5};  // Bit_Extender bit_extender_5
  Multiplexer #(.enable("false"), .width(8)) multiplexer_13 (
    .in0(SP[7:0]), .in1(multiplexer_10_p5), .out(multiplexer_13_out), .sel(and_4_out));
  Multiplexer #(.enable("false"), .width(8)) multiplexer_14 (
    .in0(multiplexer_11_out), .in1(multiplexer_12_out), .out(multiplexer_14_out), .sel(and_4_out));
  Adder #(.width(16)) adder_2 (.a(TA), .b(bit_extender_5_out), .out(adder_2_out));  // open: cin, cout
  Multiplexer #(.enable("false"), .width(8)) multiplexer_15 (
    .in0(OSP[7:0]), .in1(OFS[7:0]), .out(multiplexer_15_out), .sel(and_4_out));
  Adder adder_3 (.a(multiplexer_13_out), .b(multiplexer_14_out), .out(adder_3_out));  // open: cin, cout
  assign bit_extender_6_out = {{8{1'b0}}, multiplexer_14_out};  // Bit_Extender bit_extender_6
  Adder #(.width(16)) adder_4 (
    .a(16'hfff8), .b({{13{1'b0}}, ANRI, 1'b0}), .out(adder_4_out), .cin(R_CTRL[26]));  // open: cout
  Adder #(.width(16)) adder_5 (.a(PC), .b({X, Y}), .out(adder_5_out));  // open: cin, cout
  Multiplexer #(.enable("false"), .width(8)) multiplexer_16 (
    .in0(SP[7:0]), .in1(SP[15:8]), .out(multiplexer_16_out), .sel(YEN));
  Multiplexer #(.enable("false"), .width(8)) multiplexer_17 (
    .in0(DI), .in1(TBL), .out(multiplexer_17_out), .sel(R_CTRL[19]));
  Multiplexer #(.enable("false"), .width(16)) multiplexer_18 (
    .in0(PC), .in1(adder_2_out), .out(multiplexer_18_out), .sel(AOS_out[2]));
  and and_4 (and_4_out, ~AOS_out[1], AOS_out[0]);  // AND_Gate
  Multiplexer #(.enable("false"), .width(8)) multiplexer_19 (
    .in0(SP[15:8]), .in1(B), .out(multiplexer_19_out), .sel(and_4_out));
  Adder adder_6 (.a(multiplexer_15_out), .b(adder_3_out), .out(adder_6_out));  // open: cin, cout
  Adder #(.width(16)) adder_7 (.a(SP), .b(bit_extender_6_out), .out(adder_7_out));  // open: cin, cout
  Multiplexer #(.enable("false"), .width(16)) multiplexer_20 (
    .in0(adder_4_out), .in1(adder_5_out), .out(multiplexer_20_out), .sel(AOS_out[2]));
  Adder #(.width(16)) adder_8 (.a(multiplexer_18_out), .b(OFS), .out(adder_8_out));  // open: cin, cout
  Adder #(.width(16)) adder_9 (.a(OSP), .b(adder_7_out), .out(adder_9_out));  // open: cin, cout
  Multiplexer #(.enable("false"), .width(16)) multiplexer_21 (
    .in0(adder_9_out), .in1({multiplexer_19_out, adder_6_out}), .out(SPN), .sel(FL[5]));
  Multiplexer #(.enable("false"), .select(2), .width(8)) multiplexer_22 (
    .in0(A), .in1(X), .in2(Y), .in3(Z), .out(ALA));  // open: sel
  Multiplexer #(.enable("false"), .select(3), .width(8)) multiplexer_23 (
    .in0(A), .in1(B), .in2(X), .in3(Y), .in4(Z), .in5(multiplexer_16_out), .in6(multiplexer_17_out),
    .in7(REG), .out(ALB[7:0]));  // open: sel
  Multiplexer #(.enable("false"), .select(4), .width(8)) multiplexer_24 (
    .in0(A), .in1(B), .in2(X), .in3(Y), .in4(Z), .in5(FL), .in6(TBL), .in7(TBH), .in8(adder_8_out[7:0]),
    .in9(adder_8_out[15:8]), .out(DO));  // open: in10, in11, in12, in13, in14, in15, sel
  Decoder #(.enable("false"), .select(2)) decoder_2 (
    .out0(decoder_2_out0), .out1(VBA), .out2(VSA), .out3(decoder_2_out3), .sel(AOS_out[1:0]));
  Multiplexer #(.enable("false"), .select(2), .width(16)) multiplexer_25 (
    .in0(adder_8_out), .in1({multiplexer_19_out, adder_6_out}), .in2(SPN), .in3(multiplexer_20_out), .out(AO));  // open: sel
  and and_5 (VPA, ~AOS_out[2], decoder_2_out0);  // AND_Gate
  and and_6 (VVA, decoder_2_out3, ~AOS_out[2]);  // AND_Gate
  // Probe on AO
  // Probe on nothing

  assign ALB[15:8] = DI;

  // Other names for the same wires on the sheet: ALIL[7:0] = ALUI[7:0]; ALIH[7:0] = ALUI[15:8]; nEF = FL[5];
  //   OFS8[7:0] = OFS[7:0]; OSP8[7:0] = OSP[7:0]; ALAS[1:0] = R_CTRL[1:0]; ALBS[2:0] = R_CTRL[4:2];
  //   DOS[3:0] = R_CTRL[8:5]; RGS[2:0] = R_CTRL[11:9]; AOS[3:0] = R_CTRL[15:12]; TBS[1:0] = R_CTRL[17:16];
  //   LBL = R_CTRL[18]; LBH = R_CTRL[19]; LRS[2:0] = R_CTRL[22:20]; LRE = R_CTRL[23]; PCS[1:0] = R_CTRL[25:24];
  //   LPC = R_CTRL[26]; LSL = R_CTRL[27]; LSH = R_CTRL[28]; SPL[7:0] = SP[7:0]; SPH[7:0] = SP[15:8];
  //   TAL[7:0] = TA[7:0]

  // Notes on the sheet:
  //   ALU A Select
  //   ALU B Select
  //   Data Out Select
  //   Register Input Select
  //   Address Out Select
  //   Temp. B Select
  //   Temp. B Low Enable
  //   Temp. B High Enable 
  //   Reg Select
  //   Reg Enable
  //   PC Select
  //   LD PC
  //   LD SP Low
  //   LD SP High
  //   SXY:
  //   X -> Y; Y -> TBL
  //   TBL -> X
  //   SYZ:
  //   Z -> Y; Y -> TBL
  //   TBL -> Z
  //   SXZ:
  //   Z -> X; X -> TBL
  //   TBL -> Z
  //   00 = PC+PCO
  //   01 = PC+DI
  //   10 = PC+TBL/DI
  //   11 = TBL/DI (+3/-4)
endmodule

module ALU (
  input  R,
  input  C,
  input  [7:0] A,
  input  [15:0] B,
  input  [9:0] A_CTRL,
  input  SOB,
  input  CIB,
  output [6:0] FL,
  output [15:0] Q
);

  wire adder_1_c_o, AZS_2_out, AZS_out, CC, CI, clock_2_out, multiplexer_5_out, multiplexer_7_out,
       multiplexer_9_out, multiplexer_11_out, multiplexer_13_out, multiplexer_15_out, multiplexer_16_out,
       multiplexer_17_out, multiplexer_18_out, multiplexer_19_out, multiplexer_20_out, multiplexer_21_out,
       multiplexer_22_out, NI, not_1_out, or_2_out, or_3_out, or_4_out, or_5_out, or_6_out, or_7_out,
       or_8_out, or_9_out, QHS_out, SEL0, SEL3, VI, ZI;
  wire [1:1] and_1_out;
  wire [3:0] counter_2_q, SEL1, SEL2;
  wire [4:0] undriven;
  wire [5:0] ALU0_out;
  wire [6:0] multiplexer_2_out, SEL4;
  wire [7:0] AA8, adder_1_qh, adder_1_ql, and_3_out, ANDQ, decoder_1_out0, divider_1_out, divider_1_rem,
       multiplexer_1_out, multiplexer_4_out, multiplexer_6_out, multiplexer_8_out, multiplexer_10_out,
       multiplexer_12_out, multiplexer_14_out, multiplier_1_cout, multiplier_1_out, or_1_out, Q_t, xor_1_out;
  wire [8:0] AA, CBH_2_out, CBH_out, CHB_2_out, CHB_out;
  wire [16:0] ALU1_out, ALU_out;

  Multiplexer #(.enable("false"), .width(8)) multiplexer_1 (
    .in0(Q_t), .in1(B[7:0]), .out(multiplexer_1_out), .sel(SEL0));
  PLA #(.in_width(9), .out_width(17), .\table ("000000000 10000100000000001 # B->N/Z / BRK #\n000000001 10000100001100000 # OR / ORA (bp,x)\n000000010 00000011000000000 # CLR C / CLE\n000000011 00100001000000000 # SET E / SEE\n000000100 00000100001100000 # TSB / TSB bp\n000000101 10000100001100000 # OR / ORA bp\n000000110 10000110010100000 # ASL / ASL bp\n000000111 00000000001000010 # RMB / RMB0 bp\n000001000 10000100000000001 # B->N/Z / PHP\n000001001 10000100001100000 # OR / ORA #\n000001010 10000110010100000 # ASL / ASL A\n000001011 10000100000000001 # B->N/Z / TSY\n000001100 00000100001100000 # TSB / TSB a\n000001101 10000100001100000 # OR / ORA a\n000001110 10000110010100000 # ASL / ASL a\n000001111 10000100000000001 # B->N/Z / BBR0 bp,r\n000010000 10000100000000001 # B->N/Z / BPL/BNC r\n000010001 10000100001100000 # OR / ORA (bp),y\n000010010 10000100001100000 # OR / ORA (bp),z\n000010011 10000100000000001 # B->N/Z / BPL/BNC rr\n000010100 00000100001000000 # TRB / TRB bp\n000010101 10000100001100000 # OR / ORA bp,x\n000010110 10000110010100000 # ASL / ASL bp,x\n000010111 00000000001000010 # RMB / RMB1 bp\n000011000 00000011000000000 # CLR C / CLC\n000011001 10000100001100000 # OR / ORA a,y\n000011010 10000100000000010 # INC / INA/INC A\n000011011 10000100000000010 # INC / INZ/INC Z\n000011100 00000100001000000 # TRB / TRB a\n000011101 10000100001100000 # OR / ORA a,x\n000011110 10000110010100000 # ASL / ASL a,x\n000011111 10000100000000001 # B->N/Z / BBR1 bp,r\n000100000 10000100000000001 # B->N/Z / JSR a\n000100001 10000100000100000 # AND / AND (bp,x)\n000100010 10000100000000001 # B->N/Z / JSR (a)\n000100011 10000100000000001 # B->N/Z / JSR (a,x)\n000100100 11000100000000001 # BIT / BIT bp\n000100101 10000100000100000 # AND / AND bp\n000100110 10000110100000000 # ROL / ROL bp\n000100111 00000000001000010 # RMB / RMB2 bp\n000101000 11011110000000000 # WR FL / PLP\n000101001 10000100000100000 # AND / AND #\n000101010 10000110100000000 # ROL / ROL A\n000101011 10000100000000001 # B->N/Z / TYS\n000101100 11000100000000001 # BIT / BIT a\n000101101 10000100000100000 # AND / AND a\n000101110 10000110100000000 # ROL / ROL a\n000101111 10000100000000001 # B->N/Z / BBR2 bp,r\n000110000 10000100000000001 # B->N/Z / BMI/BNS r\n000110001 10000100000100000 # AND / AND (bp),y\n000110010 10000100000100000 # AND / AND (bp),z\n000110011 10000100000000001 # B->N/Z / BMI/BNS rr\n000110100 11000100000000001 # BIT / BIT bp,x\n000110101 10000100000100000 # AND / AND bp,x\n000110110 10000110100000000 # ROL / ROL bp,x\n000110111 00000000001000010 # RMB / RMB3 bp\n000111000 00000011000000001 # SET C / SEC\n000111001 10000100000100000 # AND / AND a,y\n000111010 10000100000000110 # DEC / DEC A\n000111011 10000100000000110 # DEC / DEZ/DEC Z\n000111100 11000100000000001 # BIT / BIT a,x\n000111101 10000100000100000 # AND / AND a,x\n000111110 10000110100000000 # ROL / ROL a,x\n000111111 10000100000000001 # B->N/Z / BBR3 bp,r\n001000000 11011110000000000 # WR FL / RTI\n001000001 10000100010000000 # XOR / XOR (bp,x)\n001000010 10000100000000001 # B->N/Z / NEG A\n001000011 10000110011000000 # ASR / ASR A\n001000100 10000110011000000 # ASR / ASR bp\n001000101 10000100010000000 # XOR / XOR bp\n001000110 10000110011100000 # LSR / LSR bp\n001000111 00000000001000010 # RMB / RMB4 bp\n001001000 10000100000000001 # B->N/Z / PHA\n001001001 10000100010000000 # XOR / XOR #\n001001010 10000110011100000 # LSR / LSR A\n001001011 10000100000000001 # B->N/Z / TAZ\n001001100 10000100000000001 # B->N/Z / JMP a\n001001101 10000100010000000 # XOR / XOR a\n001001110 10000110011100000 # LSR / LSR a\n001001111 10000100000000001 # B->N/Z / BBR4 bp,r\n001010000 10000100000000001 # B->N/Z / BVC r\n001010001 10000100010000000 # XOR / XOR (bp),y\n001010010 10000100010000000 # XOR / XOR (bp),z\n001010011 10000100000000001 # B->N/Z / BVC rr\n001010100 10000110011000000 # ASR / ASR bp,x\n001010101 10000100010000000 # XOR / XOR bp,x\n001010110 10000110011100000 # LSR / LSR bp,x\n001010111 00000000001000010 # RMB / RMB5 bp\n001011000 00001001000000001 # CLR I / CLI\n001011001 10000100010000000 # XOR / XOR a,y\n001011010 10000100000000001 # B->N/Z / PHY\n001011011 10000100000000001 # B->N/Z / TAB\n001011100 10000100000000001 # B->N/Z / EXTENDED\n001011101 10000100010000000 # XOR / XOR a,x\n001011110 10000110011100000 # LSR / LSR a,x\n001011111 10000100000000001 # B->N/Z / BBR5 bp,r\n001100000 10000100000000001 # B->N/Z / RTS\n001100001 10000110000001000 # ADC / ADC (bp,x)\n001100010 10000100000000001 # B->N/Z / RTN #\n001100011 10000100000000001 # B->N/Z / BSR rr\n001100100 10000100000000001 # B->N/Z / STZ bp\n001100101 10000110000001000 # ADC / ADC bp\n001100110 10000110100100000 # ROR / ROR bp\n001100111 00000000001000010 # RMB / RMB6 bp\n001101000 10000100000000001 # B->N/Z / PLA\n001101001 10000110000001000 # ADC / ADC #\n001101010 10000110100100000 # ROR / ROR A\n001101011 10000100000000001 # B->N/Z / TZA\n001101100 10000100000000001 # B->N/Z / JMP (a)\n001101101 10000110000001000 # ADC / ADC a\n001101110 10000110100100000 # ROR / ROR a\n001101111 10000100000000001 # B->N/Z / BBR6 bp,r\n001110000 10000100000000001 # B->N/Z / BVS r\n001110001 10000110000001000 # ADC / ADC (bp),y\n001110010 10000110000001000 # ADC / ADC (bp),z\n001110011 10000100000000001 # B->N/Z / BVS rr\n001110100 10000100000000001 # B->N/Z / STZ bp,x\n001110101 10000110000001000 # ADC / ADC bp,x\n001110110 10000110100100000 # ROR / ROR bp,x\n001110111 00000000001000010 # RMB / RMB7 bp\n001111000 00001001000000000 # SET I / SEI\n001111001 10000110000001000 # ADC / ADC a,y\n001111010 10000100000000001 # B->N/Z / PLY\n001111011 10000100000000001 # B->N/Z / TBA\n001111100 10000100000000001 # B->N/Z / JMP (a,x)\n001111101 10000110000001000 # ADC / ADC a,x\n001111110 10000110100100000 # ROR / ROR a,x\n001111111 10000100000000001 # B->N/Z / BBR7 bp,r\n010000000 10000100000000001 # B->N/Z / BRA r\n010000001 10000100000000001 # B->N/Z / STA (bp,x)\n010000010 10000100000000001 # B->N/Z / STA (d,sp),y\n010000011 10000100000000001 # B->N/Z / BRA rr\n010000100 10000100000000001 # B->N/Z / STY bp\n010000101 10000100000000001 # B->N/Z / STA bp\n010000110 10000100000000001 # B->N/Z / STX bp\n010000111 00000000001100010 # SMB / SMB0 bp\n010001000 10000100000000110 # DEC / DEY/DEC Y\n010001001 11000100000000001 # BIT / BIT #\n010001010 10000100000000001 # B->N/Z / TXA\n010001011 10000100000000001 # B->N/Z / STY a,x\n010001100 10000100000000001 # B->N/Z / STY a\n010001101 10000100000000001 # B->N/Z / STA a\n010001110 10000100000000001 # B->N/Z / STX a\n010001111 10000100000000001 # B->N/Z / BBS0 bp,r\n010010000 10000100000000001 # B->N/Z / BCC r\n010010001 10000100000000001 # B->N/Z / STA (bp),y\n010010010 10000100000000001 # B->N/Z / STA (bp),z\n010010011 10000100000000001 # B->N/Z / BCC rr\n010010100 10000100000000001 # B->N/Z / STY bp,x\n010010101 10000100000000001 # B->N/Z / STA bp,x\n010010110 10000100000000001 # B->N/Z / STX bp,y\n010010111 00000000001100010 # SMB / SMB1 bp\n010011000 10000100000000001 # B->N/Z / TYA\n010011001 10000100000000001 # B->N/Z / STA a,y\n010011010 10000100000000001 # B->N/Z / TXS\n010011011 10000100000000001 # B->N/Z / STX a,y\n010011100 10000100000000001 # B->N/Z / STZ a\n010011101 10000100000000001 # B->N/Z / STA a,x\n010011110 10000100000000001 # B->N/Z / STZ a,x\n010011111 10000100000000001 # B->N/Z / BBS1 bp,r\n010100000 10000100000000001 # B->N/Z / LDY #\n010100001 10000100000000001 # B->N/Z / LDA (bp,x)\n010100010 10000100000000001 # B->N/Z / LDX #\n010100011 10000100000000001 # B->N/Z / LDZ #\n010100100 10000100000000001 # B->N/Z / LDY bp\n010100101 10000100000000001 # B->N/Z / LDA bp\n010100110 10000100000000001 # B->N/Z / LDX bp\n010100111 00000000001100010 # SMB / SMB2 bp\n010101000 10000100000000001 # B->N/Z / TAY\n010101001 10000100000000001 # B->N/Z / LDA #\n010101010 10000100000000001 # B->N/Z / TAX\n010101011 10000100000000001 # B->N/Z / LDZ a\n010101100 10000100000000001 # B->N/Z / LDY a\n010101101 10000100000000001 # B->N/Z / LDA a\n010101110 10000100000000001 # B->N/Z / LDX a\n010101111 10000100000000001 # B->N/Z / BBS2 bp,r\n010110000 10000100000000001 # B->N/Z / BCS r\n010110001 10000100000000001 # B->N/Z / LDA (bp),y\n010110010 10000100000000001 # B->N/Z / LDA (bp),z\n010110011 10000100000000001 # B->N/Z / BCS rr\n010110100 10000100000000001 # B->N/Z / LDY bp,x\n010110101 10000100000000001 # B->N/Z / LDA bp,x\n010110110 10000100000000001 # B->N/Z / LDX bp,y\n010110111 00000000001100010 # SMB / SMB3 bp\n010111000 01000001000000000 # CLR V / CLV\n010111001 10000100000000001 # B->N/Z / LDA a,y\n010111010 10000100000000001 # B->N/Z / TSX\n010111011 10000100000000001 # B->N/Z / LDZ a,x\n010111100 10000100000000001 # B->N/Z / LDY a,x\n010111101 10000100000000001 # B->N/Z / LDA a,x\n010111110 10000100000000001 # B->N/Z / LDX a,y\n010111111 10000100000000001 # B->N/Z / BBS3 bp,r\n011000000 10000110000000100 # CMP / CPY #\n011000001 10000110000000100 # CMP / CMP (bp,x)\n011000010 10000110000000100 # CMP / CPZ #\n011000011 10000100000010110 # DEC W / DEW bp\n011000100 10000110000000100 # CMP / CPY bp\n011000101 10000110000000100 # CMP / CMP bp\n011000110 10000100000000110 # DEC / DEC bp\n011000111 00000000001100010 # SMB / SMB4 bp\n011001000 10000100000000010 # INC / INY/INC Y\n011001001 10000110000000100 # CMP / CMP #\n011001010 10000100000000110 # DEC / DEX/DEC X\n011001011 10000110010100100 # ASL W / ASW/ALW a\n011001100 10000110000000100 # CMP / CPY a\n011001101 10000110000000100 # CMP / CMP a\n011001110 10000100000000110 # DEC / DEC a\n011001111 10000100000000001 # B->N/Z / BBS4 bp,r\n011010000 10000100000000001 # B->N/Z / BNE/BZC r\n011010001 10000110000000100 # CMP / CMP (bp),y\n011010010 10000110000000100 # CMP / CMP (bp),z\n011010011 10000100000000001 # B->N/Z / BNE/BZC rr\n011010100 10000110000000100 # CMP / CPZ bp\n011010101 10000110000000100 # CMP / CMP bp,x\n011010110 10000100000000110 # DEC / DEC bp,x\n011010111 00000000001100010 # SMB / SMB5 bp\n011011000 00010001000000000 # CLR D / CLD\n011011001 10000110000000100 # CMP / CMP a,y\n011011010 10000100000000001 # B->N/Z / PHX\n011011011 10000100000000001 # B->N/Z / PHZ\n011011100 10000110000000100 # CMP / CPZ a\n011011101 10000110000000100 # CMP / CMP a,x\n011011110 10000100000000110 # DEC / DEC a,x\n011011111 10000100000000001 # B->N/Z / BBS5 bp,r\n011100000 10000110000000100 # CMP / CPX #\n011100001 10000110000001100 # SBC / SBC (bp,x)\n011100010 10000100000000001 # B->N/Z / LDA (d,sp),y\n011100011 10000100000010010 # INC W / INW bp\n011100100 10000110000000100 # CMP / CPX bp\n011100101 10000110000001100 # SBC / SBC bp\n011100110 10000100000000010 # INC / INC bp\n011100111 00000000001100010 # SMB / SMB6 bp\n011101000 10000100000000010 # INC / INX/INC X\n011101001 10000110000001100 # SBC / SBC #\n011101010 10000100000000001 # B->N/Z / NOP\n011101011 10000110100000100 # ROL W / ROW/RLW a\n011101100 10000110000000100 # CMP / CPX a\n011101101 10000110000001100 # SBC / SBC a\n011101110 10000100000000010 # INC / INC a\n011101111 10000100000000001 # B->N/Z / BBS6 bp,r\n011110000 10000100000000001 # B->N/Z / BEQ/BZS r\n011110001 10000110000001100 # SBC / SBC (bp),y\n011110010 10000110000001100 # SBC / SBC (bp),z\n011110011 10000100000000001 # B->N/Z / BEQ/BZS rr\n011110100 10000100000000001 # B->N/Z / PHW ##\n011110101 10000110000001100 # SBC / SBC bp,x\n011110110 10000100000000010 # INC / INC bp,x\n011110111 00000000001100010 # SMB / SMB7 bp\n011111000 00010001000000001 # SET D / SED\n011111001 10000110000001100 # SBC / SBC a,y\n011111010 10000100000000001 # B->N/Z / PLX\n011111011 10000100000000001 # B->N/Z / PLZ\n011111100 10000100000000001 # B->N/Z / PHW a\n011111101 10000110000001100 # SBC / SBC a,x\n011111110 10000100000000010 # INC / INC a,x\n011111111 10000100000000001 # B->N/Z / BBS7 bp,r\n100000000 10000100000000001 # B->N/Z / <INV>\n100000001 10000100000000001 # B->N/Z / <INV>\n100000010 10000100000000001 # B->N/Z / <INV>\n100000011 10000100000000001 # B->N/Z / <INV>\n100000100 10000100000000001 # B->N/Z / <INV>\n100000101 10000110101000000 # MUL / MUL bp\n100000110 10000100000000001 # B->N/Z / <INV>\n100000111 10000100000000001 # B->N/Z / <INV>\n100001000 10000100000000001 # B->N/Z / <INV>\n100001001 10000110101000000 # MUL / MUL #\n100001010 10000100000000001 # B->N/Z / <INV>\n100001011 10000100000000001 # B->N/Z / <INV>\n100001100 10000100000000001 # B->N/Z / <INV>\n100001101 10000110101000000 # MUL / MUL a\n100001110 10000100000000001 # B->N/Z / <INV>\n100001111 10000100000000001 # B->N/Z / <INV>\n100010000 10000100000000001 # B->N/Z / <INV>\n100010001 10000100000000001 # B->N/Z / <INV>\n100010010 10000100000000001 # B->N/Z / <INV>\n100010011 10000100000000001 # B->N/Z / <INV>\n100010100 10000100000000001 # B->N/Z / <INV>\n100010101 10000110101000000 # MUL / MUL bp,x\n100010110 10000100000000001 # B->N/Z / <INV>\n100010111 10000100000000001 # B->N/Z / <INV>\n100011000 10000100000000001 # B->N/Z / <INV>\n100011001 10000110101000000 # MUL / MUL a,y\n100011010 10000100000000001 # B->N/Z / <INV>\n100011011 10000100000000001 # B->N/Z / <INV>\n100011100 10000100000000001 # B->N/Z / <INV>\n100011101 10000110101000000 # MUL / MUL a,x\n100011110 10000100000000001 # B->N/Z / <INV>\n100011111 10000100000000001 # B->N/Z / <INV>\n100100000 10000100000000001 # B->N/Z / <INV>\n100100001 10000100000000001 # B->N/Z / <INV>\n100100010 10000100000000001 # B->N/Z / <INV>\n100100011 10000100000000001 # B->N/Z / <INV>\n100100100 10000100000000001 # B->N/Z / <INV>\n100100101 10000110101100000 # MLH / MLH bp\n100100110 10000100000000001 # B->N/Z / <INV>\n100100111 10000100000000001 # B->N/Z / <INV>\n100101000 10000100000000001 # B->N/Z / <INV>\n100101001 10000110101100000 # MLH / MLH #\n100101010 10000100000000001 # B->N/Z / <INV>\n100101011 10000100000000001 # B->N/Z / <INV>\n100101100 10000100000000001 # B->N/Z / <INV>\n100101101 10000110101100000 # MLH / MLH a\n100101110 10000100000000001 # B->N/Z / <INV>\n100101111 10000100000000001 # B->N/Z / <INV>\n100110000 10000100000000001 # B->N/Z / <INV>\n100110001 10000100000000001 # B->N/Z / <INV>\n100110010 10000100000000001 # B->N/Z / <INV>\n100110011 10000100000000001 # B->N/Z / <INV>\n100110100 10000100000000001 # B->N/Z / <INV>\n100110101 10000110101100000 # MLH / MLH bp,x\n100110110 10000100000000001 # B->N/Z / <INV>\n100110111 10000100000000001 # B->N/Z / <INV>\n100111000 10000100000000001 # B->N/Z / <INV>\n100111001 10000110101100000 # MLH / MLH a,y\n100111010 10000100000000001 # B->N/Z / <INV>\n100111011 10000100000000001 # B->N/Z / RND\n100111100 10000100000000001 # B->N/Z / <INV>\n100111101 10000110101100000 # MLH / MLH a,x\n100111110 10000100000000001 # B->N/Z / <INV>\n100111111 10000100000000001 # B->N/Z / <INV>\n101000000 10000100000000001 # B->N/Z / <INV>\n101000001 10000100000000001 # B->N/Z / <INV>\n101000010 10000100000000001 # B->N/Z / <INV>\n101000011 10000100000000001 # B->N/Z / <INV>\n101000100 10000100000000001 # B->N/Z / <INV>\n101000101 10000110110100000 # MOD / MOD bp\n101000110 10000100000000001 # B->N/Z / <INV>\n101000111 10000100000000001 # B->N/Z / <INV>\n101001000 10000100000000001 # B->N/Z / PHM\n101001001 10000110110100000 # MOD / MOD #\n101001010 10000100000000001 # B->N/Z / <INV>\n101001011 10000100000000001 # B->N/Z / SWN\n101001100 10000100000000001 # B->N/Z / <INV>\n101001101 10000110110100000 # MOD / MOD a\n101001110 10000100000000001 # B->N/Z / <INV>\n101001111 10000100000000001 # B->N/Z / <INV>\n101010000 10000100000000001 # B->N/Z / <INV>\n101010001 10000100000000001 # B->N/Z / <INV>\n101010010 10000100000000001 # B->N/Z / <INV>\n101010011 10000100000000001 # B->N/Z / <INV>\n101010100 10000100000000001 # B->N/Z / <INV>\n101010101 10000110110100000 # MOD / MOD bp,x\n101010110 10000100000000001 # B->N/Z / <INV>\n101010111 10000100000000001 # B->N/Z / <INV>\n101011000 10000100000000001 # B->N/Z / <INV>\n101011001 10000110110100000 # MOD / MOD a,y\n101011010 10000100000000001 # B->N/Z / <INV>\n101011011 10000100000000001 # B->N/Z / SXY\n101011100 10000100000000001 # B->N/Z / <INV>\n101011101 10000110110100000 # MOD / MOD a,x\n101011110 10000100000000001 # B->N/Z / <INV>\n101011111 10000100000000001 # B->N/Z / <INV>\n101100000 10000100000000001 # B->N/Z / <INV>\n101100001 10000100000000001 # B->N/Z / <INV>\n101100010 10000100000000001 # B->N/Z / <INV>\n101100011 10000100000000001 # B->N/Z / <INV>\n101100100 10000100000000001 # B->N/Z / <INV>\n101100101 10000110110000000 # DIV / DIV bp\n101100110 10000100000000001 # B->N/Z / <INV>\n101100111 10000100000000001 # B->N/Z / <INV>\n101101000 10000100000000001 # B->N/Z / PLM\n101101001 10000110110000000 # DIV / DIV #\n101101010 10000100000000001 # B->N/Z / <INV>\n101101011 10000100000000001 # B->N/Z / SXZ\n101101100 10000100000000001 # B->N/Z / <INV>\n101101101 10000110110000000 # DIV / DIV a\n101101110 10000100000000001 # B->N/Z / <INV>\n101101111 10000100000000001 # B->N/Z / <INV>\n101110000 10000100000000001 # B->N/Z / <INV>\n101110001 10000100000000001 # B->N/Z / <INV>\n101110010 10000100000000001 # B->N/Z / <INV>\n101110011 10000100000000001 # B->N/Z / <INV>\n101110100 10000100000000001 # B->N/Z / <INV>\n101110101 10000110110000000 # DIV / DIV bp,x\n101110110 10000100000000001 # B->N/Z / <INV>\n101110111 10000100000000001 # B->N/Z / <INV>\n101111000 10000100000000001 # B->N/Z / <INV>\n101111001 10000110110000000 # DIV / DIV a,y\n101111010 10000100000000001 # B->N/Z / <INV>\n101111011 10000100000000001 # B->N/Z / SYZ\n101111100 10000100000000001 # B->N/Z / <INV>\n101111101 10000110110000000 # DIV / DIV a,x\n101111110 10000100000000001 # B->N/Z / <INV>\n101111111 10000100000000001 # B->N/Z / <INV>\n110000000 10000100000000001 # B->N/Z / <INV>\n110000001 10000100000000001 # B->N/Z / STA (bp,x),y\n110000010 10000100000000001 # B->N/Z / STA sp,y\n110000011 10000100000000001 # B->N/Z / <INV>\n110000100 10000100000000001 # B->N/Z / <INV>\n110000101 10000100000000001 # B->N/Z / <INV>\n110000110 10000100000000001 # B->N/Z / <INV>\n110000111 10000100000000001 # B->N/Z / <INV>\n110001000 10000100000000001 # B->N/Z / <INV>\n110001001 10000100000000001 # B->N/Z / <INV>\n110001010 10000100000000001 # B->N/Z / <INV>\n110001011 10000100000000001 # B->N/Z / <INV>\n110001100 10000100000000001 # B->N/Z / <INV>\n110001101 10000100000000001 # B->N/Z / <INV>\n110001110 10000100000000001 # B->N/Z / <INV>\n110001111 10000100000000001 # B->N/Z / <INV>\n110010000 10000100000000001 # B->N/Z / <INV>\n110010001 10000100000000001 # B->N/Z / STA pc,xy\n110010010 10000100000000001 # B->N/Z / <INV>\n110010011 10000100000000001 # B->N/Z / <INV>\n110010100 10000100000000001 # B->N/Z / <INV>\n110010101 10000100000000001 # B->N/Z / <INV>\n110010110 10000100000000001 # B->N/Z / <INV>\n110010111 10000100000000001 # B->N/Z / <INV>\n110011000 10000100000000001 # B->N/Z / <INV>\n110011001 10000100000000001 # B->N/Z / <INV>\n110011010 10000100000000001 # B->N/Z / <INV>\n110011011 10000100000000001 # B->N/Z / <INV>\n110011100 10000100000000001 # B->N/Z / <INV>\n110011101 10000100000000001 # B->N/Z / <INV>\n110011110 10000100000000001 # B->N/Z / <INV>\n110011111 10000100000000001 # B->N/Z / <INV>\n110100000 10000100000000001 # B->N/Z / <INV>\n110100001 10000100000000001 # B->N/Z / <INV>\n110100010 10000100000000001 # B->N/Z / <INV>\n110100011 10000100000000001 # B->N/Z / <INV>\n110100100 10000100000000001 # B->N/Z / <INV>\n110100101 10000100000000001 # B->N/Z / <INV>\n110100110 10000100000000001 # B->N/Z / <INV>\n110100111 10000100000000001 # B->N/Z / <INV>\n110101000 10000100000000001 # B->N/Z / <INV>\n110101001 10000100000000001 # B->N/Z / <INV>\n110101010 10000100000000001 # B->N/Z / <INV>\n110101011 10000100000000001 # B->N/Z / <INV>\n110101100 10000100000000001 # B->N/Z / <INV>\n110101101 10000100000000001 # B->N/Z / <INV>\n110101110 10000100000000001 # B->N/Z / <INV>\n110101111 10000100000000001 # B->N/Z / <INV>\n110110000 10000100000000001 # B->N/Z / <INV>\n110110001 10000100000000001 # B->N/Z / <INV>\n110110010 10000100000000001 # B->N/Z / <INV>\n110110011 10000100000000001 # B->N/Z / <INV>\n110110100 10000100000000001 # B->N/Z / <INV>\n110110101 10000100000000001 # B->N/Z / <INV>\n110110110 10000100000000001 # B->N/Z / <INV>\n110110111 10000100000000001 # B->N/Z / <INV>\n110111000 10000100000000001 # B->N/Z / <INV>\n110111001 10000100000000001 # B->N/Z / <INV>\n110111010 10000100000000001 # B->N/Z / <INV>\n110111011 10000100000000001 # B->N/Z / <INV>\n110111100 10000100000000001 # B->N/Z / <INV>\n110111101 10000100000000001 # B->N/Z / <INV>\n110111110 10000100000000001 # B->N/Z / <INV>\n110111111 10000100000000001 # B->N/Z / <INV>\n111000000 10000100000000001 # B->N/Z / <INV>\n111000001 10000100000000001 # B->N/Z / <INV>\n111000010 10000100000000001 # B->N/Z / <INV>\n111000011 10000100000000001 # B->N/Z / <INV>\n111000100 10000100000000001 # B->N/Z / <INV>\n111000101 10000100000000001 # B->N/Z / <INV>\n111000110 10000110000001110 # DCC / DCC bp\n111000111 10000100000000001 # B->N/Z / <INV>\n111001000 10000110111100000 # CBH / CBH\n111001001 10000100000000001 # B->N/Z / <INV>\n111001010 10000110011100100 # LSR W / LRW a\n111001011 10000110011000100 # ASR W / ARW a\n111001100 10000100000000001 # B->N/Z / <INV>\n111001101 10000100000000001 # B->N/Z / <INV>\n111001110 10000110000001110 # DCC / DCC a\n111001111 10000100000000001 # B->N/Z / <INV>\n111010000 10000100000000001 # B->N/Z / <INV>\n111010001 10000100000000001 # B->N/Z / <INV>\n111010010 10000100000000001 # B->N/Z / <INV>\n111010011 10000100000000001 # B->N/Z / <INV>\n111010100 10000100000000001 # B->N/Z / <INV>\n111010101 10000100000000001 # B->N/Z / <INV>\n111010110 10000110000001110 # DCC / DCC bp,x\n111010111 10000100000000001 # B->N/Z / <INV>\n111011000 10000100000000001 # B->N/Z / <INV>\n111011001 10000100000000001 # B->N/Z / <INV>\n111011010 10000100000000001 # B->N/Z / <INV>\n111011011 10000100000000001 # B->N/Z / <INV>\n111011100 10000100000000001 # B->N/Z / <INV>\n111011101 10000100000000001 # B->N/Z / <INV>\n111011110 10000110000001110 # DCC / DCC a,x\n111011111 10000100000000001 # B->N/Z / <INV>\n111100000 10000100000000001 # B->N/Z / <INV>\n111100001 10000100000000001 # B->N/Z / LDA (bp,x),y\n111100010 10000100000000001 # B->N/Z / LDA sp,y\n111100011 10000100000000001 # B->N/Z / <INV>\n111100100 10000100000000001 # B->N/Z / <INV>\n111100101 10000100000000001 # B->N/Z / <INV>\n111100110 10000110000001010 # ICC / ICC bp\n111100111 10000100000000001 # B->N/Z / <INV>\n111101000 10000110111000000 # CHB / CHB\n111101001 10000100000000001 # B->N/Z / <INV>\n111101010 10000100000000001 # B->N/Z / NOP\n111101011 10000110100100100 # ROR W / RRW a\n111101100 10000100000000001 # B->N/Z / <INV>\n111101101 10000100000000001 # B->N/Z / <INV>\n111101110 10000110000001010 # ICC / ICC a\n111101111 10000100000000001 # B->N/Z / WAI\n111110000 10000100000000001 # B->N/Z / <INV>\n111110001 10000100000000001 # B->N/Z / LDA pc,xy\n111110010 10000100000000001 # B->N/Z / <INV>\n111110011 10000100000000001 # B->N/Z / <INV>\n111110100 10000100000000001 # B->N/Z / <INV>\n111110101 10000100000000001 # B->N/Z / <INV>\n111110110 10000110000001010 # ICC / ICC bp,x\n111110111 10000100000000001 # B->N/Z / <INV>\n111111000 10000100000000001 # B->N/Z / <INV>\n111111001 10000100000000001 # B->N/Z / <INV>\n111111010 10000100000000001 # B->N/Z / <INV>\n111111011 10000100000000001 # B->N/Z / <INV>\n111111100 10000100000000001 # B->N/Z / <INV>\n111111101 10000100000000001 # B->N/Z / <INV>\n111111110 10000110000001010 # ICC / ICC a,x\n111111111 10000100000000001 # B->N/Z / STP")) ALU (
    .in(A_CTRL[9:1]), .out(ALU_out));
  PLA #(.in_width(8), .out_width(1), .\table ("00000100 1 # TSB bp\n00001100 1 # TSB a\n00010100 1 # TRB bp\n00011100 1 # TRB a\n00000111 1 # RMB0 bp\n00010111 1 # RMB1 bp\n00100111 1 # RMB2 bp\n00110111 1 # RMB3 bp\n01000111 1 # RMB4 bp\n01010111 1 # RMB5 bp\n01100111 1 # RMB6 bp\n01110111 1 # RMB7 bp\n10000111 1 # SMB0 bp\n10010111 1 # SMB1 bp\n10100111 1 # SMB2 bp\n10110111 1 # SMB3 bp\n11000111 1 # SMB4 bp\n11010111 1 # SMB5 bp\n11100111 1 # SMB6 bp\n11110111 1 # SMB7 bp")) AZS (
    .in(A_CTRL[8:1]), .out(AZS_out));
  Multiplexer #(.enable("false"), .width(8)) multiplexer_2 (
    .in0(multiplexer_1_out), .in1(ANDQ), .out({NI, multiplexer_2_out}), .sel(AZS_out));
  // Probe on A
  // Probe on B[7:0]
  // Probe on Q_t
  // Probe on Q
  Multiplexer #(.enable("false"), .width(17)) multiplexer_3 (
    .in0({17{1'b0}}), .in1(ALU_out), .out({SEL4, SEL3, SEL2, SEL1, SEL0}), .sel(A_CTRL[0]));
  nor nor_1 (ZI, multiplexer_2_out[0], multiplexer_2_out[1], multiplexer_2_out[2], multiplexer_2_out[3], multiplexer_2_out[5], multiplexer_2_out[6], NI, multiplexer_2_out[4]);
  Decoder #(.enable("false"), .select(3)) decoder_1 (
    .out0(decoder_1_out0[0]), .out1(decoder_1_out0[1]), .out2(decoder_1_out0[2]), .out3(decoder_1_out0[3]),
    .out4(decoder_1_out0[4]), .out5(decoder_1_out0[5]), .out6(decoder_1_out0[6]), .out7(decoder_1_out0[7]),
    .sel(A_CTRL[7:5]));
  Multiplexer #(.enable("false"), .width(8)) multiplexer_4 (
    .in0(A), .in1(decoder_1_out0), .out(multiplexer_4_out), .sel(SEL1[0]));
  PLA #(.in_width(8), .out_width(9), .\table ("00000000 000000000 # 00\n00000001 000000001 # 01\n00000010 000000010 # 02\n00000011 000000011 # 03\n00000100 000000100 # 04\n00000101 000000101 # 05\n00000110 000000110 # 06\n00000111 000000111 # 07\n00001000 000001000 # 08\n00001001 000001001 # 09\n00001010 000010000 # 10\n00001011 000010001 # 11\n00001100 000010010 # 12\n00001101 000010011 # 13\n00001110 000010100 # 14\n00001111 000010101 # 15\n00010000 000010110 # 16\n00010001 000010111 # 17\n00010010 000011000 # 18\n00010011 000011001 # 19\n00010100 000100000 # 20\n00010101 000100001 # 21\n00010110 000100010 # 22\n00010111 000100011 # 23\n00011000 000100100 # 24\n00011001 000100101 # 25\n00011010 000100110 # 26\n00011011 000100111 # 27\n00011100 000101000 # 28\n00011101 000101001 # 29\n00011110 000110000 # 30\n00011111 000110001 # 31\n00100000 000110010 # 32\n00100001 000110011 # 33\n00100010 000110100 # 34\n00100011 000110101 # 35\n00100100 000110110 # 36\n00100101 000110111 # 37\n00100110 000111000 # 38\n00100111 000111001 # 39\n00101000 001000000 # 40\n00101001 001000001 # 41\n00101010 001000010 # 42\n00101011 001000011 # 43\n00101100 001000100 # 44\n00101101 001000101 # 45\n00101110 001000110 # 46\n00101111 001000111 # 47\n00110000 001001000 # 48\n00110001 001001001 # 49\n00110010 001010000 # 50\n00110011 001010001 # 51\n00110100 001010010 # 52\n00110101 001010011 # 53\n00110110 001010100 # 54\n00110111 001010101 # 55\n00111000 001010110 # 56\n00111001 001010111 # 57\n00111010 001011000 # 58\n00111011 001011001 # 59\n00111100 001100000 # 60\n00111101 001100001 # 61\n00111110 001100010 # 62\n00111111 001100011 # 63\n01000000 001100100 # 64\n01000001 001100101 # 65\n01000010 001100110 # 66\n01000011 001100111 # 67\n01000100 001101000 # 68\n01000101 001101001 # 69\n01000110 001110000 # 70\n01000111 001110001 # 71\n01001000 001110010 # 72\n01001001 001110011 # 73\n01001010 001110100 # 74\n01001011 001110101 # 75\n01001100 001110110 # 76\n01001101 001110111 # 77\n01001110 001111000 # 78\n01001111 001111001 # 79\n01010000 010000000 # 80\n01010001 010000001 # 81\n01010010 010000010 # 82\n01010011 010000011 # 83\n01010100 010000100 # 84\n01010101 010000101 # 85\n01010110 010000110 # 86\n01010111 010000111 # 87\n01011000 010001000 # 88\n01011001 010001001 # 89\n01011010 010010000 # 90\n01011011 010010001 # 91\n01011100 010010010 # 92\n01011101 010010011 # 93\n01011110 010010100 # 94\n01011111 010010101 # 95\n01100000 010010110 # 96\n01100001 010010111 # 97\n01100010 010011000 # 98\n01100011 010011001 # 99\n01100100 100000000 # >99\n01100101 100000000 # >99\n01100110 100000000 # >99\n01100111 100000000 # >99\n01101000 100000000 # >99\n01101001 100000000 # >99\n01101010 100000000 # >99\n01101011 100000000 # >99\n01101100 100000000 # >99\n01101101 100000000 # >99\n01101110 100000000 # >99\n01101111 100000000 # >99\n01110000 100000000 # >99\n01110001 100000000 # >99\n01110010 100000000 # >99\n01110011 100000000 # >99\n01110100 100000000 # >99\n01110101 100000000 # >99\n01110110 100000000 # >99\n01110111 100000000 # >99\n01111000 100000000 # >99\n01111001 100000000 # >99\n01111010 100000000 # >99\n01111011 100000000 # >99\n01111100 100000000 # >99\n01111101 100000000 # >99\n01111110 100000000 # >99\n01111111 100000000 # >99\n10000000 100000000 # >99\n10000001 100000000 # >99\n10000010 100000000 # >99\n10000011 100000000 # >99\n10000100 100000000 # >99\n10000101 100000000 # >99\n10000110 100000000 # >99\n10000111 100000000 # >99\n10001000 100000000 # >99\n10001001 100000000 # >99\n10001010 100000000 # >99\n10001011 100000000 # >99\n10001100 100000000 # >99\n10001101 100000000 # >99\n10001110 100000000 # >99\n10001111 100000000 # >99\n10010000 100000000 # >99\n10010001 100000000 # >99\n10010010 100000000 # >99\n10010011 100000000 # >99\n10010100 100000000 # >99\n10010101 100000000 # >99\n10010110 100000000 # >99\n10010111 100000000 # >99\n10011000 100000000 # >99\n10011001 100000000 # >99\n10011010 100000000 # >99\n10011011 100000000 # >99\n10011100 100000000 # >99\n10011101 100000000 # >99\n10011110 100000000 # >99\n10011111 100000000 # >99\n10100000 100000000 # >99\n10100001 100000000 # >99\n10100010 100000000 # >99\n10100011 100000000 # >99\n10100100 100000000 # >99\n10100101 100000000 # >99\n10100110 100000000 # >99\n10100111 100000000 # >99\n10101000 100000000 # >99\n10101001 100000000 # >99\n10101010 100000000 # >99\n10101011 100000000 # >99\n10101100 100000000 # >99\n10101101 100000000 # >99\n10101110 100000000 # >99\n10101111 100000000 # >99\n10110000 100000000 # >99\n10110001 100000000 # >99\n10110010 100000000 # >99\n10110011 100000000 # >99\n10110100 100000000 # >99\n10110101 100000000 # >99\n10110110 100000000 # >99\n10110111 100000000 # >99\n10111000 100000000 # >99\n10111001 100000000 # >99\n10111010 100000000 # >99\n10111011 100000000 # >99\n10111100 100000000 # >99\n10111101 100000000 # >99\n10111110 100000000 # >99\n10111111 100000000 # >99\n11000000 100000000 # >99\n11000001 100000000 # >99\n11000010 100000000 # >99\n11000011 100000000 # >99\n11000100 100000000 # >99\n11000101 100000000 # >99\n11000110 100000000 # >99\n11000111 100000000 # >99\n11001000 100000000 # >99\n11001001 100000000 # >99\n11001010 100000000 # >99\n11001011 100000000 # >99\n11001100 100000000 # >99\n11001101 100000000 # >99\n11001110 100000000 # >99\n11001111 100000000 # >99\n11010000 100000000 # >99\n11010001 100000000 # >99\n11010010 100000000 # >99\n11010011 100000000 # >99\n11010100 100000000 # >99\n11010101 100000000 # >99\n11010110 100000000 # >99\n11010111 100000000 # >99\n11011000 100000000 # >99\n11011001 100000000 # >99\n11011010 100000000 # >99\n11011011 100000000 # >99\n11011100 100000000 # >99\n11011101 100000000 # >99\n11011110 100000000 # >99\n11011111 100000000 # >99\n11100000 100000000 # >99\n11100001 100000000 # >99\n11100010 100000000 # >99\n11100011 100000000 # >99\n11100100 100000000 # >99\n11100101 100000000 # >99\n11100110 100000000 # >99\n11100111 100000000 # >99\n11101000 100000000 # >99\n11101001 100000000 # >99\n11101010 100000000 # >99\n11101011 100000000 # >99\n11101100 100000000 # >99\n11101101 100000000 # >99\n11101110 100000000 # >99\n11101111 100000000 # >99\n11110000 100000000 # >99\n11110001 100000000 # >99\n11110010 100000000 # >99\n11110011 100000000 # >99\n11110100 100000000 # >99\n11110101 100000000 # >99\n11110110 100000000 # >99\n11110111 100000000 # >99\n11111000 100000000 # >99\n11111001 100000000 # >99\n11111010 100000000 # >99\n11111011 100000000 # >99\n11111100 100000000 # >99\n11111101 100000000 # >99\n11111110 100000000 # >99\n11111111 100000000 # >99")) CHB (
    .in(B[7:0]), .out(CHB_out));
  PLA #(.in_width(8), .out_width(9), .\table ("00000000 000000000 # 00\n00000001 000000001 # 01\n00000010 000000010 # 02\n00000011 000000011 # 03\n00000100 000000100 # 04\n00000101 000000101 # 05\n00000110 000000110 # 06\n00000111 000000111 # 07\n00001000 000001000 # 08\n00001001 000001001 # 09\n00001010 100000000 # XX\n00001011 100000000 # XX\n00001100 100000000 # XX\n00001101 100000000 # XX\n00001110 100000000 # XX\n00001111 100000000 # XX\n00010000 000001010 # 10\n00010001 000001011 # 11\n00010010 000001100 # 12\n00010011 000001101 # 13\n00010100 000001110 # 14\n00010101 000001111 # 15\n00010110 000010000 # 16\n00010111 000010001 # 17\n00011000 000010010 # 18\n00011001 000010011 # 19\n00011010 100000000 # XX\n00011011 100000000 # XX\n00011100 100000000 # XX\n00011101 100000000 # XX\n00011110 100000000 # XX\n00011111 100000000 # XX\n00100000 000010100 # 20\n00100001 000010101 # 21\n00100010 000010110 # 22\n00100011 000010111 # 23\n00100100 000011000 # 24\n00100101 000011001 # 25\n00100110 000011010 # 26\n00100111 000011011 # 27\n00101000 000011100 # 28\n00101001 000011101 # 29\n00101010 100000000 # XX\n00101011 100000000 # XX\n00101100 100000000 # XX\n00101101 100000000 # XX\n00101110 100000000 # XX\n00101111 100000000 # XX\n00110000 000011110 # 30\n00110001 000011111 # 31\n00110010 000100000 # 32\n00110011 000100001 # 33\n00110100 000100010 # 34\n00110101 000100011 # 35\n00110110 000100100 # 36\n00110111 000100101 # 37\n00111000 000100110 # 38\n00111001 000100111 # 39\n00111010 100000000 # XX\n00111011 100000000 # XX\n00111100 100000000 # XX\n00111101 100000000 # XX\n00111110 100000000 # XX\n00111111 100000000 # XX\n01000000 000101000 # 40\n01000001 000101001 # 41\n01000010 000101010 # 42\n01000011 000101011 # 43\n01000100 000101100 # 44\n01000101 000101101 # 45\n01000110 000101110 # 46\n01000111 000101111 # 47\n01001000 000110000 # 48\n01001001 000110001 # 49\n01001010 100000000 # XX\n01001011 100000000 # XX\n01001100 100000000 # XX\n01001101 100000000 # XX\n01001110 100000000 # XX\n01001111 100000000 # XX\n01010000 000110010 # 50\n01010001 000110011 # 51\n01010010 000110100 # 52\n01010011 000110101 # 53\n01010100 000110110 # 54\n01010101 000110111 # 55\n01010110 000111000 # 56\n01010111 000111001 # 57\n01011000 000111010 # 58\n01011001 000111011 # 59\n01011010 100000000 # XX\n01011011 100000000 # XX\n01011100 100000000 # XX\n01011101 100000000 # XX\n01011110 100000000 # XX\n01011111 100000000 # XX\n01100000 000111100 # 60\n01100001 000111101 # 61\n01100010 000111110 # 62\n01100011 000111111 # 63\n01100100 001000000 # 64\n01100101 001000001 # 65\n01100110 001000010 # 66\n01100111 001000011 # 67\n01101000 001000100 # 68\n01101001 001000101 # 69\n01101010 100000000 # XX\n01101011 100000000 # XX\n01101100 100000000 # XX\n01101101 100000000 # XX\n01101110 100000000 # XX\n01101111 100000000 # XX\n01110000 001000110 # 70\n01110001 001000111 # 71\n01110010 001001000 # 72\n01110011 001001001 # 73\n01110100 001001010 # 74\n01110101 001001011 # 75\n01110110 001001100 # 76\n01110111 001001101 # 77\n01111000 001001110 # 78\n01111001 001001111 # 79\n01111010 100000000 # XX\n01111011 100000000 # XX\n01111100 100000000 # XX\n01111101 100000000 # XX\n01111110 100000000 # XX\n01111111 100000000 # XX\n10000000 001010000 # 80\n10000001 001010001 # 81\n10000010 001010010 # 82\n10000011 001010011 # 83\n10000100 001010100 # 84\n10000101 001010101 # 85\n10000110 001010110 # 86\n10000111 001010111 # 87\n10001000 001011000 # 88\n10001001 001011001 # 89\n10001010 100000000 # XX\n10001011 100000000 # XX\n10001100 100000000 # XX\n10001101 100000000 # XX\n10001110 100000000 # XX\n10001111 100000000 # XX\n10010000 001011010 # 90\n10010001 001011011 # 91\n10010010 001011100 # 92\n10010011 001011101 # 93\n10010100 001011110 # 94\n10010101 001011111 # 95\n10010110 001100000 # 96\n10010111 001100001 # 97\n10011000 001100010 # 98\n10011001 001100011 # 99\n10011010 100000000 # XX\n10011011 100000000 # XX\n10011100 100000000 # XX\n10011101 100000000 # XX\n10011110 100000000 # XX\n10011111 100000000 # XX\n10100000 100000000 # XX\n10100001 100000000 # XX\n10100010 100000000 # XX\n10100011 100000000 # XX\n10100100 100000000 # XX\n10100101 100000000 # XX\n10100110 100000000 # XX\n10100111 100000000 # XX\n10101000 100000000 # XX\n10101001 100000000 # XX\n10101010 100000000 # XX\n10101011 100000000 # XX\n10101100 100000000 # XX\n10101101 100000000 # XX\n10101110 100000000 # XX\n10101111 100000000 # XX\n10110000 100000000 # XX\n10110001 100000000 # XX\n10110010 100000000 # XX\n10110011 100000000 # XX\n10110100 100000000 # XX\n10110101 100000000 # XX\n10110110 100000000 # XX\n10110111 100000000 # XX\n10111000 100000000 # XX\n10111001 100000000 # XX\n10111010 100000000 # XX\n10111011 100000000 # XX\n10111100 100000000 # XX\n10111101 100000000 # XX\n10111110 100000000 # XX\n10111111 100000000 # XX\n11000000 100000000 # XX\n11000001 100000000 # XX\n11000010 100000000 # XX\n11000011 100000000 # XX\n11000100 100000000 # XX\n11000101 100000000 # XX\n11000110 100000000 # XX\n11000111 100000000 # XX\n11001000 100000000 # XX\n11001001 100000000 # XX\n11001010 100000000 # XX\n11001011 100000000 # XX\n11001100 100000000 # XX\n11001101 100000000 # XX\n11001110 100000000 # XX\n11001111 100000000 # XX\n11010000 100000000 # XX\n11010001 100000000 # XX\n11010010 100000000 # XX\n11010011 100000000 # XX\n11010100 100000000 # XX\n11010101 100000000 # XX\n11010110 100000000 # XX\n11010111 100000000 # XX\n11011000 100000000 # XX\n11011001 100000000 # XX\n11011010 100000000 # XX\n11011011 100000000 # XX\n11011100 100000000 # XX\n11011101 100000000 # XX\n11011110 100000000 # XX\n11011111 100000000 # XX\n11100000 100000000 # XX\n11100001 100000000 # XX\n11100010 100000000 # XX\n11100011 100000000 # XX\n11100100 100000000 # XX\n11100101 100000000 # XX\n11100110 100000000 # XX\n11100111 100000000 # XX\n11101000 100000000 # XX\n11101001 100000000 # XX\n11101010 100000000 # XX\n11101011 100000000 # XX\n11101100 100000000 # XX\n11101101 100000000 # XX\n11101110 100000000 # XX\n11101111 100000000 # XX\n11110000 100000000 # XX\n11110001 100000000 # XX\n11110010 100000000 # XX\n11110011 100000000 # XX\n11110100 100000000 # XX\n11110101 100000000 # XX\n11110110 100000000 # XX\n11110111 100000000 # XX\n11111000 100000000 # XX\n11111001 100000000 # XX\n11111010 100000000 # XX\n11111011 100000000 # XX\n11111100 100000000 # XX\n11111101 100000000 # XX\n11111110 100000000 # XX\n11111111 100000000 # XX")) CBH (
    .in(B[7:0]), .out(CBH_out));
  and and_1 (and_1_out[1], ~A_CTRL[1], ~A_CTRL[2], ~A_CTRL[3], A_CTRL[4], ~A_CTRL[5], A_CTRL[6], ~A_CTRL[7], ~A_CTRL[8], ~A_CTRL[9]);  // AND_Gate
  ADDER adder_1 (
    .QL(adder_1_ql), .V_O(VI), .C_O(adder_1_c_o), .QH(adder_1_qh), .D_I(FL[3]), .C_I(FL[0]), .SEL(SEL1),
    .A(A), .B(B));
  assign ANDQ = A & B[7:0];  // AND_Gate and_2, 8 bits wide
  assign and_3_out = ~multiplexer_4_out & B[7:0];  // AND_Gate and_3, 8 bits wide
  assign or_1_out = multiplexer_4_out | B[7:0];  // OR_Gate or_1, 8 bits wide
  assign xor_1_out = A ^ B[7:0];  // XOR_Gate xor_1, 8 bits wide
  Multiplexer #(.enable("false")) multiplexer_5 (.in0(B[7]), .in1(B[15]), .out(multiplexer_5_out), .sel(SEL1[1]));
  Multiplexer #(.enable("false"), .width(8)) multiplexer_6 (
    .in0({B[6:0], 1'b0}), .in1({B[6:0], 1'b0}), .out(multiplexer_6_out), .sel(SEL1[1]));
  Multiplexer #(.enable("false")) multiplexer_7 (.in0(B[0]), .in1(B[0]), .out(multiplexer_7_out), .sel(SEL1[1]));
  Multiplexer #(.enable("false"), .width(8)) multiplexer_8 (
    .in0({{2{B[7]}}, B[6:1]}), .in1(B[8:1]), .out(multiplexer_8_out), .sel(SEL1[1]));
  Multiplexer #(.enable("false")) multiplexer_9 (.in0(B[0]), .in1(B[0]), .out(multiplexer_9_out), .sel(SEL1[1]));
  Multiplexer #(.enable("false"), .width(8)) multiplexer_10 (
    .in0({1'b0, B[7:1]}), .in1(B[8:1]), .out(multiplexer_10_out), .sel(SEL1[1]));
  Multiplexer #(.enable("false")) multiplexer_11 (.in0(B[7]), .in1(B[15]), .out(multiplexer_11_out), .sel(SEL1[1]));
  Multiplexer #(.enable("false"), .width(8)) multiplexer_12 (
    .in0({B[6:0], FL[0]}), .in1({B[6:0], FL[0]}), .out(multiplexer_12_out), .sel(SEL1[1]));
  Multiplexer #(.enable("false")) multiplexer_13 (.in0(B[0]), .in1(B[0]), .out(multiplexer_13_out), .sel(SEL1[1]));
  Multiplexer #(.enable("false"), .width(8)) multiplexer_14 (
    .in0({FL[0], B[7:1]}), .in1(B[8:1]), .out(multiplexer_14_out), .sel(SEL1[1]));
  Multiplier #(.mode("unsigned")) multiplier_1 (
    .a(A), .b(B[7:0]), .out(multiplier_1_out), .cout(multiplier_1_cout));  // open: cin
  Divider #(.mode("unsigned")) divider_1 (.a(A), .b(B[7:0]), .out(divider_1_out), .rem(divider_1_rem));  // open: upper
  Multiplexer #(.enable("false"), .select(2)) multiplexer_15 (
    .in0(CI), .in1(SEL0), .in2(B[0]), .out(multiplexer_15_out));  // open: in3, sel
  Multiplexer #(.enable("false"), .select(2)) multiplexer_16 (
    .in0(ZI), .in1(SEL0), .in2(B[1]), .out(multiplexer_16_out));  // open: in3, sel
  Multiplexer #(.enable("false")) multiplexer_17 (
    .in0(SEL0), .in1(not_1_out), .out(multiplexer_17_out), .sel(and_1_out[1]));
  not not_1 (not_1_out, B[2]);
  Multiplexer #(.enable("false")) multiplexer_18 (.in0(SEL0), .in1(B[3]), .out(multiplexer_18_out), .sel(and_1_out[1]));
  Multiplexer #(.enable("false")) multiplexer_19 (.in0(VI), .in1(B[6]), .out(multiplexer_19_out), .sel(SEL0));
  Multiplexer #(.enable("false"), .select(2)) multiplexer_20 (
    .in0(multiplexer_19_out), .in1(SEL0), .in2(B[6]), .out(multiplexer_20_out));  // open: in3, sel
  Multiplexer #(.enable("false")) multiplexer_21 (.in0(NI), .in1(B[7]), .out(multiplexer_21_out), .sel(SEL0));
  Multiplexer #(.enable("false"), .select(2)) multiplexer_22 (
    .in0(multiplexer_21_out), .in1(SEL0), .in2(B[7]), .out(multiplexer_22_out));  // open: in3, sel
  PLA #(.in_width(9), .out_width(3), .\table ("011100011 001 # INW bp\n011000011 001 # DEW bp\n011001011 010 # ASW/ALW a\n111001011 011 # ARW a\n111001010 100 # LRW a\n111101011 101 # RRW a\n011101011 110 # ROW/RLW a")) QHS (
    .in(A_CTRL[9:1]), .out(QHS_out));
  or or_2 (or_2_out, multiplexer_17_out, CIB);
  or or_3 (or_3_out, multiplexer_20_out, SOB);
  Multiplexer #(.enable("false"), .select(3), .width(8)) multiplexer_23 (
    .in0({8{1'b0}}), .in1(adder_1_qh), .in2(B[14:7]), .in3({{2{B[15]}}, B[14:9]}), .in4({1'b0, B[15:9]}),
    .in5(B[14:7]), .in6({FL[0], B[15:9]}), .out(Q[15:8]));  // open: in7, sel
  D_Flip_Flop #(.enable("true"), .trigger("falling")) u_C (
    .clk(C), .D(multiplexer_15_out), .Q(FL[0]), .en(SEL4[0]), .reset(R));  // open: Qn, preset
  D_Flip_Flop #(.enable("true"), .trigger("falling")) Z (
    .clk(C), .D(multiplexer_16_out), .Q(FL[1]), .en(SEL4[1]), .reset(R));  // open: Qn, preset
  D_Flip_Flop #(.enable("true"), .trigger("falling")) I (
    .clk(C), .D(or_2_out), .Qn(FL[2]), .en(or_4_out), .reset(R));  // open: Q, preset
  or or_4 (or_4_out, SEL4[2], CIB);
  D_Flip_Flop #(.enable("true"), .trigger("falling")) D (
    .clk(C), .D(multiplexer_18_out), .Q(FL[3]), .en(SEL4[3]), .reset(R));  // open: Qn, preset
  D_Flip_Flop #(.enable("true"), .trigger("falling")) E (
    .clk(C), .D(SEL0), .Qn(FL[4]), .en(SEL4[4]), .reset(R));  // open: Q, preset
  D_Flip_Flop #(.enable("true"), .trigger("falling")) V (
    .clk(C), .D(or_3_out), .Q(FL[5]), .en(or_5_out), .reset(R));  // open: Qn, preset
  or or_5 (or_5_out, SEL4[5], SOB);
  D_Flip_Flop #(.enable("true"), .trigger("falling")) N (
    .clk(C), .D(multiplexer_22_out), .Q(FL[6]), .en(SEL4[6]), .reset(R));  // open: Qn, preset
  Multiplexer #(.enable("false"), .select(4), .width(8)) multiplexer_24 (
    .in0(adder_1_ql), .in1(ANDQ), .in2(and_3_out), .in3(or_1_out), .in4(xor_1_out), .in5(multiplexer_6_out),
    .in6(multiplexer_8_out), .in7(multiplexer_10_out), .in8(multiplexer_12_out), .in9(multiplexer_14_out),
    .in10(multiplier_1_out), .in11(multiplier_1_cout), .in12(divider_1_out), .in13(divider_1_rem),
    .in14(CHB_out[7:0]), .in15(CBH_out[7:0]), .out(Q_t));  // open: sel
  Multiplexer #(.enable("false"), .select(4)) multiplexer_25 (
    .in0(adder_1_c_o), .in1(1'b0), .in2(1'b0), .in3(1'b0), .in4(1'b0), .in5(multiplexer_5_out),
    .in6(multiplexer_7_out), .in7(multiplexer_9_out), .in8(multiplexer_11_out), .in9(multiplexer_13_out),
    .in10(or_6_out), .in11(or_7_out), .in12(or_8_out), .in13(or_9_out), .in14(CHB_out[8]), .in15(CBH_out[8]),
    .out(CI));  // open: sel
  or or_6 (or_6_out, multiplier_1_cout[0], multiplier_1_cout[1], multiplier_1_cout[2], multiplier_1_cout[3], multiplier_1_cout[5], multiplier_1_cout[6], multiplier_1_cout[7], multiplier_1_cout[4]);
  or or_7 (or_7_out, multiplier_1_out[0], multiplier_1_out[1], multiplier_1_out[2], multiplier_1_out[3], multiplier_1_out[5], multiplier_1_out[6], multiplier_1_out[7], multiplier_1_out[4]);
  or or_8 (or_8_out, divider_1_rem[0], divider_1_rem[1], divider_1_rem[2], divider_1_rem[3], divider_1_rem[5], divider_1_rem[6], divider_1_rem[7], divider_1_rem[4]);
  or or_9 (or_9_out, divider_1_out[0], divider_1_out[1], divider_1_out[2], divider_1_out[3], divider_1_out[5], divider_1_out[6], divider_1_out[7], divider_1_out[4]);
  Multiplexer #(.enable("false"), .width(8)) multiplexer_26 (.in0(Q_t), .in1(B[7:0]), .out(Q[7:0]), .sel(SEL0));
  LED C_2 (.in(FL[0]));
  LED Z_2 (.in(FL[1]));
  LED I_2 (.in(FL[2]));
  LED D_2 (.in(FL[3]));
  LED E_2 (.in(FL[4]));
  LED V_2 (.in(FL[5]));
  LED N_2 (.in(FL[6]));
  Clock clock_1 (.out(CC));
  Counter #(.max('h1ff), .ongoal("stay"), .trigger("falling"), .width(9)) counter_1 (
    .Q(AA), .clk(CC));  // open: load, D, count, carry, clr
  PLA #(.in_width(9), .out_width(6), .\table ("000000000 000000 # B->N/Z\n000000001 011000 # OR\n000000010 000101 # CLR E\n000000011 001100 # SET E\n000000100 010010 # TSB\n000000101 011000 # OR\n000000110 100001 # ASL\n000000111 010011 # RMB\n000001000 000000 # B->N/Z\n000001001 011000 # OR\n000001010 100001 # ASL\n000001011 000000 # B->N/Z\n000001100 010010 # TSB\n000001101 011000 # OR\n000001110 100001 # ASL\n000001111 000000 # B->N/Z\n000010000 000000 # B->N/Z\n000010001 011000 # OR\n000010010 011000 # OR\n000010011 000000 # B->N/Z\n000010100 010001 # TRB\n000010101 011000 # OR\n000010110 100001 # ASL\n000010111 010011 # RMB\n000011000 000001 # CLR C\n000011001 011000 # OR\n000011010 011101 # INC\n000011011 011101 # INC\n000011100 010001 # TRB\n000011101 011000 # OR\n000011110 100001 # ASL\n000011111 000000 # B->N/Z\n000100000 000000 # B->N/Z\n000100001 010111 # AND\n000100010 000000 # B->N/Z\n000100011 000000 # B->N/Z\n000100100 010000 # BIT\n000100101 010111 # AND\n000100110 100111 # ROL\n000100111 010011 # RMB\n000101000 001111 # WR FL\n000101001 010111 # AND\n000101010 100111 # ROL\n000101011 000000 # B->N/Z\n000101100 010000 # BIT\n000101101 010111 # AND\n000101110 100111 # ROL\n000101111 000000 # B->N/Z\n000110000 000000 # B->N/Z\n000110001 010111 # AND\n000110010 010111 # AND\n000110011 000000 # B->N/Z\n000110100 010000 # BIT\n000110101 010111 # AND\n000110110 100111 # ROL\n000110111 010011 # RMB\n000111000 001000 # SET C\n000111001 010111 # AND\n000111010 011111 # DEC\n000111011 011111 # DEC\n000111100 010000 # BIT\n000111101 010111 # AND\n000111110 100111 # ROL\n000111111 000000 # B->N/Z\n001000000 001111 # WR FL\n001000001 011001 # XOR\n001000010 000000 # B->N/Z\n001000011 100011 # ASR\n001000100 100011 # ASR\n001000101 011001 # XOR\n001000110 100101 # LSR\n001000111 010011 # RMB\n001001000 000000 # B->N/Z\n001001001 011001 # XOR\n001001010 100101 # LSR\n001001011 000000 # B->N/Z\n001001100 000000 # B->N/Z\n001001101 011001 # XOR\n001001110 100101 # LSR\n001001111 000000 # B->N/Z\n001010000 000000 # B->N/Z\n001010001 011001 # XOR\n001010010 011001 # XOR\n001010011 000000 # B->N/Z\n001010100 100011 # ASR\n001010101 011001 # XOR\n001010110 100101 # LSR\n001010111 010011 # RMB\n001011000 000011 # CLR I\n001011001 011001 # XOR\n001011010 000000 # B->N/Z\n001011011 000000 # B->N/Z\n001011100 000000 # B->N/Z\n001011101 011001 # XOR\n001011110 100101 # LSR\n001011111 000000 # B->N/Z\n001100000 000000 # B->N/Z\n001100001 010101 # ADC\n001100010 000000 # B->N/Z\n001100011 000000 # B->N/Z\n001100100 000000 # B->N/Z\n001100101 010101 # ADC\n001100110 101001 # ROR\n001100111 010011 # RMB\n001101000 000000 # B->N/Z\n001101001 010101 # ADC\n001101010 101001 # ROR\n001101011 000000 # B->N/Z\n001101100 000000 # B->N/Z\n001101101 010101 # ADC\n001101110 101001 # ROR\n001101111 000000 # B->N/Z\n001110000 000000 # B->N/Z\n001110001 010101 # ADC\n001110010 010101 # ADC\n001110011 000000 # B->N/Z\n001110100 000000 # B->N/Z\n001110101 010101 # ADC\n001110110 101001 # ROR\n001110111 010011 # RMB\n001111000 001010 # SET I\n001111001 010101 # ADC\n001111010 000000 # B->N/Z\n001111011 000000 # B->N/Z\n001111100 000000 # B->N/Z\n001111101 010101 # ADC\n001111110 101001 # ROR\n001111111 000000 # B->N/Z\n010000000 000000 # B->N/Z\n010000001 000000 # B->N/Z\n010000010 000000 # B->N/Z\n010000011 000000 # B->N/Z\n010000100 000000 # B->N/Z\n010000101 000000 # B->N/Z\n010000110 000000 # B->N/Z\n010000111 010100 # SMB\n010001000 011111 # DEC\n010001001 010000 # BIT\n010001010 000000 # B->N/Z\n010001011 000000 # B->N/Z\n010001100 000000 # B->N/Z\n010001101 000000 # B->N/Z\n010001110 000000 # B->N/Z\n010001111 000000 # B->N/Z\n010010000 000000 # B->N/Z\n010010001 000000 # B->N/Z\n010010010 000000 # B->N/Z\n010010011 000000 # B->N/Z\n010010100 000000 # B->N/Z\n010010101 000000 # B->N/Z\n010010110 000000 # B->N/Z\n010010111 010100 # SMB\n010011000 000000 # B->N/Z\n010011001 000000 # B->N/Z\n010011010 000000 # B->N/Z\n010011011 000000 # B->N/Z\n010011100 000000 # B->N/Z\n010011101 000000 # B->N/Z\n010011110 000000 # B->N/Z\n010011111 000000 # B->N/Z\n010100000 000000 # B->N/Z\n010100001 000000 # B->N/Z\n010100010 000000 # B->N/Z\n010100011 000000 # B->N/Z\n010100100 000000 # B->N/Z\n010100101 000000 # B->N/Z\n010100110 000000 # B->N/Z\n010100111 010100 # SMB\n010101000 000000 # B->N/Z\n010101001 000000 # B->N/Z\n010101010 000000 # B->N/Z\n010101011 000000 # B->N/Z\n010101100 000000 # B->N/Z\n010101101 000000 # B->N/Z\n010101110 000000 # B->N/Z\n010101111 000000 # B->N/Z\n010110000 000000 # B->N/Z\n010110001 000000 # B->N/Z\n010110010 000000 # B->N/Z\n010110011 000000 # B->N/Z\n010110100 000000 # B->N/Z\n010110101 000000 # B->N/Z\n010110110 000000 # B->N/Z\n010110111 010100 # SMB\n010111000 000110 # CLR V\n010111001 000000 # B->N/Z\n010111010 000000 # B->N/Z\n010111011 000000 # B->N/Z\n010111100 000000 # B->N/Z\n010111101 000000 # B->N/Z\n010111110 000000 # B->N/Z\n010111111 000000 # B->N/Z\n011000000 011010 # CMP\n011000001 011010 # CMP\n011000010 011010 # CMP\n011000011 100000 # DEC W\n011000100 011010 # CMP\n011000101 011010 # CMP\n011000110 011111 # DEC\n011000111 010100 # SMB\n011001000 011101 # INC\n011001001 011010 # CMP\n011001010 011111 # DEC\n011001011 100010 # ASL W\n011001100 011010 # CMP\n011001101 011010 # CMP\n011001110 011111 # DEC\n011001111 000000 # B->N/Z\n011010000 000000 # B->N/Z\n011010001 011010 # CMP\n011010010 011010 # CMP\n011010011 000000 # B->N/Z\n011010100 011010 # CMP\n011010101 011010 # CMP\n011010110 011111 # DEC\n011010111 010100 # SMB\n011011000 000100 # CLR D\n011011001 011010 # CMP\n011011010 000000 # B->N/Z\n011011011 000000 # B->N/Z\n011011100 011010 # CMP\n011011101 011010 # CMP\n011011110 011111 # DEC\n011011111 000000 # B->N/Z\n011100000 011010 # CMP\n011100001 010110 # SBC\n011100010 000000 # B->N/Z\n011100011 011110 # INC W\n011100100 011010 # CMP\n011100101 010110 # SBC\n011100110 011101 # INC\n011100111 010100 # SMB\n011101000 011101 # INC\n011101001 010110 # SBC\n011101010 000000 # B->N/Z\n011101011 101000 # ROL W\n011101100 011010 # CMP\n011101101 010110 # SBC\n011101110 011101 # INC\n011101111 000000 # B->N/Z\n011110000 000000 # B->N/Z\n011110001 010110 # SBC\n011110010 010110 # SBC\n011110011 000000 # B->N/Z\n011110100 000000 # B->N/Z\n011110101 010110 # SBC\n011110110 011101 # INC\n011110111 010100 # SMB\n011111000 001011 # SET D\n011111001 010110 # SBC\n011111010 000000 # B->N/Z\n011111011 000000 # B->N/Z\n011111100 000000 # B->N/Z\n011111101 010110 # SBC\n011111110 011101 # INC\n011111111 000000 # B->N/Z\n100000000 000000 # B->N/Z\n100000001 000000 # B->N/Z\n100000010 000000 # B->N/Z\n100000011 000000 # B->N/Z\n100000100 000000 # B->N/Z\n100000101 101011 # MUL\n100000110 000000 # B->N/Z\n100000111 000000 # B->N/Z\n100001000 000000 # B->N/Z\n100001001 101011 # MUL\n100001010 000000 # B->N/Z\n100001011 000000 # B->N/Z\n100001100 000000 # B->N/Z\n100001101 101011 # MUL\n100001110 000000 # B->N/Z\n100001111 000000 # B->N/Z\n100010000 000000 # B->N/Z\n100010001 000000 # B->N/Z\n100010010 000000 # B->N/Z\n100010011 000000 # B->N/Z\n100010100 000000 # B->N/Z\n100010101 101011 # MUL\n100010110 000000 # B->N/Z\n100010111 000000 # B->N/Z\n100011000 000000 # B->N/Z\n100011001 101011 # MUL\n100011010 000000 # B->N/Z\n100011011 000000 # B->N/Z\n100011100 000000 # B->N/Z\n100011101 101011 # MUL\n100011110 000000 # B->N/Z\n100011111 000000 # B->N/Z\n100100000 000000 # B->N/Z\n100100001 000000 # B->N/Z\n100100010 000000 # B->N/Z\n100100011 000000 # B->N/Z\n100100100 000000 # B->N/Z\n100100101 101100 # MLH\n100100110 000000 # B->N/Z\n100100111 000000 # B->N/Z\n100101000 000000 # B->N/Z\n100101001 101100 # MLH\n100101010 000000 # B->N/Z\n100101011 000000 # B->N/Z\n100101100 000000 # B->N/Z\n100101101 101100 # MLH\n100101110 000000 # B->N/Z\n100101111 000000 # B->N/Z\n100110000 000000 # B->N/Z\n100110001 000000 # B->N/Z\n100110010 000000 # B->N/Z\n100110011 000000 # B->N/Z\n100110100 000000 # B->N/Z\n100110101 101100 # MLH\n100110110 000000 # B->N/Z\n100110111 000000 # B->N/Z\n100111000 000000 # B->N/Z\n100111001 101100 # MLH\n100111010 000000 # B->N/Z\n100111011 000000 # B->N/Z\n100111100 000000 # B->N/Z\n100111101 101100 # MLH\n100111110 000000 # B->N/Z\n100111111 000000 # B->N/Z\n101000000 000000 # B->N/Z\n101000001 000000 # B->N/Z\n101000010 000000 # B->N/Z\n101000011 000000 # B->N/Z\n101000100 000000 # B->N/Z\n101000101 101101 # MOD\n101000110 000000 # B->N/Z\n101000111 000000 # B->N/Z\n101001000 000000 # B->N/Z\n101001001 101101 # MOD\n101001010 000000 # B->N/Z\n101001011 000000 # B->N/Z\n101001100 000000 # B->N/Z\n101001101 101101 # MOD\n101001110 000000 # B->N/Z\n101001111 000000 # B->N/Z\n101010000 000000 # B->N/Z\n101010001 000000 # B->N/Z\n101010010 000000 # B->N/Z\n101010011 000000 # B->N/Z\n101010100 000000 # B->N/Z\n101010101 101101 # MOD\n101010110 000000 # B->N/Z\n101010111 000000 # B->N/Z\n101011000 000000 # B->N/Z\n101011001 101101 # MOD\n101011010 000000 # B->N/Z\n101011011 000000 # B->N/Z\n101011100 000000 # B->N/Z\n101011101 101101 # MOD\n101011110 000000 # B->N/Z\n101011111 000000 # B->N/Z\n101100000 000000 # B->N/Z\n101100001 000000 # B->N/Z\n101100010 000000 # B->N/Z\n101100011 000000 # B->N/Z\n101100100 000000 # B->N/Z\n101100101 101110 # DIV\n101100110 000000 # B->N/Z\n101100111 000000 # B->N/Z\n101101000 000000 # B->N/Z\n101101001 101110 # DIV\n101101010 000000 # B->N/Z\n101101011 000000 # B->N/Z\n101101100 000000 # B->N/Z\n101101101 101110 # DIV\n101101110 000000 # B->N/Z\n101101111 000000 # B->N/Z\n101110000 000000 # B->N/Z\n101110001 000000 # B->N/Z\n101110010 000000 # B->N/Z\n101110011 000000 # B->N/Z\n101110100 000000 # B->N/Z\n101110101 101110 # DIV\n101110110 000000 # B->N/Z\n101110111 000000 # B->N/Z\n101111000 000000 # B->N/Z\n101111001 101110 # DIV\n101111010 000000 # B->N/Z\n101111011 000000 # B->N/Z\n101111100 000000 # B->N/Z\n101111101 101110 # DIV\n101111110 000000 # B->N/Z\n101111111 000000 # B->N/Z\n110000000 000000 # B->N/Z\n110000001 000000 # B->N/Z\n110000010 000000 # B->N/Z\n110000011 000000 # B->N/Z\n110000100 000000 # B->N/Z\n110000101 000000 # B->N/Z\n110000110 000000 # B->N/Z\n110000111 000000 # B->N/Z\n110001000 000000 # B->N/Z\n110001001 000000 # B->N/Z\n110001010 000000 # B->N/Z\n110001011 000000 # B->N/Z\n110001100 000000 # B->N/Z\n110001101 000000 # B->N/Z\n110001110 000000 # B->N/Z\n110001111 000000 # B->N/Z\n110010000 000000 # B->N/Z\n110010001 000000 # B->N/Z\n110010010 000000 # B->N/Z\n110010011 000000 # B->N/Z\n110010100 000000 # B->N/Z\n110010101 000000 # B->N/Z\n110010110 000000 # B->N/Z\n110010111 000000 # B->N/Z\n110011000 000000 # B->N/Z\n110011001 000000 # B->N/Z\n110011010 000000 # B->N/Z\n110011011 000000 # B->N/Z\n110011100 000000 # B->N/Z\n110011101 000000 # B->N/Z\n110011110 000000 # B->N/Z\n110011111 000000 # B->N/Z\n110100000 000000 # B->N/Z\n110100001 000000 # B->N/Z\n110100010 000000 # B->N/Z\n110100011 000000 # B->N/Z\n110100100 000000 # B->N/Z\n110100101 000000 # B->N/Z\n110100110 000000 # B->N/Z\n110100111 000000 # B->N/Z\n110101000 000000 # B->N/Z\n110101001 000000 # B->N/Z\n110101010 000000 # B->N/Z\n110101011 000000 # B->N/Z\n110101100 000000 # B->N/Z\n110101101 000000 # B->N/Z\n110101110 000000 # B->N/Z\n110101111 000000 # B->N/Z\n110110000 000000 # B->N/Z\n110110001 000000 # B->N/Z\n110110010 000000 # B->N/Z\n110110011 000000 # B->N/Z\n110110100 000000 # B->N/Z\n110110101 000000 # B->N/Z\n110110110 000000 # B->N/Z\n110110111 000000 # B->N/Z\n110111000 000000 # B->N/Z\n110111001 000000 # B->N/Z\n110111010 000000 # B->N/Z\n110111011 000000 # B->N/Z\n110111100 000000 # B->N/Z\n110111101 000000 # B->N/Z\n110111110 000000 # B->N/Z\n110111111 000000 # B->N/Z\n111000000 000000 # B->N/Z\n111000001 000000 # B->N/Z\n111000010 000000 # B->N/Z\n111000011 000000 # B->N/Z\n111000100 000000 # B->N/Z\n111000101 000000 # B->N/Z\n111000110 011100 # DCC\n111000111 000000 # B->N/Z\n111001000 101111 # CBH\n111001001 000000 # B->N/Z\n111001010 100110 # LSR W\n111001011 100100 # ASR W\n111001100 000000 # B->N/Z\n111001101 000000 # B->N/Z\n111001110 011100 # DCC\n111001111 000000 # B->N/Z\n111010000 000000 # B->N/Z\n111010001 000000 # B->N/Z\n111010010 000000 # B->N/Z\n111010011 000000 # B->N/Z\n111010100 000000 # B->N/Z\n111010101 000000 # B->N/Z\n111010110 011100 # DCC\n111010111 000000 # B->N/Z\n111011000 000000 # B->N/Z\n111011001 000000 # B->N/Z\n111011010 000000 # B->N/Z\n111011011 000000 # B->N/Z\n111011100 000000 # B->N/Z\n111011101 000000 # B->N/Z\n111011110 011100 # DCC\n111011111 000000 # B->N/Z\n111100000 000000 # B->N/Z\n111100001 000000 # B->N/Z\n111100010 000000 # B->N/Z\n111100011 000000 # B->N/Z\n111100100 000000 # B->N/Z\n111100101 000000 # B->N/Z\n111100110 011011 # ICC\n111100111 000000 # B->N/Z\n111101000 110000 # CHB\n111101001 000000 # B->N/Z\n111101010 000000 # B->N/Z\n111101011 101010 # ROR W\n111101100 000000 # B->N/Z\n111101101 000000 # B->N/Z\n111101110 011011 # ICC\n111101111 000000 # B->N/Z\n111110000 000000 # B->N/Z\n111110001 000000 # B->N/Z\n111110010 000000 # B->N/Z\n111110011 000000 # B->N/Z\n111110100 000000 # B->N/Z\n111110101 000000 # B->N/Z\n111110110 011011 # ICC\n111110111 000000 # B->N/Z\n111111000 000000 # B->N/Z\n111111001 000000 # B->N/Z\n111111010 000000 # B->N/Z\n111111011 000000 # B->N/Z\n111111100 000000 # B->N/Z\n111111101 000000 # B->N/Z\n111111110 011011 # ICC\n111111111 000000 # B->N/Z")) ALU0 (
    .in(AA), .out(ALU0_out));
  PLA #(.in_width(6), .out_width(17), .\table ("000000 10000100000000001 # B->N/Z\n000001 00000011000000000 # CLR C\n000010 00000101000000000 # CLR Z\n000011 00001001000000001 # CLR I\n000100 00010001000000000 # CLR D\n000101 00100001000000001 # CLR E\n000110 01000001000000000 # CLR V\n000111 10000001000000000 # CLR N\n001000 00000011000000001 # SET C\n001001 00000101000000001 # SET Z\n001010 00001001000000000 # SET I\n001011 00010001000000001 # SET D\n001100 00100001000000000 # SET E\n001101 01000001000000001 # SET V\n001110 10000001000000001 # SET N\n001111 11011110000000000 # WR FL\n010000 11000100000000001 # BIT\n010001 00000100001000000 # TRB\n010010 00000100001100000 # TSB\n010011 00000000001000010 # RMB\n010100 00000000001100010 # SMB\n010101 10000110000001000 # ADC\n010110 10000110000001100 # SBC\n010111 10000100000100000 # AND\n011000 10000100001100000 # OR\n011001 10000100010000000 # XOR\n011010 10000110000000100 # CMP\n011011 10000110000001010 # ICC\n011100 10000110000001110 # DCC\n011101 10000100000000010 # INC\n011110 10000100000010010 # INC W\n011111 10000100000000110 # DEC\n100000 10000100000010110 # DEC W\n100001 10000110010100000 # ASL\n100010 10000110010100100 # ASL W\n100011 10000110011000000 # ASR\n100100 10000110011000100 # ASR W\n100101 10000110011100000 # LSR\n100110 10000110011100100 # LSR W\n100111 10000110100000000 # ROL\n101000 10000110100000100 # ROL W\n101001 10000110100100000 # ROR\n101010 10000110100100100 # ROR W\n101011 10000110101000000 # MUL\n101100 10000110101100000 # MLH\n101101 10000110110100000 # MOD\n101110 10000110110000000 # DIV\n101111 10000110111100000 # CBH\n110000 10000110111000000 # CHB")) ALU1 (
    .in(AA[5:0]), .out(ALU1_out));
  PLA #(.in_width(8), .out_width(1), .\table ("00000100 1 # TSB bp\n00001100 1 # TSB a\n00010100 1 # TRB bp\n00011100 1 # TRB a\n00000111 1 # RMB0 bp\n00010111 1 # RMB1 bp\n00100111 1 # RMB2 bp\n00110111 1 # RMB3 bp\n01000111 1 # RMB4 bp\n01010111 1 # RMB5 bp\n01100111 1 # RMB6 bp\n01110111 1 # RMB7 bp\n10000111 1 # SMB0 bp\n10010111 1 # SMB1 bp\n10100111 1 # SMB2 bp\n10110111 1 # SMB3 bp\n11000111 1 # SMB4 bp\n11010111 1 # SMB5 bp\n11100111 1 # SMB6 bp\n11110111 1 # SMB7 bp")) AZS_2 (
    .in(AA8), .out(AZS_2_out));
  PLA #(.in_width(8), .out_width(9), .\table ("00000000 000000000 # 00\n00000001 000000001 # 01\n00000010 000000010 # 02\n00000011 000000011 # 03\n00000100 000000100 # 04\n00000101 000000101 # 05\n00000110 000000110 # 06\n00000111 000000111 # 07\n00001000 000001000 # 08\n00001001 000001001 # 09\n00001010 000010000 # 10\n00001011 000010001 # 11\n00001100 000010010 # 12\n00001101 000010011 # 13\n00001110 000010100 # 14\n00001111 000010101 # 15\n00010000 000010110 # 16\n00010001 000010111 # 17\n00010010 000011000 # 18\n00010011 000011001 # 19\n00010100 000100000 # 20\n00010101 000100001 # 21\n00010110 000100010 # 22\n00010111 000100011 # 23\n00011000 000100100 # 24\n00011001 000100101 # 25\n00011010 000100110 # 26\n00011011 000100111 # 27\n00011100 000101000 # 28\n00011101 000101001 # 29\n00011110 000110000 # 30\n00011111 000110001 # 31\n00100000 000110010 # 32\n00100001 000110011 # 33\n00100010 000110100 # 34\n00100011 000110101 # 35\n00100100 000110110 # 36\n00100101 000110111 # 37\n00100110 000111000 # 38\n00100111 000111001 # 39\n00101000 001000000 # 40\n00101001 001000001 # 41\n00101010 001000010 # 42\n00101011 001000011 # 43\n00101100 001000100 # 44\n00101101 001000101 # 45\n00101110 001000110 # 46\n00101111 001000111 # 47\n00110000 001001000 # 48\n00110001 001001001 # 49\n00110010 001010000 # 50\n00110011 001010001 # 51\n00110100 001010010 # 52\n00110101 001010011 # 53\n00110110 001010100 # 54\n00110111 001010101 # 55\n00111000 001010110 # 56\n00111001 001010111 # 57\n00111010 001011000 # 58\n00111011 001011001 # 59\n00111100 001100000 # 60\n00111101 001100001 # 61\n00111110 001100010 # 62\n00111111 001100011 # 63\n01000000 001100100 # 64\n01000001 001100101 # 65\n01000010 001100110 # 66\n01000011 001100111 # 67\n01000100 001101000 # 68\n01000101 001101001 # 69\n01000110 001110000 # 70\n01000111 001110001 # 71\n01001000 001110010 # 72\n01001001 001110011 # 73\n01001010 001110100 # 74\n01001011 001110101 # 75\n01001100 001110110 # 76\n01001101 001110111 # 77\n01001110 001111000 # 78\n01001111 001111001 # 79\n01010000 010000000 # 80\n01010001 010000001 # 81\n01010010 010000010 # 82\n01010011 010000011 # 83\n01010100 010000100 # 84\n01010101 010000101 # 85\n01010110 010000110 # 86\n01010111 010000111 # 87\n01011000 010001000 # 88\n01011001 010001001 # 89\n01011010 010010000 # 90\n01011011 010010001 # 91\n01011100 010010010 # 92\n01011101 010010011 # 93\n01011110 010010100 # 94\n01011111 010010101 # 95\n01100000 010010110 # 96\n01100001 010010111 # 97\n01100010 010011000 # 98\n01100011 010011001 # 99\n01100100 100000000 # >99\n01100101 100000000 # >99\n01100110 100000000 # >99\n01100111 100000000 # >99\n01101000 100000000 # >99\n01101001 100000000 # >99\n01101010 100000000 # >99\n01101011 100000000 # >99\n01101100 100000000 # >99\n01101101 100000000 # >99\n01101110 100000000 # >99\n01101111 100000000 # >99\n01110000 100000000 # >99\n01110001 100000000 # >99\n01110010 100000000 # >99\n01110011 100000000 # >99\n01110100 100000000 # >99\n01110101 100000000 # >99\n01110110 100000000 # >99\n01110111 100000000 # >99\n01111000 100000000 # >99\n01111001 100000000 # >99\n01111010 100000000 # >99\n01111011 100000000 # >99\n01111100 100000000 # >99\n01111101 100000000 # >99\n01111110 100000000 # >99\n01111111 100000000 # >99\n10000000 100000000 # >99\n10000001 100000000 # >99\n10000010 100000000 # >99\n10000011 100000000 # >99\n10000100 100000000 # >99\n10000101 100000000 # >99\n10000110 100000000 # >99\n10000111 100000000 # >99\n10001000 100000000 # >99\n10001001 100000000 # >99\n10001010 100000000 # >99\n10001011 100000000 # >99\n10001100 100000000 # >99\n10001101 100000000 # >99\n10001110 100000000 # >99\n10001111 100000000 # >99\n10010000 100000000 # >99\n10010001 100000000 # >99\n10010010 100000000 # >99\n10010011 100000000 # >99\n10010100 100000000 # >99\n10010101 100000000 # >99\n10010110 100000000 # >99\n10010111 100000000 # >99\n10011000 100000000 # >99\n10011001 100000000 # >99\n10011010 100000000 # >99\n10011011 100000000 # >99\n10011100 100000000 # >99\n10011101 100000000 # >99\n10011110 100000000 # >99\n10011111 100000000 # >99\n10100000 100000000 # >99\n10100001 100000000 # >99\n10100010 100000000 # >99\n10100011 100000000 # >99\n10100100 100000000 # >99\n10100101 100000000 # >99\n10100110 100000000 # >99\n10100111 100000000 # >99\n10101000 100000000 # >99\n10101001 100000000 # >99\n10101010 100000000 # >99\n10101011 100000000 # >99\n10101100 100000000 # >99\n10101101 100000000 # >99\n10101110 100000000 # >99\n10101111 100000000 # >99\n10110000 100000000 # >99\n10110001 100000000 # >99\n10110010 100000000 # >99\n10110011 100000000 # >99\n10110100 100000000 # >99\n10110101 100000000 # >99\n10110110 100000000 # >99\n10110111 100000000 # >99\n10111000 100000000 # >99\n10111001 100000000 # >99\n10111010 100000000 # >99\n10111011 100000000 # >99\n10111100 100000000 # >99\n10111101 100000000 # >99\n10111110 100000000 # >99\n10111111 100000000 # >99\n11000000 100000000 # >99\n11000001 100000000 # >99\n11000010 100000000 # >99\n11000011 100000000 # >99\n11000100 100000000 # >99\n11000101 100000000 # >99\n11000110 100000000 # >99\n11000111 100000000 # >99\n11001000 100000000 # >99\n11001001 100000000 # >99\n11001010 100000000 # >99\n11001011 100000000 # >99\n11001100 100000000 # >99\n11001101 100000000 # >99\n11001110 100000000 # >99\n11001111 100000000 # >99\n11010000 100000000 # >99\n11010001 100000000 # >99\n11010010 100000000 # >99\n11010011 100000000 # >99\n11010100 100000000 # >99\n11010101 100000000 # >99\n11010110 100000000 # >99\n11010111 100000000 # >99\n11011000 100000000 # >99\n11011001 100000000 # >99\n11011010 100000000 # >99\n11011011 100000000 # >99\n11011100 100000000 # >99\n11011101 100000000 # >99\n11011110 100000000 # >99\n11011111 100000000 # >99\n11100000 100000000 # >99\n11100001 100000000 # >99\n11100010 100000000 # >99\n11100011 100000000 # >99\n11100100 100000000 # >99\n11100101 100000000 # >99\n11100110 100000000 # >99\n11100111 100000000 # >99\n11101000 100000000 # >99\n11101001 100000000 # >99\n11101010 100000000 # >99\n11101011 100000000 # >99\n11101100 100000000 # >99\n11101101 100000000 # >99\n11101110 100000000 # >99\n11101111 100000000 # >99\n11110000 100000000 # >99\n11110001 100000000 # >99\n11110010 100000000 # >99\n11110011 100000000 # >99\n11110100 100000000 # >99\n11110101 100000000 # >99\n11110110 100000000 # >99\n11110111 100000000 # >99\n11111000 100000000 # >99\n11111001 100000000 # >99\n11111010 100000000 # >99\n11111011 100000000 # >99\n11111100 100000000 # >99\n11111101 100000000 # >99\n11111110 100000000 # >99\n11111111 100000000 # >99")) CHB_2 (
    .in(AA8), .out(CHB_2_out));
  PLA #(.in_width(8), .out_width(9), .\table ("00000000 000000000 # 00\n00000001 000000001 # 01\n00000010 000000010 # 02\n00000011 000000011 # 03\n00000100 000000100 # 04\n00000101 000000101 # 05\n00000110 000000110 # 06\n00000111 000000111 # 07\n00001000 000001000 # 08\n00001001 000001001 # 09\n00001010 100000000 # XX\n00001011 100000000 # XX\n00001100 100000000 # XX\n00001101 100000000 # XX\n00001110 100000000 # XX\n00001111 100000000 # XX\n00010000 000001010 # 10\n00010001 000001011 # 11\n00010010 000001100 # 12\n00010011 000001101 # 13\n00010100 000001110 # 14\n00010101 000001111 # 15\n00010110 000010000 # 16\n00010111 000010001 # 17\n00011000 000010010 # 18\n00011001 000010011 # 19\n00011010 100000000 # XX\n00011011 100000000 # XX\n00011100 100000000 # XX\n00011101 100000000 # XX\n00011110 100000000 # XX\n00011111 100000000 # XX\n00100000 000010100 # 20\n00100001 000010101 # 21\n00100010 000010110 # 22\n00100011 000010111 # 23\n00100100 000011000 # 24\n00100101 000011001 # 25\n00100110 000011010 # 26\n00100111 000011011 # 27\n00101000 000011100 # 28\n00101001 000011101 # 29\n00101010 100000000 # XX\n00101011 100000000 # XX\n00101100 100000000 # XX\n00101101 100000000 # XX\n00101110 100000000 # XX\n00101111 100000000 # XX\n00110000 000011110 # 30\n00110001 000011111 # 31\n00110010 000100000 # 32\n00110011 000100001 # 33\n00110100 000100010 # 34\n00110101 000100011 # 35\n00110110 000100100 # 36\n00110111 000100101 # 37\n00111000 000100110 # 38\n00111001 000100111 # 39\n00111010 100000000 # XX\n00111011 100000000 # XX\n00111100 100000000 # XX\n00111101 100000000 # XX\n00111110 100000000 # XX\n00111111 100000000 # XX\n01000000 000101000 # 40\n01000001 000101001 # 41\n01000010 000101010 # 42\n01000011 000101011 # 43\n01000100 000101100 # 44\n01000101 000101101 # 45\n01000110 000101110 # 46\n01000111 000101111 # 47\n01001000 000110000 # 48\n01001001 000110001 # 49\n01001010 100000000 # XX\n01001011 100000000 # XX\n01001100 100000000 # XX\n01001101 100000000 # XX\n01001110 100000000 # XX\n01001111 100000000 # XX\n01010000 000110010 # 50\n01010001 000110011 # 51\n01010010 000110100 # 52\n01010011 000110101 # 53\n01010100 000110110 # 54\n01010101 000110111 # 55\n01010110 000111000 # 56\n01010111 000111001 # 57\n01011000 000111010 # 58\n01011001 000111011 # 59\n01011010 100000000 # XX\n01011011 100000000 # XX\n01011100 100000000 # XX\n01011101 100000000 # XX\n01011110 100000000 # XX\n01011111 100000000 # XX\n01100000 000111100 # 60\n01100001 000111101 # 61\n01100010 000111110 # 62\n01100011 000111111 # 63\n01100100 001000000 # 64\n01100101 001000001 # 65\n01100110 001000010 # 66\n01100111 001000011 # 67\n01101000 001000100 # 68\n01101001 001000101 # 69\n01101010 100000000 # XX\n01101011 100000000 # XX\n01101100 100000000 # XX\n01101101 100000000 # XX\n01101110 100000000 # XX\n01101111 100000000 # XX\n01110000 001000110 # 70\n01110001 001000111 # 71\n01110010 001001000 # 72\n01110011 001001001 # 73\n01110100 001001010 # 74\n01110101 001001011 # 75\n01110110 001001100 # 76\n01110111 001001101 # 77\n01111000 001001110 # 78\n01111001 001001111 # 79\n01111010 100000000 # XX\n01111011 100000000 # XX\n01111100 100000000 # XX\n01111101 100000000 # XX\n01111110 100000000 # XX\n01111111 100000000 # XX\n10000000 001010000 # 80\n10000001 001010001 # 81\n10000010 001010010 # 82\n10000011 001010011 # 83\n10000100 001010100 # 84\n10000101 001010101 # 85\n10000110 001010110 # 86\n10000111 001010111 # 87\n10001000 001011000 # 88\n10001001 001011001 # 89\n10001010 100000000 # XX\n10001011 100000000 # XX\n10001100 100000000 # XX\n10001101 100000000 # XX\n10001110 100000000 # XX\n10001111 100000000 # XX\n10010000 001011010 # 90\n10010001 001011011 # 91\n10010010 001011100 # 92\n10010011 001011101 # 93\n10010100 001011110 # 94\n10010101 001011111 # 95\n10010110 001100000 # 96\n10010111 001100001 # 97\n10011000 001100010 # 98\n10011001 001100011 # 99\n10011010 100000000 # XX\n10011011 100000000 # XX\n10011100 100000000 # XX\n10011101 100000000 # XX\n10011110 100000000 # XX\n10011111 100000000 # XX\n10100000 100000000 # XX\n10100001 100000000 # XX\n10100010 100000000 # XX\n10100011 100000000 # XX\n10100100 100000000 # XX\n10100101 100000000 # XX\n10100110 100000000 # XX\n10100111 100000000 # XX\n10101000 100000000 # XX\n10101001 100000000 # XX\n10101010 100000000 # XX\n10101011 100000000 # XX\n10101100 100000000 # XX\n10101101 100000000 # XX\n10101110 100000000 # XX\n10101111 100000000 # XX\n10110000 100000000 # XX\n10110001 100000000 # XX\n10110010 100000000 # XX\n10110011 100000000 # XX\n10110100 100000000 # XX\n10110101 100000000 # XX\n10110110 100000000 # XX\n10110111 100000000 # XX\n10111000 100000000 # XX\n10111001 100000000 # XX\n10111010 100000000 # XX\n10111011 100000000 # XX\n10111100 100000000 # XX\n10111101 100000000 # XX\n10111110 100000000 # XX\n10111111 100000000 # XX\n11000000 100000000 # XX\n11000001 100000000 # XX\n11000010 100000000 # XX\n11000011 100000000 # XX\n11000100 100000000 # XX\n11000101 100000000 # XX\n11000110 100000000 # XX\n11000111 100000000 # XX\n11001000 100000000 # XX\n11001001 100000000 # XX\n11001010 100000000 # XX\n11001011 100000000 # XX\n11001100 100000000 # XX\n11001101 100000000 # XX\n11001110 100000000 # XX\n11001111 100000000 # XX\n11010000 100000000 # XX\n11010001 100000000 # XX\n11010010 100000000 # XX\n11010011 100000000 # XX\n11010100 100000000 # XX\n11010101 100000000 # XX\n11010110 100000000 # XX\n11010111 100000000 # XX\n11011000 100000000 # XX\n11011001 100000000 # XX\n11011010 100000000 # XX\n11011011 100000000 # XX\n11011100 100000000 # XX\n11011101 100000000 # XX\n11011110 100000000 # XX\n11011111 100000000 # XX\n11100000 100000000 # XX\n11100001 100000000 # XX\n11100010 100000000 # XX\n11100011 100000000 # XX\n11100100 100000000 # XX\n11100101 100000000 # XX\n11100110 100000000 # XX\n11100111 100000000 # XX\n11101000 100000000 # XX\n11101001 100000000 # XX\n11101010 100000000 # XX\n11101011 100000000 # XX\n11101100 100000000 # XX\n11101101 100000000 # XX\n11101110 100000000 # XX\n11101111 100000000 # XX\n11110000 100000000 # XX\n11110001 100000000 # XX\n11110010 100000000 # XX\n11110011 100000000 # XX\n11110100 100000000 # XX\n11110101 100000000 # XX\n11110110 100000000 # XX\n11110111 100000000 # XX\n11111000 100000000 # XX\n11111001 100000000 # XX\n11111010 100000000 # XX\n11111011 100000000 # XX\n11111100 100000000 # XX\n11111101 100000000 # XX\n11111110 100000000 # XX\n11111111 100000000 # XX")) CBH_2 (
    .in(AA8), .out(CBH_2_out));
  Counter #(.max('hf), .trigger("falling"), .width(4)) counter_2 (
    .Q(counter_2_q), .clk(clock_2_out));  // open: load, D, count, carry, clr
  Clock clock_2 (.out(clock_2_out));
  RAM #(.addrWidth(9), .dataWidth(6)) ram_1 (.addr(AA), .we(1'b1), .clk(CC), .din(ALU0_out));  // open: dout
  RAM #(.addrWidth(6), .dataWidth(17)) ram_2 (.addr(AA[5:0]), .we(1'b1), .clk(CC), .din(ALU1_out));  // open: dout
  RAM #(.dataWidth(1)) ram_3 (.addr(AA8), .we(1'b1), .clk(CC), .din(AZS_2_out));  // open: dout
  RAM #(.dataWidth(9)) ram_4 (.addr(AA8), .we(1'b1), .clk(CC), .din(CHB_2_out));  // open: dout
  RAM #(.dataWidth(9)) ram_5 (.addr(AA8), .we(1'b1), .clk(CC), .din(CBH_2_out));  // open: dout
  RAM #(.addrWidth(4), .dataWidth(5)) ram_6 (
    .addr(counter_2_q), .we(clock_2_out), .clk(clock_2_out), .din(undriven));  // open: dout
  // Probe on nothing

  // Other names for the same wires on the sheet: B16[15:0] = B; B_t[7:0] = B[7:0]; D0 = B[0]; D1 = B[1]; D2 = B[2];
  //   D3 = B[3]; D4 = B[4]; D5 = B[5]; D6 = B[6]; D7 = B[7]; BH[7:0] = B[15:8]; E = A_CTRL[0];
  //   INST[8:0] = A_CTRL[9:1]; CO = FL[0]; ZO = FL[1]; nIO = FL[2]; DO = FL[3]; nEO = FL[4]; VO = FL[5]; NO = FL[6];
  //   Q16[15:0] = Q; QH[7:0] = Q[15:8]; SO = SOB

  // Notes on the sheet:
  //   B->N/Z
  //   INC
  //   DEC
  //   INC W
  //   DEC W
  //   ADC
  //   ICC
  //   SBC
  //   DCC
  //   AND
  //   OR
  //   XOR
  //   ASL
  //   ASR
  //   LSR
  //   ROL
  //   ROR
  //   ASL W
  //   ASR W
  //   LSR W
  //   ROL W
  //   ROR W
  //   MUL
  //   MLH
  //   MOD
  //   DIV
  //   HTB
  //   BTH
  //   CMP
  //   SET C
  //   SET D
  //   SET E
  //   SET I
  //   CLR C
  //   CLR D
  //   CLR E
  //   CLR I
  //   CLR V
  //   BIT
  //   WR FL
  //   SMB0
  //   SMB1
  //   SMB2
  //   SMB3
  //   SMB4
  //   SMB5
  //   SMB6
  //   SMB7
  //   RMB0
  //   RMB1
  //   RMB2
  //   RMB3
  //   RMB4
  //   RMB5
  //   RMB6
  //   RMB7
  //   TSB
  //   TRB
  //   TSB:
  //   Z = A & B
  //   Q = A | B
  //   TRB:
  //   Z = A & B
  //   Q = !A & B
  //   0000 ADD (C/D has no effect)
  //   0001 INC (C/D has no effect)
  //   0010 SUB (C/D has no effect)
  //   0011 DEC (C/D has no effect)
  //   0100 ADC
  //   0101 ICC
  //   0110 SBC
  //   0111 DCC
  //   1001 INC WORD
  //   1011 DEC WORD
  //   ASL (BYTE/WORD)
  //   ASR (BYTE/WORD)
  //   LSR (BYTE/WORD)
  //   ROL (BYTE/WORD)
  //   ROR (BYTE/WORD)
endmodule
module CU (
  input  R,
  input  C,
  input  [7:0] DI,
  input  [6:0] FL,
  input  IRQ,
  input  NMI,
  input  ABT,
  output [1:0] ANRI,
  output INT,
  output LDIR,
  output [9:0] A_CTRL,
  output [31:0] R_CTRL,
  output [3:0] SPO,
  output [2:0] M_CTRL,
  output [2:0] PCO
);

  wire ABT_qn, ABT_t, ACY0, and_1_out, and_2_out, and_3_out, and_4_out, and_5_out, and_6_out, and_7_out,
       and_8_out, and_9_out, and_11_out, and_12_out, and_14_out, and_16_out, and_17_out, and_19_out,
       and_20_out, and_21_out, CABT, CABT_q, CC, CIRQ_q, CLR_INT, CNMI_q, comparator_1_eq, COND, COND_E, CY0,
       END, INTQ, IRQ_t, NMI_t, nor_1_out, not_1_out, OP2C, or_1_out, or_2_out, or_3_out, or_4_out, or_5_out,
       or_6_out, or_7_out, or_8_out, or_9_out, or_10_out, or_11_out, or_13_out, or_14_out, or_15_out, RES,
       SKIP, WAIT;
  wire [1:0] priority_encoder_1_out;
  wire [2:0] adder_1_out, CY, negator_1_out, PCO_data;
  wire [3:0] CON_out, CON_S, multiplexer_2_out, multiplexer_3_out;
  wire [7:0] INST_data, IRQ_NMI_ABT_data, multiplexer_4_out, multiplexer_5_out, multiplexer_6_out, OPC_2_out,
       OPC_out, RES_data;
  wire [8:0] AA;
  wire [8:8] multiplexer_7_out;
  wire [11:0] multiplexer_8_out, ROM_12_data;
  wire [31:0] multiplexer_9_out, ROM_32_data;
  wire [31:29] multiplexer_10_out;

  and and_1 (and_1_out, RES, ~CLR_INT);  // AND_Gate
  and and_2 (and_2_out, ABT_t, ~CLR_INT);  // AND_Gate
  Comparator #(.mode("unsigned")) comparator_1 (.a(A_CTRL[8:1]), .b(8'h5c), .eq(comparator_1_eq));  // open: gt, lt
  and and_3 (and_3_out, NMI_t, ~CLR_INT);  // AND_Gate
  or or_1 (or_1_out, FL[2], and_3_out, and_2_out, and_1_out);
  or or_2 (or_2_out, and_3_out, and_2_out, and_1_out);
  or or_3 (or_3_out, and_2_out, and_1_out);
  D_Flip_Flop CPREF (.clk(C), .D(comparator_1_eq), .Q(OP2C), .reset(R));  // open: Qn, preset
  not not_1 (not_1_out, CLR_INT);
  and and_4 (and_4_out, IRQ, ~or_1_out);  // AND_Gate
  and and_5 (and_5_out, ~or_2_out, NMI);  // AND_Gate
  and and_6 (and_6_out, ~or_3_out, ABT);  // AND_Gate
  or or_4 (or_4_out, IRQ_t, NMI_t);
  or or_5 (or_5_out, OP2C, CLR_INT);
  J_K_Flip_Flop #(.trigger("falling")) CIRQ (
    .J(and_4_out), .clk(C), .K(not_1_out), .Q(CIRQ_q), .reset(R));  // open: Qn, preset
  J_K_Flip_Flop #(.trigger("falling")) CNMI (
    .J(and_5_out), .clk(C), .K(not_1_out), .Q(CNMI_q), .reset(R));  // open: Qn, preset
  J_K_Flip_Flop #(.trigger("falling")) u_CABT (
    .J(and_6_out), .clk(C), .K(not_1_out), .Q(CABT_q), .reset(R));  // open: Qn, preset
  or or_6 (or_6_out, CNMI_q, CIRQ_q);
  Multiplexer #(.select(4)) multiplexer_1 (
    .in0(1'b1), .in1(1'b0), .in2(1'b0), .in3(1'b0), .in4(FL[0]), .in5(FL[1]), .in6(FL[5]), .in7(FL[6]),
    .in8(DI[0]), .in9(DI[1]), .in10(DI[2]), .in11(DI[3]), .in12(DI[4]), .in13(DI[5]), .in14(DI[6]),
    .in15(DI[7]), .out(COND));  // open: sel, en
  and and_7 (and_7_out, ~or_5_out, END, CIRQ_q);  // AND_Gate
  and and_8 (and_8_out, ~or_5_out, END, CNMI_q);  // AND_Gate
  and and_9 (and_9_out, ~or_5_out, CABT_q);  // AND_Gate
  and and_10 (INTQ, or_6_out, ~or_4_out, ~OP2C);  // AND_Gate
  and and_11 (and_11_out, OP2C, or_7_out);
  or or_7 (or_7_out, ABT_t, END);
  and and_12 (and_12_out, END, A_CTRL[9]);
  and and_13 (WAIT, ~CON_S[3], ~CON_S[2], CON_S[1], CON_S[0]);  // AND_Gate
  and and_14 (and_14_out, ~WAIT, COND_E);  // AND_Gate
  Counter #(.max('h1ff), .ongoal("stay"), .trigger("falling"), .width(9)) counter_1 (
    .Q(AA), .clk(CC));  // open: load, D, count, carry, clr
  Clock clock_1 (.out(CC));
  J_K_Flip_Flop #(.trigger("falling")) u_IRQ (
    .J(and_7_out), .clk(C), .K(CLR_INT), .Q(IRQ_t), .reset(R));  // open: Qn, preset
  J_K_Flip_Flop #(.trigger("falling")) u_NMI (
    .J(and_8_out), .clk(C), .K(CLR_INT), .Q(NMI_t), .reset(R));  // open: Qn, preset
  J_K_Flip_Flop #(.trigger("falling")) u_ABT (
    .J(and_9_out), .clk(C), .K(CLR_INT), .Q(ABT_t), .Qn(ABT_qn), .reset(R));  // open: preset
  J_K_Flip_Flop #(.trigger("falling")) PREF (
    .J(and_11_out), .clk(C), .K(and_12_out), .Q(A_CTRL[9]), .reset(R));  // open: Qn, preset
  LED EXT (.in(A_CTRL[9]));
  PLA #(.in_width(9), .out_width(8), .\table ("000000000 00000000 # BRK #\n000000001 00011100 # ORA (bp,x)\n000000010 00000010 # CLE\n000000011 00000010 # SEE\n000000100 01010101 # TSB bp\n000000101 00010111 # ORA bp\n000000110 01010101 # SFL bp\n000000111 01010101 # RMB0 bp\n000001000 01011011 # PHP\n000001001 00010110 # ORA #\n000001010 01010100 # ASL A\n000001011 01111000 # TSY\n000001100 01010111 # TSB a\n000001101 00011001 # ORA a\n000001110 01010111 # ASL a\n000001111 00010011 # BBR0 bp,r\n000010000 00001111 # BPL/BNC r\n000010001 00011101 # ORA (bp),y\n000010010 00011110 # ORA (bp),z\n000010011 00010001 # BPL/BNC rr\n000010100 01010101 # TRB bp\n000010101 00011000 # ORA bp,x\n000010110 01010110 # SFL bp,x\n000010111 01010101 # RMB1 bp\n000011000 00000010 # CLC\n000011001 00011011 # ORA a,y\n000011010 01010100 # INA/INC A\n000011011 01101001 # INZ/INC Z\n000011100 01010111 # TRB a\n000011101 00011010 # ORA a,x\n000011110 01011000 # ASL a,x\n000011111 00010011 # BBR1 bp,r\n000100000 00000011 # JSR a\n000100001 00011100 # AND (bp,x)\n000100010 00000100 # JSR (a)\n000100011 00000101 # JSR (a,x)\n000100100 01000011 # BIT bp\n000100101 00010111 # AND bp\n000100110 01010101 # ROL bp\n000100111 01010101 # RMB2 bp\n000101000 01100010 # PLP\n000101001 00010110 # AND #\n000101010 01010100 # ROL A\n000101011 01110110 # TYS\n000101100 01000101 # BIT a\n000101101 00011001 # AND a\n000101110 01010111 # ROL a\n000101111 00010011 # BBR2 bp,r\n000110000 00010000 # BMI/BNS r\n000110001 00011101 # AND (bp),y\n000110010 00011110 # AND (bp),z\n000110011 00010010 # BMI/BNS rr\n000110100 01000100 # BIT bp,x\n000110101 00011000 # AND bp,x\n000110110 01010110 # ROL bp,x\n000110111 01010101 # RMB3 bp\n000111000 00000010 # SEC\n000111001 00011011 # AND a,y\n000111010 01010100 # DEC A\n000111011 01101100 # DEZ/DEC Z\n000111100 01000110 # BIT a,x\n000111101 00011010 # AND a,x\n000111110 01011000 # ROL a,x\n000111111 00010011 # BBR3 bp,r\n001000000 00000111 # RTI\n001000001 00011100 # XOR (bp,x)\n001000010 00010101 # NEG A\n001000011 01010100 # ASR A\n001000100 01010101 # ASR bp\n001000101 00010111 # XOR bp\n001000110 01010101 # SFR bp\n001000111 01010101 # RMB4 bp\n001001000 01011100 # PHA\n001001001 00010110 # XOR #\n001001010 01010100 # LSR A\n001001011 01110000 # TAZ\n001001100 00001010 # JMP a\n001001101 00011001 # XOR a\n001001110 01010111 # LSR a\n001001111 00010011 # BBR4 bp,r\n001010000 00001111 # BVC r\n001010001 00011101 # XOR (bp),y\n001010010 00011110 # XOR (bp),z\n001010011 00010001 # BVC rr\n001010100 01010110 # ASR bp,x\n001010101 00011000 # XOR bp,x\n001010110 01010110 # SFR bp,x\n001010111 01010101 # RMB5 bp\n001011000 00000010 # CLI\n001011001 00011011 # XOR a,y\n001011010 01011110 # PHY\n001011011 01101101 # TAB\n001011100 01111001 # EXTENDED\n001011101 00011010 # XOR a,x\n001011110 01011000 # LSR a,x\n001011111 00010011 # BBR5 bp,r\n001100000 00001000 # RTS\n001100001 00011100 # ADC (bp,x)\n001100010 00001001 # RTN #\n001100011 00000110 # BSR rr\n001100100 00110100 # STZ bp\n001100101 00010111 # ADC bp\n001100110 01010101 # ROR bp\n001100111 01010101 # RMB6 bp\n001101000 01100011 # PLA\n001101001 00010110 # ADC #\n001101010 01010100 # ROR A\n001101011 01110100 # TZA\n001101100 00001011 # JMP (a)\n001101101 00011001 # ADC a\n001101110 01010111 # ROR a\n001101111 00010011 # BBR6 bp,r\n001110000 00010000 # BVS r\n001110001 00011101 # ADC (bp),y\n001110010 00011110 # ADC (bp),z\n001110011 00010010 # BVS rr\n001110100 00111000 # STZ bp,x\n001110101 00011000 # ADC bp,x\n001110110 01010110 # ROR bp,x\n001110111 01010101 # RMB7 bp\n001111000 00000010 # SEI\n001111001 00011011 # ADC a,y\n001111010 01100101 # PLY\n001111011 01110001 # TBA\n001111100 00001100 # JMP (a,x)\n001111101 00011010 # ADC a,x\n001111110 01011000 # ROR a,x\n001111111 00010011 # BBR7 bp,r\n010000000 00001101 # BRA r\n010000001 00101110 # STA (bp,x)\n010000010 00101101 # STA (d,sp),y\n010000011 00001110 # BRA rr\n010000100 00110011 # STY bp\n010000101 00110001 # STA bp\n010000110 00110010 # STX bp\n010000111 01010101 # SMB0 bp\n010001000 01101011 # DEY/DEC Y\n010001001 01000010 # BIT #\n010001010 01110010 # TXA\n010001011 00111110 # STY a,x\n010001100 00111011 # STY a\n010001101 00111001 # STA a\n010001110 00111010 # STX a\n010001111 00010100 # BBS0 bp,r\n010010000 00001111 # BCC r\n010010001 00101111 # STA (bp),y\n010010010 00110000 # STA (bp),z\n010010011 00010001 # BCC rr\n010010100 00110111 # STY bp,x\n010010101 00110101 # STA bp,x\n010010110 00110110 # STX bp,y\n010010111 01010101 # SMB1 bp\n010011000 01110011 # TYA\n010011001 01000000 # STA a,y\n010011010 01110101 # TXS\n010011011 01000001 # STX a,y\n010011100 00111100 # STZ a\n010011101 00111101 # STA a,x\n010011110 00111111 # STZ a,x\n010011111 00010100 # BBS1 bp,r\n010100000 00100001 # LDY #\n010100001 00011100 # LDA (bp,x)\n010100010 00100000 # LDX #\n010100011 00100010 # LDZ #\n010100100 00100100 # LDY bp\n010100101 00010111 # LDA bp\n010100110 00100011 # LDX bp\n010100111 01010101 # SMB2 bp\n010101000 01101111 # TAY\n010101001 00010110 # LDA #\n010101010 01101110 # TAX\n010101011 00101001 # LDZ a\n010101100 00101000 # LDY a\n010101101 00011001 # LDA a\n010101110 00100111 # LDX a\n010101111 00010100 # BBS2 bp,r\n010110000 00010000 # BCS r\n010110001 00011101 # LDA (bp),y\n010110010 00011110 # LDA (bp),z\n010110011 00010010 # BCS rr\n010110100 00100110 # LDY bp,x\n010110101 00011000 # LDA bp,x\n010110110 00100101 # LDX bp,y\n010110111 01010101 # SMB3 bp\n010111000 00000010 # CLV\n010111001 00011011 # LDA a,y\n010111010 01110111 # TSX\n010111011 00101100 # LDZ a,x\n010111100 00101011 # LDY a,x\n010111101 00011010 # LDA a,x\n010111110 00101010 # LDX a,y\n010111111 00010100 # BBS3 bp,r\n011000000 01001100 # CPY #\n011000001 01001000 # CMP (bp,x)\n011000010 01001101 # CPZ #\n011000011 01011001 # DEW bp\n011000100 01001111 # CPY bp\n011000101 01000011 # CMP bp\n011000110 01010101 # DEC bp\n011000111 01010101 # SMB4 bp\n011001000 01101000 # INY/INC Y\n011001001 01000010 # CMP #\n011001010 01101010 # DEX/DEC X\n011001011 01011010 # ASW/ALW a\n011001100 01010010 # CPY a\n011001101 01000101 # CMP a\n011001110 01010111 # DEC a\n011001111 00010100 # BBS4 bp,r\n011010000 00001111 # BNE/BZC r\n011010001 01001001 # CMP (bp),y\n011010010 01001010 # CMP (bp),z\n011010011 00010001 # BNE/BZC rr\n011010100 01010000 # CPZ bp\n011010101 01000100 # CMP bp,x\n011010110 01010110 # DEC bp,x\n011010111 01010101 # SMB5 bp\n011011000 00000010 # CLD\n011011001 01000111 # CMP a,y\n011011010 01011101 # PHX\n011011011 01011111 # PHZ\n011011100 01010011 # CPZ a\n011011101 01000110 # CMP a,x\n011011110 01011000 # DEC a,x\n011011111 00010100 # BBS5 bp,r\n011100000 01001011 # CPX #\n011100001 00011100 # SBC (bp,x)\n011100010 00011111 # LDA (d,sp),y\n011100011 01011001 # INW bp\n011100100 01001110 # CPX bp\n011100101 00010111 # SBC bp\n011100110 01010101 # INC bp\n011100111 01010101 # SMB6 bp\n011101000 01100111 # INX/INC X\n011101001 00010110 # SBC #\n011101010 00000001 # NOP\n011101011 01011010 # ROW/RLW a\n011101100 01010001 # CPX a\n011101101 00011001 # SBC a\n011101110 01010111 # INC a\n011101111 00010100 # BBS6 bp,r\n011110000 00010000 # BEQ/BZS r\n011110001 00011101 # SBC (bp),y\n011110010 00011110 # SBC (bp),z\n011110011 00010010 # BEQ/BZS rr\n011110100 01100000 # PHW ##\n011110101 00011000 # SBC bp,x\n011110110 01010110 # INC bp,x\n011110111 01010101 # SMB7 bp\n011111000 00000010 # SED\n011111001 00011011 # SBC a,y\n011111010 01100100 # PLX\n011111011 01100110 # PLZ\n011111100 01100001 # PHW a\n011111101 00011010 # SBC a,x\n011111110 01011000 # INC a,x\n011111111 00010100 # BBS7 bp,r\n100000000 00000000 # <INV>\n100000001 00000000 # <INV>\n100000010 00000000 # <INV>\n100000011 00000000 # <INV>\n100000100 00000000 # <INV>\n100000101 00010111 # MUL bp\n100000110 00000000 # <INV>\n100000111 00000000 # <INV>\n100001000 00000000 # <INV>\n100001001 00010110 # MUL #\n100001010 00000000 # <INV>\n100001011 00000000 # <INV>\n100001100 00000000 # <INV>\n100001101 00011001 # MUL a\n100001110 00000000 # <INV>\n100001111 00000000 # <INV>\n100010000 00000000 # <INV>\n100010001 00000000 # <INV>\n100010010 00000000 # <INV>\n100010011 00000000 # <INV>\n100010100 00000000 # <INV>\n100010101 00011000 # MUL bp,x\n100010110 00000000 # <INV>\n100010111 00000000 # <INV>\n100011000 00000000 # <INV>\n100011001 00011011 # MUL a,y\n100011010 00000000 # <INV>\n100011011 00000000 # <INV>\n100011100 00000000 # <INV>\n100011101 00011010 # MUL a,x\n100011110 00000000 # <INV>\n100011111 00000000 # <INV>\n100100000 00000000 # <INV>\n100100001 00000000 # <INV>\n100100010 00000000 # <INV>\n100100011 00000000 # <INV>\n100100100 00000000 # <INV>\n100100101 00010111 # MLH bp\n100100110 00000000 # <INV>\n100100111 00000000 # <INV>\n100101000 00000000 # <INV>\n100101001 00010110 # MLH #\n100101010 00000000 # <INV>\n100101011 00000000 # <INV>\n100101100 00000000 # <INV>\n100101101 00011001 # MLH a\n100101110 00000000 # <INV>\n100101111 00000000 # <INV>\n100110000 00000000 # <INV>\n100110001 00000000 # <INV>\n100110010 00000000 # <INV>\n100110011 00000000 # <INV>\n100110100 00000000 # <INV>\n100110101 00011000 # MLH bp,x\n100110110 00000000 # <INV>\n100110111 00000000 # <INV>\n100111000 00000000 # <INV>\n100111001 00011011 # MLH a,y\n100111010 00000000 # <INV>\n100111011 01111010 # RND\n100111100 00000000 # <INV>\n100111101 00011010 # MLH a,x\n100111110 00000000 # <INV>\n100111111 00000000 # <INV>\n101000000 00000000 # <INV>\n101000001 00000000 # <INV>\n101000010 00000000 # <INV>\n101000011 00000000 # <INV>\n101000100 00000000 # <INV>\n101000101 00010111 # MOD bp\n101000110 00000000 # <INV>\n101000111 00000000 # <INV>\n101001000 10000001 # PHR\n101001001 00010110 # MOD #\n101001010 00000000 # <INV>\n101001011 01111011 # SWN\n101001100 00000000 # <INV>\n101001101 00011001 # MOD a\n101001110 00000000 # <INV>\n101001111 00000000 # <INV>\n101010000 00000000 # <INV>\n101010001 00000000 # <INV>\n101010010 00000000 # <INV>\n101010011 00000000 # <INV>\n101010100 00000000 # <INV>\n101010101 00011000 # MOD bp,x\n101010110 00000000 # <INV>\n101010111 00000000 # <INV>\n101011000 00000000 # <INV>\n101011001 00011011 # MOD a,y\n101011010 00000000 # <INV>\n101011011 01111100 # SXY\n101011100 00000000 # <INV>\n101011101 00011010 # MOD a,x\n101011110 00000000 # <INV>\n101011111 00000000 # <INV>\n101100000 00000000 # <INV>\n101100001 00000000 # <INV>\n101100010 00000000 # <INV>\n101100011 00000000 # <INV>\n101100100 00000000 # <INV>\n101100101 00010111 # DIV bp\n101100110 00000000 # <INV>\n101100111 00000000 # <INV>\n101101000 10000010 # PLR\n101101001 00010110 # DIV #\n101101010 00000000 # <INV>\n101101011 01111101 # SXZ\n101101100 00000000 # <INV>\n101101101 00011001 # DIV a\n101101110 00000000 # <INV>\n101101111 00000000 # <INV>\n101110000 00000000 # <INV>\n101110001 00000000 # <INV>\n101110010 00000000 # <INV>\n101110011 00000000 # <INV>\n101110100 00000000 # <INV>\n101110101 00011000 # DIV bp,x\n101110110 00000000 # <INV>\n101110111 00000000 # <INV>\n101111000 00000000 # <INV>\n101111001 00011011 # DIV a,y\n101111010 00000000 # <INV>\n101111011 01111110 # SYZ\n101111100 00000000 # <INV>\n101111101 00011010 # DIV a,x\n101111110 00000000 # <INV>\n101111111 00000000 # <INV>\n110000000 00000000 # <INV>\n110000001 10000101 # STA (bp,x),y\n110000010 10000000 # STA sp,y\n110000011 00000000 # <INV>\n110000100 00000000 # <INV>\n110000101 00000000 # <INV>\n110000110 00000000 # <INV>\n110000111 00000000 # <INV>\n110001000 00000000 # <INV>\n110001001 00000000 # <INV>\n110001010 00000000 # <INV>\n110001011 00000000 # <INV>\n110001100 00000000 # <INV>\n110001101 00000000 # <INV>\n110001110 00000000 # <INV>\n110001111 00000000 # <INV>\n110010000 00000000 # <INV>\n110010001 10000111 # STA pc,xy\n110010010 00000000 # <INV>\n110010011 00000000 # <INV>\n110010100 00000000 # <INV>\n110010101 00000000 # <INV>\n110010110 00000000 # <INV>\n110010111 00000000 # <INV>\n110011000 00000000 # <INV>\n110011001 00000000 # <INV>\n110011010 00000000 # <INV>\n110011011 00000000 # <INV>\n110011100 00000000 # <INV>\n110011101 00000000 # <INV>\n110011110 00000000 # <INV>\n110011111 00000000 # <INV>\n110100000 00000000 # <INV>\n110100001 00000000 # <INV>\n110100010 00000000 # <INV>\n110100011 00000000 # <INV>\n110100100 00000000 # <INV>\n110100101 00000000 # <INV>\n110100110 00000000 # <INV>\n110100111 00000000 # <INV>\n110101000 00000000 # <INV>\n110101001 00000000 # <INV>\n110101010 00000000 # <INV>\n110101011 00000000 # <INV>\n110101100 00000000 # <INV>\n110101101 00000000 # <INV>\n110101110 00000000 # <INV>\n110101111 00000000 # <INV>\n110110000 00000000 # <INV>\n110110001 00000000 # <INV>\n110110010 00000000 # <INV>\n110110011 00000000 # <INV>\n110110100 00000000 # <INV>\n110110101 00000000 # <INV>\n110110110 00000000 # <INV>\n110110111 00000000 # <INV>\n110111000 00000000 # <INV>\n110111001 00000000 # <INV>\n110111010 00000000 # <INV>\n110111011 00000000 # <INV>\n110111100 00000000 # <INV>\n110111101 00000000 # <INV>\n110111110 00000000 # <INV>\n110111111 00000000 # <INV>\n111000000 00000000 # <INV>\n111000001 00000000 # <INV>\n111000010 00000000 # <INV>\n111000011 00000000 # <INV>\n111000100 00000000 # <INV>\n111000101 00000000 # <INV>\n111000110 01010101 # DCC bp\n111000111 00000000 # <INV>\n111001000 01010100 # BTH\n111001001 00000000 # <INV>\n111001010 01011010 # LRW a\n111001011 01011010 # ARW a\n111001100 00000000 # <INV>\n111001101 00000000 # <INV>\n111001110 01010111 # DCC a\n111001111 00000000 # <INV>\n111010000 00000000 # <INV>\n111010001 00000000 # <INV>\n111010010 00000000 # <INV>\n111010011 00000000 # <INV>\n111010100 00000000 # <INV>\n111010101 00000000 # <INV>\n111010110 01010110 # DCC bp,x\n111010111 00000000 # <INV>\n111011000 00000000 # <INV>\n111011001 00000000 # <INV>\n111011010 00000000 # <INV>\n111011011 00000000 # <INV>\n111011100 00000000 # <INV>\n111011101 00000000 # <INV>\n111011110 01011000 # DCC a,x\n111011111 00000000 # <INV>\n111100000 00000000 # <INV>\n111100001 10000110 # LDA (bp,x),y\n111100010 01111111 # LDA sp,y\n111100011 00000000 # <INV>\n111100100 00000000 # <INV>\n111100101 00000000 # <INV>\n111100110 01010101 # ICC bp\n111100111 00000000 # <INV>\n111101000 01010100 # HTB\n111101001 00000000 # <INV>\n111101010 00000001 # NOP\n111101011 01011010 # RRW a\n111101100 00000000 # <INV>\n111101101 00000000 # <INV>\n111101110 01010111 # ICC a\n111101111 10000011 # WAI\n111110000 00000000 # <INV>\n111110001 10000110 # LDA pc,xy\n111110010 00000000 # <INV>\n111110011 00000000 # <INV>\n111110100 00000000 # <INV>\n111110101 00000000 # <INV>\n111110110 01010110 # ICC bp,x\n111110111 00000000 # <INV>\n111111000 00000000 # <INV>\n111111001 00000000 # <INV>\n111111010 00000000 # <INV>\n111111011 00000000 # <INV>\n111111100 00000000 # <INV>\n111111101 00000000 # <INV>\n111111110 01011000 # ICC a,x\n111111111 10000100 # STP")) OPC (
    .in(AA), .out(OPC_out));
  PLA #(.in_width(9), .out_width(4), .\table ("000000000 0000 # BRK #\n000000001 0000 # ORA (bp,x)\n000000010 0000 # CLE\n000000011 0000 # SEE\n000000100 0000 # TSB bp\n000000101 0000 # ORA bp\n000000110 0000 # SFL bp\n000000111 0000 # RMB0 bp\n000001000 0000 # PHP\n000001001 0000 # ORA #\n000001010 0000 # ASL A\n000001011 0000 # TSY\n000001100 0000 # TSB a\n000001101 0000 # ORA a\n000001110 0000 # ASL a\n000001111 1000 # BBR0 bp,r\n000010000 0111 # BPL/BNC r\n000010001 0000 # ORA (bp),y\n000010010 0000 # ORA (bp),z\n000010011 0111 # BPL/BNC rr\n000010100 0000 # TRB bp\n000010101 0000 # ORA bp,x\n000010110 0000 # SFL bp,x\n000010111 0000 # RMB1 bp\n000011000 0000 # CLC\n000011001 0000 # ORA a,y\n000011010 0000 # INA/INC A\n000011011 0000 # INZ/INC Z\n000011100 0000 # TRB a\n000011101 0000 # ORA a,x\n000011110 0000 # ASL a,x\n000011111 1001 # BBR1 bp,r\n000100000 0000 # JSR a\n000100001 0000 # AND (bp,x)\n000100010 0000 # JSR (a)\n000100011 0000 # JSR (a,x)\n000100100 0000 # BIT bp\n000100101 0000 # AND bp\n000100110 0000 # ROL bp\n000100111 0000 # RMB2 bp\n000101000 0000 # PLP\n000101001 0000 # AND #\n000101010 0000 # ROL A\n000101011 0000 # TYS\n000101100 0000 # BIT a\n000101101 0000 # AND a\n000101110 0000 # ROL a\n000101111 1010 # BBR2 bp,r\n000110000 0111 # BMI/BNS r\n000110001 0000 # AND (bp),y\n000110010 0000 # AND (bp),z\n000110011 0111 # BMI/BNS rr\n000110100 0000 # BIT bp,x\n000110101 0000 # AND bp,x\n000110110 0000 # ROL bp,x\n000110111 0000 # RMB3 bp\n000111000 0000 # SEC\n000111001 0000 # AND a,y\n000111010 0000 # DEC A\n000111011 0000 # DEZ/DEC Z\n000111100 0000 # BIT a,x\n000111101 0000 # AND a,x\n000111110 0000 # ROL a,x\n000111111 1011 # BBR3 bp,r\n001000000 0000 # RTI\n001000001 0000 # XOR (bp,x)\n001000010 0000 # NEG A\n001000011 0000 # ASR A\n001000100 0000 # ASR bp\n001000101 0000 # XOR bp\n001000110 0000 # SFR bp\n001000111 0000 # RMB4 bp\n001001000 0000 # PHA\n001001001 0000 # XOR #\n001001010 0000 # LSR A\n001001011 0000 # TAZ\n001001100 0000 # JMP a\n001001101 0000 # XOR a\n001001110 0000 # LSR a\n001001111 1100 # BBR4 bp,r\n001010000 0110 # BVC r\n001010001 0000 # XOR (bp),y\n001010010 0000 # XOR (bp),z\n001010011 0110 # BVC rr\n001010100 0000 # ASR bp,x\n001010101 0000 # XOR bp,x\n001010110 0000 # SFR bp,x\n001010111 0000 # RMB5 bp\n001011000 0000 # CLI\n001011001 0000 # XOR a,y\n001011010 0000 # PHY\n001011011 0000 # TAB\n001011100 0000 # EXTENDED\n001011101 0000 # XOR a,x\n001011110 0000 # LSR a,x\n001011111 1101 # BBR5 bp,r\n001100000 0000 # RTS\n001100001 0000 # ADC (bp,x)\n001100010 0000 # RTN #\n001100011 0000 # BSR rr\n001100100 0000 # STZ bp\n001100101 0000 # ADC bp\n001100110 0000 # ROR bp\n001100111 0000 # RMB6 bp\n001101000 0000 # PLA\n001101001 0000 # ADC #\n001101010 0000 # ROR A\n001101011 0000 # TZA\n001101100 0000 # JMP (a)\n001101101 0000 # ADC a\n001101110 0000 # ROR a\n001101111 1110 # BBR6 bp,r\n001110000 0110 # BVS r\n001110001 0000 # ADC (bp),y\n001110010 0000 # ADC (bp),z\n001110011 0110 # BVS rr\n001110100 0000 # STZ bp,x\n001110101 0000 # ADC bp,x\n001110110 0000 # ROR bp,x\n001110111 0000 # RMB7 bp\n001111000 0000 # SEI\n001111001 0000 # ADC a,y\n001111010 0000 # PLY\n001111011 0000 # TBA\n001111100 0000 # JMP (a,x)\n001111101 0000 # ADC a,x\n001111110 0000 # ROR a,x\n001111111 1111 # BBR7 bp,r\n010000000 0000 # BRA r\n010000001 0000 # STA (bp,x)\n010000010 0000 # STA (d,sp),y\n010000011 0000 # BRA rr\n010000100 0000 # STY bp\n010000101 0000 # STA bp\n010000110 0000 # STX bp\n010000111 0000 # SMB0 bp\n010001000 0000 # DEY/DEC Y\n010001001 0000 # BIT #\n010001010 0000 # TXA\n010001011 0000 # STY a,x\n010001100 0000 # STY a\n010001101 0000 # STA a\n010001110 0000 # STX a\n010001111 1000 # BBS0 bp,r\n010010000 0100 # BCC r\n010010001 0000 # STA (bp),y\n010010010 0000 # STA (bp),z\n010010011 0100 # BCC rr\n010010100 0000 # STY bp,x\n010010101 0000 # STA bp,x\n010010110 0000 # STX bp,y\n010010111 0000 # SMB1 bp\n010011000 0000 # TYA\n010011001 0000 # STA a,y\n010011010 0000 # TXS\n010011011 0000 # STX a,y\n010011100 0000 # STZ a\n010011101 0000 # STA a,x\n010011110 0000 # STZ a,x\n010011111 1001 # BBS1 bp,r\n010100000 0000 # LDY #\n010100001 0000 # LDA (bp,x)\n010100010 0000 # LDX #\n010100011 0000 # LDZ #\n010100100 0000 # LDY bp\n010100101 0000 # LDA bp\n010100110 0000 # LDX bp\n010100111 0000 # SMB2 bp\n010101000 0000 # TAY\n010101001 0000 # LDA #\n010101010 0000 # TAX\n010101011 0000 # LDZ a\n010101100 0000 # LDY a\n010101101 0000 # LDA a\n010101110 0000 # LDX a\n010101111 1010 # BBS2 bp,r\n010110000 0100 # BCS r\n010110001 0000 # LDA (bp),y\n010110010 0000 # LDA (bp),z\n010110011 0100 # BCS rr\n010110100 0000 # LDY bp,x\n010110101 0000 # LDA bp,x\n010110110 0000 # LDX bp,y\n010110111 0000 # SMB3 bp\n010111000 0000 # CLV\n010111001 0000 # LDA a,y\n010111010 0000 # TSX\n010111011 0000 # LDZ a,x\n010111100 0000 # LDY a,x\n010111101 0000 # LDA a,x\n010111110 0000 # LDX a,y\n010111111 1011 # BBS3 bp,r\n011000000 0000 # CPY #\n011000001 0000 # CMP (bp,x)\n011000010 0000 # CPZ #\n011000011 0000 # DEW bp\n011000100 0000 # CPY bp\n011000101 0000 # CMP bp\n011000110 0000 # DEC bp\n011000111 0000 # SMB4 bp\n011001000 0000 # INY/INC Y\n011001001 0000 # CMP #\n011001010 0000 # DEX/DEC X\n011001011 0000 # ASW/ALW a\n011001100 0000 # CPY a\n011001101 0000 # CMP a\n011001110 0000 # DEC a\n011001111 1100 # BBS4 bp,r\n011010000 0101 # BNE/BZC r\n011010001 0000 # CMP (bp),y\n011010010 0000 # CMP (bp),z\n011010011 0101 # BNE/BZC rr\n011010100 0000 # CPZ bp\n011010101 0000 # CMP bp,x\n011010110 0000 # DEC bp,x\n011010111 0000 # SMB5 bp\n011011000 0000 # CLD\n011011001 0000 # CMP a,y\n011011010 0000 # PHX\n011011011 0000 # PHZ\n011011100 0000 # CPZ a\n011011101 0000 # CMP a,x\n011011110 0000 # DEC a,x\n011011111 1101 # BBS5 bp,r\n011100000 0000 # CPX #\n011100001 0000 # SBC (bp,x)\n011100010 0000 # LDA (d,sp),y\n011100011 0000 # INW bp\n011100100 0000 # CPX bp\n011100101 0000 # SBC bp\n011100110 0000 # INC bp\n011100111 0000 # SMB6 bp\n011101000 0000 # INX/INC X\n011101001 0000 # SBC #\n011101010 0000 # NOP\n011101011 0000 # ROW/RLW a\n011101100 0000 # CPX a\n011101101 0000 # SBC a\n011101110 0000 # INC a\n011101111 1110 # BBS6 bp,r\n011110000 0101 # BEQ/BZS r\n011110001 0000 # SBC (bp),y\n011110010 0000 # SBC (bp),z\n011110011 0101 # BEQ/BZS rr\n011110100 0000 # PHW ##\n011110101 0000 # SBC bp,x\n011110110 0000 # INC bp,x\n011110111 0000 # SMB7 bp\n011111000 0000 # SED\n011111001 0000 # SBC a,y\n011111010 0000 # PLX\n011111011 0000 # PLZ\n011111100 0000 # PHW a\n011111101 0000 # SBC a,x\n011111110 0000 # INC a,x\n011111111 1111 # BBS7 bp,r\n100000000 0000 # <INV>\n100000001 0000 # <INV>\n100000010 0000 # <INV>\n100000011 0000 # <INV>\n100000100 0000 # <INV>\n100000101 0000 # MUL bp\n100000110 0000 # <INV>\n100000111 0000 # <INV>\n100001000 0000 # <INV>\n100001001 0000 # MUL #\n100001010 0000 # <INV>\n100001011 0000 # <INV>\n100001100 0000 # <INV>\n100001101 0000 # MUL a\n100001110 0000 # <INV>\n100001111 0000 # <INV>\n100010000 0000 # <INV>\n100010001 0000 # <INV>\n100010010 0000 # <INV>\n100010011 0000 # <INV>\n100010100 0000 # <INV>\n100010101 0000 # MUL bp,x\n100010110 0000 # <INV>\n100010111 0000 # <INV>\n100011000 0000 # <INV>\n100011001 0000 # MUL a,y\n100011010 0000 # <INV>\n100011011 0000 # <INV>\n100011100 0000 # <INV>\n100011101 0000 # MUL a,x\n100011110 0000 # <INV>\n100011111 0000 # <INV>\n100100000 0000 # <INV>\n100100001 0000 # <INV>\n100100010 0000 # <INV>\n100100011 0000 # <INV>\n100100100 0000 # <INV>\n100100101 0000 # MLH bp\n100100110 0000 # <INV>\n100100111 0000 # <INV>\n100101000 0000 # <INV>\n100101001 0000 # MLH #\n100101010 0000 # <INV>\n100101011 0000 # <INV>\n100101100 0000 # <INV>\n100101101 0000 # MLH a\n100101110 0000 # <INV>\n100101111 0000 # <INV>\n100110000 0000 # <INV>\n100110001 0000 # <INV>\n100110010 0000 # <INV>\n100110011 0000 # <INV>\n100110100 0000 # <INV>\n100110101 0000 # MLH bp,x\n100110110 0000 # <INV>\n100110111 0000 # <INV>\n100111000 0000 # <INV>\n100111001 0000 # MLH a,y\n100111010 0000 # <INV>\n100111011 0000 # RND\n100111100 0000 # <INV>\n100111101 0000 # MLH a,x\n100111110 0000 # <INV>\n100111111 0000 # <INV>\n101000000 0000 # <INV>\n101000001 0000 # <INV>\n101000010 0000 # <INV>\n101000011 0000 # <INV>\n101000100 0000 # <INV>\n101000101 0000 # MOD bp\n101000110 0000 # <INV>\n101000111 0000 # <INV>\n101001000 0000 # PHM\n101001001 0000 # MOD #\n101001010 0000 # <INV>\n101001011 0000 # SWN\n101001100 0000 # <INV>\n101001101 0000 # MOD a\n101001110 0000 # <INV>\n101001111 0000 # <INV>\n101010000 0000 # <INV>\n101010001 0000 # <INV>\n101010010 0000 # <INV>\n101010011 0000 # <INV>\n101010100 0000 # <INV>\n101010101 0000 # MOD bp,x\n101010110 0000 # <INV>\n101010111 0000 # <INV>\n101011000 0000 # <INV>\n101011001 0000 # MOD a,y\n101011010 0000 # <INV>\n101011011 0000 # SXY\n101011100 0000 # <INV>\n101011101 0000 # MOD a,x\n101011110 0000 # <INV>\n101011111 0000 # <INV>\n101100000 0000 # <INV>\n101100001 0000 # <INV>\n101100010 0000 # <INV>\n101100011 0000 # <INV>\n101100100 0000 # <INV>\n101100101 0000 # DIV bp\n101100110 0000 # <INV>\n101100111 0000 # <INV>\n101101000 0000 # PLM\n101101001 0000 # DIV #\n101101010 0000 # <INV>\n101101011 0000 # SXZ\n101101100 0000 # <INV>\n101101101 0000 # DIV a\n101101110 0000 # <INV>\n101101111 0000 # <INV>\n101110000 0000 # <INV>\n101110001 0000 # <INV>\n101110010 0000 # <INV>\n101110011 0000 # <INV>\n101110100 0000 # <INV>\n101110101 0000 # DIV bp,x\n101110110 0000 # <INV>\n101110111 0000 # <INV>\n101111000 0000 # <INV>\n101111001 0000 # DIV a,y\n101111010 0000 # <INV>\n101111011 0000 # SYZ\n101111100 0000 # <INV>\n101111101 0000 # DIV a,x\n101111110 0000 # <INV>\n101111111 0000 # <INV>\n110000000 0000 # <INV>\n110000001 0000 # STA (bp,x),y\n110000010 0000 # STA sp,y\n110000011 0000 # <INV>\n110000100 0000 # <INV>\n110000101 0000 # <INV>\n110000110 0000 # <INV>\n110000111 0000 # <INV>\n110001000 0000 # <INV>\n110001001 0000 # <INV>\n110001010 0000 # <INV>\n110001011 0000 # <INV>\n110001100 0000 # <INV>\n110001101 0000 # <INV>\n110001110 0000 # <INV>\n110001111 0000 # <INV>\n110010000 0000 # <INV>\n110010001 0000 # STA pc,xy\n110010010 0000 # <INV>\n110010011 0000 # <INV>\n110010100 0000 # <INV>\n110010101 0000 # <INV>\n110010110 0000 # <INV>\n110010111 0000 # <INV>\n110011000 0000 # <INV>\n110011001 0000 # <INV>\n110011010 0000 # <INV>\n110011011 0000 # <INV>\n110011100 0000 # <INV>\n110011101 0000 # <INV>\n110011110 0000 # <INV>\n110011111 0000 # <INV>\n110100000 0000 # <INV>\n110100001 0000 # <INV>\n110100010 0000 # <INV>\n110100011 0000 # <INV>\n110100100 0000 # <INV>\n110100101 0000 # <INV>\n110100110 0000 # <INV>\n110100111 0000 # <INV>\n110101000 0000 # <INV>\n110101001 0000 # <INV>\n110101010 0000 # <INV>\n110101011 0000 # <INV>\n110101100 0000 # <INV>\n110101101 0000 # <INV>\n110101110 0000 # <INV>\n110101111 0000 # <INV>\n110110000 0000 # <INV>\n110110001 0000 # <INV>\n110110010 0000 # <INV>\n110110011 0000 # <INV>\n110110100 0000 # <INV>\n110110101 0000 # <INV>\n110110110 0000 # <INV>\n110110111 0000 # <INV>\n110111000 0000 # <INV>\n110111001 0000 # <INV>\n110111010 0000 # <INV>\n110111011 0000 # <INV>\n110111100 0000 # <INV>\n110111101 0000 # <INV>\n110111110 0000 # <INV>\n110111111 0000 # <INV>\n111000000 0000 # <INV>\n111000001 0000 # <INV>\n111000010 0000 # <INV>\n111000011 0000 # <INV>\n111000100 0000 # <INV>\n111000101 0000 # <INV>\n111000110 0000 # DCC bp\n111000111 0000 # <INV>\n111001000 0000 # BTH\n111001001 0000 # <INV>\n111001010 0000 # LRW a\n111001011 0000 # ARW a\n111001100 0000 # <INV>\n111001101 0000 # <INV>\n111001110 0000 # DCC a\n111001111 0000 # <INV>\n111010000 0000 # <INV>\n111010001 0000 # <INV>\n111010010 0000 # <INV>\n111010011 0000 # <INV>\n111010100 0000 # <INV>\n111010101 0000 # <INV>\n111010110 0000 # DCC bp,x\n111010111 0000 # <INV>\n111011000 0000 # <INV>\n111011001 0000 # <INV>\n111011010 0000 # <INV>\n111011011 0000 # <INV>\n111011100 0000 # <INV>\n111011101 0000 # <INV>\n111011110 0000 # DCC a,x\n111011111 0000 # <INV>\n111100000 0000 # <INV>\n111100001 0000 # LDA (bp,x),y\n111100010 0000 # LDA sp,y\n111100011 0000 # <INV>\n111100100 0000 # <INV>\n111100101 0000 # <INV>\n111100110 0000 # ICC bp\n111100111 0000 # <INV>\n111101000 0000 # HTB\n111101001 0000 # <INV>\n111101010 0000 # NOP\n111101011 0000 # RRW a\n111101100 0000 # <INV>\n111101101 0000 # <INV>\n111101110 0000 # ICC a\n111101111 0011 # WAI\n111110000 0000 # <INV>\n111110001 0000 # LDA pc,xy\n111110010 0000 # <INV>\n111110011 0000 # <INV>\n111110100 0000 # <INV>\n111110101 0000 # <INV>\n111110110 0000 # ICC bp,x\n111110111 0000 # <INV>\n111111000 0000 # <INV>\n111111001 0000 # <INV>\n111111010 0000 # <INV>\n111111011 0000 # <INV>\n111111100 0000 # <INV>\n111111101 0000 # <INV>\n111111110 0000 # ICC a,x\n111111111 0000 # STP")) CON (
    .in(AA), .out(CON_out));
  and and_15 (CABT, ABT_qn, CABT_q);
  PLA #(.in_width(9), .out_width(8), .\table ("000000000 00000000 # BRK #\n000000001 00011100 # ORA (bp,x)\n000000010 00000010 # CLE\n000000011 00000010 # SEE\n000000100 01010101 # TSB bp\n000000101 00010111 # ORA bp\n000000110 01010101 # SFL bp\n000000111 01010101 # RMB0 bp\n000001000 01011011 # PHP\n000001001 00010110 # ORA #\n000001010 01010100 # ASL A\n000001011 01111000 # TSY\n000001100 01010111 # TSB a\n000001101 00011001 # ORA a\n000001110 01010111 # ASL a\n000001111 00010011 # BBR0 bp,r\n000010000 00001111 # BPL/BNC r\n000010001 00011101 # ORA (bp),y\n000010010 00011110 # ORA (bp),z\n000010011 00010001 # BPL/BNC rr\n000010100 01010101 # TRB bp\n000010101 00011000 # ORA bp,x\n000010110 01010110 # SFL bp,x\n000010111 01010101 # RMB1 bp\n000011000 00000010 # CLC\n000011001 00011011 # ORA a,y\n000011010 01010100 # INA/INC A\n000011011 01101001 # INZ/INC Z\n000011100 01010111 # TRB a\n000011101 00011010 # ORA a,x\n000011110 01011000 # ASL a,x\n000011111 00010011 # BBR1 bp,r\n000100000 00000011 # JSR a\n000100001 00011100 # AND (bp,x)\n000100010 00000100 # JSR (a)\n000100011 00000101 # JSR (a,x)\n000100100 01000011 # BIT bp\n000100101 00010111 # AND bp\n000100110 01010101 # ROL bp\n000100111 01010101 # RMB2 bp\n000101000 01100010 # PLP\n000101001 00010110 # AND #\n000101010 01010100 # ROL A\n000101011 01110110 # TYS\n000101100 01000101 # BIT a\n000101101 00011001 # AND a\n000101110 01010111 # ROL a\n000101111 00010011 # BBR2 bp,r\n000110000 00010000 # BMI/BNS r\n000110001 00011101 # AND (bp),y\n000110010 00011110 # AND (bp),z\n000110011 00010010 # BMI/BNS rr\n000110100 01000100 # BIT bp,x\n000110101 00011000 # AND bp,x\n000110110 01010110 # ROL bp,x\n000110111 01010101 # RMB3 bp\n000111000 00000010 # SEC\n000111001 00011011 # AND a,y\n000111010 01010100 # DEC A\n000111011 01101100 # DEZ/DEC Z\n000111100 01000110 # BIT a,x\n000111101 00011010 # AND a,x\n000111110 01011000 # ROL a,x\n000111111 00010011 # BBR3 bp,r\n001000000 00000111 # RTI\n001000001 00011100 # XOR (bp,x)\n001000010 00010101 # NEG A\n001000011 01010100 # ASR A\n001000100 01010101 # ASR bp\n001000101 00010111 # XOR bp\n001000110 01010101 # SFR bp\n001000111 01010101 # RMB4 bp\n001001000 01011100 # PHA\n001001001 00010110 # XOR #\n001001010 01010100 # LSR A\n001001011 01110000 # TAZ\n001001100 00001010 # JMP a\n001001101 00011001 # XOR a\n001001110 01010111 # LSR a\n001001111 00010011 # BBR4 bp,r\n001010000 00001111 # BVC r\n001010001 00011101 # XOR (bp),y\n001010010 00011110 # XOR (bp),z\n001010011 00010001 # BVC rr\n001010100 01010110 # ASR bp,x\n001010101 00011000 # XOR bp,x\n001010110 01010110 # SFR bp,x\n001010111 01010101 # RMB5 bp\n001011000 00000010 # CLI\n001011001 00011011 # XOR a,y\n001011010 01011110 # PHY\n001011011 01101101 # TAB\n001011100 01111001 # EXTENDED\n001011101 00011010 # XOR a,x\n001011110 01011000 # LSR a,x\n001011111 00010011 # BBR5 bp,r\n001100000 00001000 # RTS\n001100001 00011100 # ADC (bp,x)\n001100010 00001001 # RTN #\n001100011 00000110 # BSR rr\n001100100 00110100 # STZ bp\n001100101 00010111 # ADC bp\n001100110 01010101 # ROR bp\n001100111 01010101 # RMB6 bp\n001101000 01100011 # PLA\n001101001 00010110 # ADC #\n001101010 01010100 # ROR A\n001101011 01110100 # TZA\n001101100 00001011 # JMP (a)\n001101101 00011001 # ADC a\n001101110 01010111 # ROR a\n001101111 00010011 # BBR6 bp,r\n001110000 00010000 # BVS r\n001110001 00011101 # ADC (bp),y\n001110010 00011110 # ADC (bp),z\n001110011 00010010 # BVS rr\n001110100 00111000 # STZ bp,x\n001110101 00011000 # ADC bp,x\n001110110 01010110 # ROR bp,x\n001110111 01010101 # RMB7 bp\n001111000 00000010 # SEI\n001111001 00011011 # ADC a,y\n001111010 01100101 # PLY\n001111011 01110001 # TBA\n001111100 00001100 # JMP (a,x)\n001111101 00011010 # ADC a,x\n001111110 01011000 # ROR a,x\n001111111 00010011 # BBR7 bp,r\n010000000 00001101 # BRA r\n010000001 00101110 # STA (bp,x)\n010000010 00101101 # STA (d,sp),y\n010000011 00001110 # BRA rr\n010000100 00110011 # STY bp\n010000101 00110001 # STA bp\n010000110 00110010 # STX bp\n010000111 01010101 # SMB0 bp\n010001000 01101011 # DEY/DEC Y\n010001001 01000010 # BIT #\n010001010 01110010 # TXA\n010001011 00111110 # STY a,x\n010001100 00111011 # STY a\n010001101 00111001 # STA a\n010001110 00111010 # STX a\n010001111 00010100 # BBS0 bp,r\n010010000 00001111 # BCC r\n010010001 00101111 # STA (bp),y\n010010010 00110000 # STA (bp),z\n010010011 00010001 # BCC rr\n010010100 00110111 # STY bp,x\n010010101 00110101 # STA bp,x\n010010110 00110110 # STX bp,y\n010010111 01010101 # SMB1 bp\n010011000 01110011 # TYA\n010011001 01000000 # STA a,y\n010011010 01110101 # TXS\n010011011 01000001 # STX a,y\n010011100 00111100 # STZ a\n010011101 00111101 # STA a,x\n010011110 00111111 # STZ a,x\n010011111 00010100 # BBS1 bp,r\n010100000 00100001 # LDY #\n010100001 00011100 # LDA (bp,x)\n010100010 00100000 # LDX #\n010100011 00100010 # LDZ #\n010100100 00100100 # LDY bp\n010100101 00010111 # LDA bp\n010100110 00100011 # LDX bp\n010100111 01010101 # SMB2 bp\n010101000 01101111 # TAY\n010101001 00010110 # LDA #\n010101010 01101110 # TAX\n010101011 00101001 # LDZ a\n010101100 00101000 # LDY a\n010101101 00011001 # LDA a\n010101110 00100111 # LDX a\n010101111 00010100 # BBS2 bp,r\n010110000 00010000 # BCS r\n010110001 00011101 # LDA (bp),y\n010110010 00011110 # LDA (bp),z\n010110011 00010010 # BCS rr\n010110100 00100110 # LDY bp,x\n010110101 00011000 # LDA bp,x\n010110110 00100101 # LDX bp,y\n010110111 01010101 # SMB3 bp\n010111000 00000010 # CLV\n010111001 00011011 # LDA a,y\n010111010 01110111 # TSX\n010111011 00101100 # LDZ a,x\n010111100 00101011 # LDY a,x\n010111101 00011010 # LDA a,x\n010111110 00101010 # LDX a,y\n010111111 00010100 # BBS3 bp,r\n011000000 01001100 # CPY #\n011000001 01001000 # CMP (bp,x)\n011000010 01001101 # CPZ #\n011000011 01011001 # DEW bp\n011000100 01001111 # CPY bp\n011000101 01000011 # CMP bp\n011000110 01010101 # DEC bp\n011000111 01010101 # SMB4 bp\n011001000 01101000 # INY/INC Y\n011001001 01000010 # CMP #\n011001010 01101010 # DEX/DEC X\n011001011 01011010 # ASW/ALW a\n011001100 01010010 # CPY a\n011001101 01000101 # CMP a\n011001110 01010111 # DEC a\n011001111 00010100 # BBS4 bp,r\n011010000 00001111 # BNE/BZC r\n011010001 01001001 # CMP (bp),y\n011010010 01001010 # CMP (bp),z\n011010011 00010001 # BNE/BZC rr\n011010100 01010000 # CPZ bp\n011010101 01000100 # CMP bp,x\n011010110 01010110 # DEC bp,x\n011010111 01010101 # SMB5 bp\n011011000 00000010 # CLD\n011011001 01000111 # CMP a,y\n011011010 01011101 # PHX\n011011011 01011111 # PHZ\n011011100 01010011 # CPZ a\n011011101 01000110 # CMP a,x\n011011110 01011000 # DEC a,x\n011011111 00010100 # BBS5 bp,r\n011100000 01001011 # CPX #\n011100001 00011100 # SBC (bp,x)\n011100010 00011111 # LDA (d,sp),y\n011100011 01011001 # INW bp\n011100100 01001110 # CPX bp\n011100101 00010111 # SBC bp\n011100110 01010101 # INC bp\n011100111 01010101 # SMB6 bp\n011101000 01100111 # INX/INC X\n011101001 00010110 # SBC #\n011101010 00000001 # NOP\n011101011 01011010 # ROW/RLW a\n011101100 01010001 # CPX a\n011101101 00011001 # SBC a\n011101110 01010111 # INC a\n011101111 00010100 # BBS6 bp,r\n011110000 00010000 # BEQ/BZS r\n011110001 00011101 # SBC (bp),y\n011110010 00011110 # SBC (bp),z\n011110011 00010010 # BEQ/BZS rr\n011110100 01100000 # PHW ##\n011110101 00011000 # SBC bp,x\n011110110 01010110 # INC bp,x\n011110111 01010101 # SMB7 bp\n011111000 00000010 # SED\n011111001 00011011 # SBC a,y\n011111010 01100100 # PLX\n011111011 01100110 # PLZ\n011111100 01100001 # PHW a\n011111101 00011010 # SBC a,x\n011111110 01011000 # INC a,x\n011111111 00010100 # BBS7 bp,r\n100000000 00000000 # <INV>\n100000001 00000000 # <INV>\n100000010 00000000 # <INV>\n100000011 00000000 # <INV>\n100000100 00000000 # <INV>\n100000101 00010111 # MUL bp\n100000110 00000000 # <INV>\n100000111 00000000 # <INV>\n100001000 00000000 # <INV>\n100001001 00010110 # MUL #\n100001010 00000000 # <INV>\n100001011 00000000 # <INV>\n100001100 00000000 # <INV>\n100001101 00011001 # MUL a\n100001110 00000000 # <INV>\n100001111 00000000 # <INV>\n100010000 00000000 # <INV>\n100010001 00000000 # <INV>\n100010010 00000000 # <INV>\n100010011 00000000 # <INV>\n100010100 00000000 # <INV>\n100010101 00011000 # MUL bp,x\n100010110 00000000 # <INV>\n100010111 00000000 # <INV>\n100011000 00000000 # <INV>\n100011001 00011011 # MUL a,y\n100011010 00000000 # <INV>\n100011011 00000000 # <INV>\n100011100 00000000 # <INV>\n100011101 00011010 # MUL a,x\n100011110 00000000 # <INV>\n100011111 00000000 # <INV>\n100100000 00000000 # <INV>\n100100001 00000000 # <INV>\n100100010 00000000 # <INV>\n100100011 00000000 # <INV>\n100100100 00000000 # <INV>\n100100101 00010111 # MLH bp\n100100110 00000000 # <INV>\n100100111 00000000 # <INV>\n100101000 00000000 # <INV>\n100101001 00010110 # MLH #\n100101010 00000000 # <INV>\n100101011 00000000 # <INV>\n100101100 00000000 # <INV>\n100101101 00011001 # MLH a\n100101110 00000000 # <INV>\n100101111 00000000 # <INV>\n100110000 00000000 # <INV>\n100110001 00000000 # <INV>\n100110010 00000000 # <INV>\n100110011 00000000 # <INV>\n100110100 00000000 # <INV>\n100110101 00011000 # MLH bp,x\n100110110 00000000 # <INV>\n100110111 00000000 # <INV>\n100111000 00000000 # <INV>\n100111001 00011011 # MLH a,y\n100111010 00000000 # <INV>\n100111011 01111010 # RND\n100111100 00000000 # <INV>\n100111101 00011010 # MLH a,x\n100111110 00000000 # <INV>\n100111111 00000000 # <INV>\n101000000 00000000 # <INV>\n101000001 00000000 # <INV>\n101000010 00000000 # <INV>\n101000011 00000000 # <INV>\n101000100 00000000 # <INV>\n101000101 00010111 # MOD bp\n101000110 00000000 # <INV>\n101000111 00000000 # <INV>\n101001000 10000001 # PHR\n101001001 00010110 # MOD #\n101001010 00000000 # <INV>\n101001011 01111011 # SWN\n101001100 00000000 # <INV>\n101001101 00011001 # MOD a\n101001110 00000000 # <INV>\n101001111 00000000 # <INV>\n101010000 00000000 # <INV>\n101010001 00000000 # <INV>\n101010010 00000000 # <INV>\n101010011 00000000 # <INV>\n101010100 00000000 # <INV>\n101010101 00011000 # MOD bp,x\n101010110 00000000 # <INV>\n101010111 00000000 # <INV>\n101011000 00000000 # <INV>\n101011001 00011011 # MOD a,y\n101011010 00000000 # <INV>\n101011011 01111100 # SXY\n101011100 00000000 # <INV>\n101011101 00011010 # MOD a,x\n101011110 00000000 # <INV>\n101011111 00000000 # <INV>\n101100000 00000000 # <INV>\n101100001 00000000 # <INV>\n101100010 00000000 # <INV>\n101100011 00000000 # <INV>\n101100100 00000000 # <INV>\n101100101 00010111 # DIV bp\n101100110 00000000 # <INV>\n101100111 00000000 # <INV>\n101101000 10000010 # PLR\n101101001 00010110 # DIV #\n101101010 00000000 # <INV>\n101101011 01111101 # SXZ\n101101100 00000000 # <INV>\n101101101 00011001 # DIV a\n101101110 00000000 # <INV>\n101101111 00000000 # <INV>\n101110000 00000000 # <INV>\n101110001 00000000 # <INV>\n101110010 00000000 # <INV>\n101110011 00000000 # <INV>\n101110100 00000000 # <INV>\n101110101 00011000 # DIV bp,x\n101110110 00000000 # <INV>\n101110111 00000000 # <INV>\n101111000 00000000 # <INV>\n101111001 00011011 # DIV a,y\n101111010 00000000 # <INV>\n101111011 01111110 # SYZ\n101111100 00000000 # <INV>\n101111101 00011010 # DIV a,x\n101111110 00000000 # <INV>\n101111111 00000000 # <INV>\n110000000 00000000 # <INV>\n110000001 10000101 # STA (bp,x),y\n110000010 10000000 # STA sp,y\n110000011 00000000 # <INV>\n110000100 00000000 # <INV>\n110000101 00000000 # <INV>\n110000110 00000000 # <INV>\n110000111 00000000 # <INV>\n110001000 00000000 # <INV>\n110001001 00000000 # <INV>\n110001010 00000000 # <INV>\n110001011 00000000 # <INV>\n110001100 00000000 # <INV>\n110001101 00000000 # <INV>\n110001110 00000000 # <INV>\n110001111 00000000 # <INV>\n110010000 00000000 # <INV>\n110010001 10000111 # STA pc,xy\n110010010 00000000 # <INV>\n110010011 00000000 # <INV>\n110010100 00000000 # <INV>\n110010101 00000000 # <INV>\n110010110 00000000 # <INV>\n110010111 00000000 # <INV>\n110011000 00000000 # <INV>\n110011001 00000000 # <INV>\n110011010 00000000 # <INV>\n110011011 00000000 # <INV>\n110011100 00000000 # <INV>\n110011101 00000000 # <INV>\n110011110 00000000 # <INV>\n110011111 00000000 # <INV>\n110100000 00000000 # <INV>\n110100001 00000000 # <INV>\n110100010 00000000 # <INV>\n110100011 00000000 # <INV>\n110100100 00000000 # <INV>\n110100101 00000000 # <INV>\n110100110 00000000 # <INV>\n110100111 00000000 # <INV>\n110101000 00000000 # <INV>\n110101001 00000000 # <INV>\n110101010 00000000 # <INV>\n110101011 00000000 # <INV>\n110101100 00000000 # <INV>\n110101101 00000000 # <INV>\n110101110 00000000 # <INV>\n110101111 00000000 # <INV>\n110110000 00000000 # <INV>\n110110001 00000000 # <INV>\n110110010 00000000 # <INV>\n110110011 00000000 # <INV>\n110110100 00000000 # <INV>\n110110101 00000000 # <INV>\n110110110 00000000 # <INV>\n110110111 00000000 # <INV>\n110111000 00000000 # <INV>\n110111001 00000000 # <INV>\n110111010 00000000 # <INV>\n110111011 00000000 # <INV>\n110111100 00000000 # <INV>\n110111101 00000000 # <INV>\n110111110 00000000 # <INV>\n110111111 00000000 # <INV>\n111000000 00000000 # <INV>\n111000001 00000000 # <INV>\n111000010 00000000 # <INV>\n111000011 00000000 # <INV>\n111000100 00000000 # <INV>\n111000101 00000000 # <INV>\n111000110 01010101 # DCC bp\n111000111 00000000 # <INV>\n111001000 01010100 # BTH\n111001001 00000000 # <INV>\n111001010 01011010 # LRW a\n111001011 01011010 # ARW a\n111001100 00000000 # <INV>\n111001101 00000000 # <INV>\n111001110 01010111 # DCC a\n111001111 00000000 # <INV>\n111010000 00000000 # <INV>\n111010001 00000000 # <INV>\n111010010 00000000 # <INV>\n111010011 00000000 # <INV>\n111010100 00000000 # <INV>\n111010101 00000000 # <INV>\n111010110 01010110 # DCC bp,x\n111010111 00000000 # <INV>\n111011000 00000000 # <INV>\n111011001 00000000 # <INV>\n111011010 00000000 # <INV>\n111011011 00000000 # <INV>\n111011100 00000000 # <INV>\n111011101 00000000 # <INV>\n111011110 01011000 # DCC a,x\n111011111 00000000 # <INV>\n111100000 00000000 # <INV>\n111100001 10000110 # LDA (bp,x),y\n111100010 01111111 # LDA sp,y\n111100011 00000000 # <INV>\n111100100 00000000 # <INV>\n111100101 00000000 # <INV>\n111100110 01010101 # ICC bp\n111100111 00000000 # <INV>\n111101000 01010100 # HTB\n111101001 00000000 # <INV>\n111101010 00000001 # NOP\n111101011 01011010 # RRW a\n111101100 00000000 # <INV>\n111101101 00000000 # <INV>\n111101110 01010111 # ICC a\n111101111 10000011 # WAI\n111110000 00000000 # <INV>\n111110001 10000110 # LDA pc,xy\n111110010 00000000 # <INV>\n111110011 00000000 # <INV>\n111110100 00000000 # <INV>\n111110101 00000000 # <INV>\n111110110 01010110 # ICC bp,x\n111110111 00000000 # <INV>\n111111000 00000000 # <INV>\n111111001 00000000 # <INV>\n111111010 00000000 # <INV>\n111111011 00000000 # <INV>\n111111100 00000000 # <INV>\n111111101 00000000 # <INV>\n111111110 01011000 # ICC a,x\n111111111 10000100 # STP")) OPC_2 (
    .in(A_CTRL[9:1]), .out(OPC_2_out));
  PLA #(.in_width(9), .out_width(4), .\table ("000000000 0000 # BRK #\n000000001 0000 # ORA (bp,x)\n000000010 0000 # CLE\n000000011 0000 # SEE\n000000100 0000 # TSB bp\n000000101 0000 # ORA bp\n000000110 0000 # SFL bp\n000000111 0000 # RMB0 bp\n000001000 0000 # PHP\n000001001 0000 # ORA #\n000001010 0000 # ASL A\n000001011 0000 # TSY\n000001100 0000 # TSB a\n000001101 0000 # ORA a\n000001110 0000 # ASL a\n000001111 1000 # BBR0 bp,r\n000010000 0111 # BPL/BNC r\n000010001 0000 # ORA (bp),y\n000010010 0000 # ORA (bp),z\n000010011 0111 # BPL/BNC rr\n000010100 0000 # TRB bp\n000010101 0000 # ORA bp,x\n000010110 0000 # SFL bp,x\n000010111 0000 # RMB1 bp\n000011000 0000 # CLC\n000011001 0000 # ORA a,y\n000011010 0000 # INA/INC A\n000011011 0000 # INZ/INC Z\n000011100 0000 # TRB a\n000011101 0000 # ORA a,x\n000011110 0000 # ASL a,x\n000011111 1001 # BBR1 bp,r\n000100000 0000 # JSR a\n000100001 0000 # AND (bp,x)\n000100010 0000 # JSR (a)\n000100011 0000 # JSR (a,x)\n000100100 0000 # BIT bp\n000100101 0000 # AND bp\n000100110 0000 # ROL bp\n000100111 0000 # RMB2 bp\n000101000 0000 # PLP\n000101001 0000 # AND #\n000101010 0000 # ROL A\n000101011 0000 # TYS\n000101100 0000 # BIT a\n000101101 0000 # AND a\n000101110 0000 # ROL a\n000101111 1010 # BBR2 bp,r\n000110000 0111 # BMI/BNS r\n000110001 0000 # AND (bp),y\n000110010 0000 # AND (bp),z\n000110011 0111 # BMI/BNS rr\n000110100 0000 # BIT bp,x\n000110101 0000 # AND bp,x\n000110110 0000 # ROL bp,x\n000110111 0000 # RMB3 bp\n000111000 0000 # SEC\n000111001 0000 # AND a,y\n000111010 0000 # DEC A\n000111011 0000 # DEZ/DEC Z\n000111100 0000 # BIT a,x\n000111101 0000 # AND a,x\n000111110 0000 # ROL a,x\n000111111 1011 # BBR3 bp,r\n001000000 0000 # RTI\n001000001 0000 # XOR (bp,x)\n001000010 0000 # NEG A\n001000011 0000 # ASR A\n001000100 0000 # ASR bp\n001000101 0000 # XOR bp\n001000110 0000 # SFR bp\n001000111 0000 # RMB4 bp\n001001000 0000 # PHA\n001001001 0000 # XOR #\n001001010 0000 # LSR A\n001001011 0000 # TAZ\n001001100 0000 # JMP a\n001001101 0000 # XOR a\n001001110 0000 # LSR a\n001001111 1100 # BBR4 bp,r\n001010000 0110 # BVC r\n001010001 0000 # XOR (bp),y\n001010010 0000 # XOR (bp),z\n001010011 0110 # BVC rr\n001010100 0000 # ASR bp,x\n001010101 0000 # XOR bp,x\n001010110 0000 # SFR bp,x\n001010111 0000 # RMB5 bp\n001011000 0000 # CLI\n001011001 0000 # XOR a,y\n001011010 0000 # PHY\n001011011 0000 # TAB\n001011100 0000 # EXTENDED\n001011101 0000 # XOR a,x\n001011110 0000 # LSR a,x\n001011111 1101 # BBR5 bp,r\n001100000 0000 # RTS\n001100001 0000 # ADC (bp,x)\n001100010 0000 # RTN #\n001100011 0000 # BSR rr\n001100100 0000 # STZ bp\n001100101 0000 # ADC bp\n001100110 0000 # ROR bp\n001100111 0000 # RMB6 bp\n001101000 0000 # PLA\n001101001 0000 # ADC #\n001101010 0000 # ROR A\n001101011 0000 # TZA\n001101100 0000 # JMP (a)\n001101101 0000 # ADC a\n001101110 0000 # ROR a\n001101111 1110 # BBR6 bp,r\n001110000 0110 # BVS r\n001110001 0000 # ADC (bp),y\n001110010 0000 # ADC (bp),z\n001110011 0110 # BVS rr\n001110100 0000 # STZ bp,x\n001110101 0000 # ADC bp,x\n001110110 0000 # ROR bp,x\n001110111 0000 # RMB7 bp\n001111000 0000 # SEI\n001111001 0000 # ADC a,y\n001111010 0000 # PLY\n001111011 0000 # TBA\n001111100 0000 # JMP (a,x)\n001111101 0000 # ADC a,x\n001111110 0000 # ROR a,x\n001111111 1111 # BBR7 bp,r\n010000000 0000 # BRA r\n010000001 0000 # STA (bp,x)\n010000010 0000 # STA (d,sp),y\n010000011 0000 # BRA rr\n010000100 0000 # STY bp\n010000101 0000 # STA bp\n010000110 0000 # STX bp\n010000111 0000 # SMB0 bp\n010001000 0000 # DEY/DEC Y\n010001001 0000 # BIT #\n010001010 0000 # TXA\n010001011 0000 # STY a,x\n010001100 0000 # STY a\n010001101 0000 # STA a\n010001110 0000 # STX a\n010001111 1000 # BBS0 bp,r\n010010000 0100 # BCC r\n010010001 0000 # STA (bp),y\n010010010 0000 # STA (bp),z\n010010011 0100 # BCC rr\n010010100 0000 # STY bp,x\n010010101 0000 # STA bp,x\n010010110 0000 # STX bp,y\n010010111 0000 # SMB1 bp\n010011000 0000 # TYA\n010011001 0000 # STA a,y\n010011010 0000 # TXS\n010011011 0000 # STX a,y\n010011100 0000 # STZ a\n010011101 0000 # STA a,x\n010011110 0000 # STZ a,x\n010011111 1001 # BBS1 bp,r\n010100000 0000 # LDY #\n010100001 0000 # LDA (bp,x)\n010100010 0000 # LDX #\n010100011 0000 # LDZ #\n010100100 0000 # LDY bp\n010100101 0000 # LDA bp\n010100110 0000 # LDX bp\n010100111 0000 # SMB2 bp\n010101000 0000 # TAY\n010101001 0000 # LDA #\n010101010 0000 # TAX\n010101011 0000 # LDZ a\n010101100 0000 # LDY a\n010101101 0000 # LDA a\n010101110 0000 # LDX a\n010101111 1010 # BBS2 bp,r\n010110000 0100 # BCS r\n010110001 0000 # LDA (bp),y\n010110010 0000 # LDA (bp),z\n010110011 0100 # BCS rr\n010110100 0000 # LDY bp,x\n010110101 0000 # LDA bp,x\n010110110 0000 # LDX bp,y\n010110111 0000 # SMB3 bp\n010111000 0000 # CLV\n010111001 0000 # LDA a,y\n010111010 0000 # TSX\n010111011 0000 # LDZ a,x\n010111100 0000 # LDY a,x\n010111101 0000 # LDA a,x\n010111110 0000 # LDX a,y\n010111111 1011 # BBS3 bp,r\n011000000 0000 # CPY #\n011000001 0000 # CMP (bp,x)\n011000010 0000 # CPZ #\n011000011 0000 # DEW bp\n011000100 0000 # CPY bp\n011000101 0000 # CMP bp\n011000110 0000 # DEC bp\n011000111 0000 # SMB4 bp\n011001000 0000 # INY/INC Y\n011001001 0000 # CMP #\n011001010 0000 # DEX/DEC X\n011001011 0000 # ASW/ALW a\n011001100 0000 # CPY a\n011001101 0000 # CMP a\n011001110 0000 # DEC a\n011001111 1100 # BBS4 bp,r\n011010000 0101 # BNE/BZC r\n011010001 0000 # CMP (bp),y\n011010010 0000 # CMP (bp),z\n011010011 0101 # BNE/BZC rr\n011010100 0000 # CPZ bp\n011010101 0000 # CMP bp,x\n011010110 0000 # DEC bp,x\n011010111 0000 # SMB5 bp\n011011000 0000 # CLD\n011011001 0000 # CMP a,y\n011011010 0000 # PHX\n011011011 0000 # PHZ\n011011100 0000 # CPZ a\n011011101 0000 # CMP a,x\n011011110 0000 # DEC a,x\n011011111 1101 # BBS5 bp,r\n011100000 0000 # CPX #\n011100001 0000 # SBC (bp,x)\n011100010 0000 # LDA (d,sp),y\n011100011 0000 # INW bp\n011100100 0000 # CPX bp\n011100101 0000 # SBC bp\n011100110 0000 # INC bp\n011100111 0000 # SMB6 bp\n011101000 0000 # INX/INC X\n011101001 0000 # SBC #\n011101010 0000 # NOP\n011101011 0000 # ROW/RLW a\n011101100 0000 # CPX a\n011101101 0000 # SBC a\n011101110 0000 # INC a\n011101111 1110 # BBS6 bp,r\n011110000 0101 # BEQ/BZS r\n011110001 0000 # SBC (bp),y\n011110010 0000 # SBC (bp),z\n011110011 0101 # BEQ/BZS rr\n011110100 0000 # PHW ##\n011110101 0000 # SBC bp,x\n011110110 0000 # INC bp,x\n011110111 0000 # SMB7 bp\n011111000 0000 # SED\n011111001 0000 # SBC a,y\n011111010 0000 # PLX\n011111011 0000 # PLZ\n011111100 0000 # PHW a\n011111101 0000 # SBC a,x\n011111110 0000 # INC a,x\n011111111 1111 # BBS7 bp,r\n100000000 0000 # <INV>\n100000001 0000 # <INV>\n100000010 0000 # <INV>\n100000011 0000 # <INV>\n100000100 0000 # <INV>\n100000101 0000 # MUL bp\n100000110 0000 # <INV>\n100000111 0000 # <INV>\n100001000 0000 # <INV>\n100001001 0000 # MUL #\n100001010 0000 # <INV>\n100001011 0000 # <INV>\n100001100 0000 # <INV>\n100001101 0000 # MUL a\n100001110 0000 # <INV>\n100001111 0000 # <INV>\n100010000 0000 # <INV>\n100010001 0000 # <INV>\n100010010 0000 # <INV>\n100010011 0000 # <INV>\n100010100 0000 # <INV>\n100010101 0000 # MUL bp,x\n100010110 0000 # <INV>\n100010111 0000 # <INV>\n100011000 0000 # <INV>\n100011001 0000 # MUL a,y\n100011010 0000 # <INV>\n100011011 0000 # <INV>\n100011100 0000 # <INV>\n100011101 0000 # MUL a,x\n100011110 0000 # <INV>\n100011111 0000 # <INV>\n100100000 0000 # <INV>\n100100001 0000 # <INV>\n100100010 0000 # <INV>\n100100011 0000 # <INV>\n100100100 0000 # <INV>\n100100101 0000 # MLH bp\n100100110 0000 # <INV>\n100100111 0000 # <INV>\n100101000 0000 # <INV>\n100101001 0000 # MLH #\n100101010 0000 # <INV>\n100101011 0000 # <INV>\n100101100 0000 # <INV>\n100101101 0000 # MLH a\n100101110 0000 # <INV>\n100101111 0000 # <INV>\n100110000 0000 # <INV>\n100110001 0000 # <INV>\n100110010 0000 # <INV>\n100110011 0000 # <INV>\n100110100 0000 # <INV>\n100110101 0000 # MLH bp,x\n100110110 0000 # <INV>\n100110111 0000 # <INV>\n100111000 0000 # <INV>\n100111001 0000 # MLH a,y\n100111010 0000 # <INV>\n100111011 0000 # RND\n100111100 0000 # <INV>\n100111101 0000 # MLH a,x\n100111110 0000 # <INV>\n100111111 0000 # <INV>\n101000000 0000 # <INV>\n101000001 0000 # <INV>\n101000010 0000 # <INV>\n101000011 0000 # <INV>\n101000100 0000 # <INV>\n101000101 0000 # MOD bp\n101000110 0000 # <INV>\n101000111 0000 # <INV>\n101001000 0000 # PHM\n101001001 0000 # MOD #\n101001010 0000 # <INV>\n101001011 0000 # SWN\n101001100 0000 # <INV>\n101001101 0000 # MOD a\n101001110 0000 # <INV>\n101001111 0000 # <INV>\n101010000 0000 # <INV>\n101010001 0000 # <INV>\n101010010 0000 # <INV>\n101010011 0000 # <INV>\n101010100 0000 # <INV>\n101010101 0000 # MOD bp,x\n101010110 0000 # <INV>\n101010111 0000 # <INV>\n101011000 0000 # <INV>\n101011001 0000 # MOD a,y\n101011010 0000 # <INV>\n101011011 0000 # SXY\n101011100 0000 # <INV>\n101011101 0000 # MOD a,x\n101011110 0000 # <INV>\n101011111 0000 # <INV>\n101100000 0000 # <INV>\n101100001 0000 # <INV>\n101100010 0000 # <INV>\n101100011 0000 # <INV>\n101100100 0000 # <INV>\n101100101 0000 # DIV bp\n101100110 0000 # <INV>\n101100111 0000 # <INV>\n101101000 0000 # PLM\n101101001 0000 # DIV #\n101101010 0000 # <INV>\n101101011 0000 # SXZ\n101101100 0000 # <INV>\n101101101 0000 # DIV a\n101101110 0000 # <INV>\n101101111 0000 # <INV>\n101110000 0000 # <INV>\n101110001 0000 # <INV>\n101110010 0000 # <INV>\n101110011 0000 # <INV>\n101110100 0000 # <INV>\n101110101 0000 # DIV bp,x\n101110110 0000 # <INV>\n101110111 0000 # <INV>\n101111000 0000 # <INV>\n101111001 0000 # DIV a,y\n101111010 0000 # <INV>\n101111011 0000 # SYZ\n101111100 0000 # <INV>\n101111101 0000 # DIV a,x\n101111110 0000 # <INV>\n101111111 0000 # <INV>\n110000000 0000 # <INV>\n110000001 0000 # STA (bp,x),y\n110000010 0000 # STA sp,y\n110000011 0000 # <INV>\n110000100 0000 # <INV>\n110000101 0000 # <INV>\n110000110 0000 # <INV>\n110000111 0000 # <INV>\n110001000 0000 # <INV>\n110001001 0000 # <INV>\n110001010 0000 # <INV>\n110001011 0000 # <INV>\n110001100 0000 # <INV>\n110001101 0000 # <INV>\n110001110 0000 # <INV>\n110001111 0000 # <INV>\n110010000 0000 # <INV>\n110010001 0000 # STA pc,xy\n110010010 0000 # <INV>\n110010011 0000 # <INV>\n110010100 0000 # <INV>\n110010101 0000 # <INV>\n110010110 0000 # <INV>\n110010111 0000 # <INV>\n110011000 0000 # <INV>\n110011001 0000 # <INV>\n110011010 0000 # <INV>\n110011011 0000 # <INV>\n110011100 0000 # <INV>\n110011101 0000 # <INV>\n110011110 0000 # <INV>\n110011111 0000 # <INV>\n110100000 0000 # <INV>\n110100001 0000 # <INV>\n110100010 0000 # <INV>\n110100011 0000 # <INV>\n110100100 0000 # <INV>\n110100101 0000 # <INV>\n110100110 0000 # <INV>\n110100111 0000 # <INV>\n110101000 0000 # <INV>\n110101001 0000 # <INV>\n110101010 0000 # <INV>\n110101011 0000 # <INV>\n110101100 0000 # <INV>\n110101101 0000 # <INV>\n110101110 0000 # <INV>\n110101111 0000 # <INV>\n110110000 0000 # <INV>\n110110001 0000 # <INV>\n110110010 0000 # <INV>\n110110011 0000 # <INV>\n110110100 0000 # <INV>\n110110101 0000 # <INV>\n110110110 0000 # <INV>\n110110111 0000 # <INV>\n110111000 0000 # <INV>\n110111001 0000 # <INV>\n110111010 0000 # <INV>\n110111011 0000 # <INV>\n110111100 0000 # <INV>\n110111101 0000 # <INV>\n110111110 0000 # <INV>\n110111111 0000 # <INV>\n111000000 0000 # <INV>\n111000001 0000 # <INV>\n111000010 0000 # <INV>\n111000011 0000 # <INV>\n111000100 0000 # <INV>\n111000101 0000 # <INV>\n111000110 0000 # DCC bp\n111000111 0000 # <INV>\n111001000 0000 # BTH\n111001001 0000 # <INV>\n111001010 0000 # LRW a\n111001011 0000 # ARW a\n111001100 0000 # <INV>\n111001101 0000 # <INV>\n111001110 0000 # DCC a\n111001111 0000 # <INV>\n111010000 0000 # <INV>\n111010001 0000 # <INV>\n111010010 0000 # <INV>\n111010011 0000 # <INV>\n111010100 0000 # <INV>\n111010101 0000 # <INV>\n111010110 0000 # DCC bp,x\n111010111 0000 # <INV>\n111011000 0000 # <INV>\n111011001 0000 # <INV>\n111011010 0000 # <INV>\n111011011 0000 # <INV>\n111011100 0000 # <INV>\n111011101 0000 # <INV>\n111011110 0000 # DCC a,x\n111011111 0000 # <INV>\n111100000 0000 # <INV>\n111100001 0000 # LDA (bp,x),y\n111100010 0000 # LDA sp,y\n111100011 0000 # <INV>\n111100100 0000 # <INV>\n111100101 0000 # <INV>\n111100110 0000 # ICC bp\n111100111 0000 # <INV>\n111101000 0000 # HTB\n111101001 0000 # <INV>\n111101010 0000 # NOP\n111101011 0000 # RRW a\n111101100 0000 # <INV>\n111101101 0000 # <INV>\n111101110 0000 # ICC a\n111101111 0011 # WAI\n111110000 0000 # <INV>\n111110001 0000 # LDA pc,xy\n111110010 0000 # <INV>\n111110011 0000 # <INV>\n111110100 0000 # <INV>\n111110101 0000 # <INV>\n111110110 0000 # ICC bp,x\n111110111 0000 # <INV>\n111111000 0000 # <INV>\n111111001 0000 # <INV>\n111111010 0000 # <INV>\n111111011 0000 # <INV>\n111111100 0000 # <INV>\n111111101 0000 # <INV>\n111111110 0000 # ICC a,x\n111111111 0000 # STP")) CON_2 (
    .in(A_CTRL[9:1]), .out(CON_S));
  or or_8 (or_8_out, INTQ, CABT);
  and and_16 (and_16_out, COND, ~or_8_out);  // AND_Gate
  Multiplexer #(.enable("false"), .width(4)) multiplexer_2 (
    .in0(4'b1111), .in1(4'b0101), .out(multiplexer_2_out), .sel(and_16_out));
  or or_9 (or_9_out, IRQ_t, NMI_t, ABT_t, RES);
  or or_10 (or_10_out, INTQ, CABT);
  and and_17 (and_17_out, ~or_10_out, SKIP);  // AND_Gate
  ROM #(.addrWidth(11)) INST (.addr({OPC_2_out, CY}), .data(INST_data));
  ROM #(.addrWidth(3)) IRQ_NMI_ABT (.addr(CY), .data(IRQ_NMI_ABT_data));
  ROM #(.addrWidth(2)) u_RES (.addr(CY[1:0]), .data(RES_data));
  RAM #(.addrWidth(9)) ram_1 (.addr(AA), .we(1'b1), .clk(CC), .din(OPC_out));  // open: dout
  RAM #(.addrWidth(9), .dataWidth(4)) ram_2 (.addr(AA), .we(1'b1), .clk(CC), .din(CON_out));  // open: dout
  or or_11 (or_11_out, COND, CABT, END);
  Multiplexer #(.enable("false"), .width(4)) multiplexer_3 (
    .in0(multiplexer_2_out), .in1(4'b0000), .out(multiplexer_3_out), .sel(and_17_out));
  and and_18 (ACY0, ~or_9_out, CY0);  // AND_Gate
  and and_19 (and_19_out, ~WAIT, and_17_out);  // AND_Gate
  STATE u_CY (.RES(RES), .O({CY0, CY}), .R(R), .C(C), .L(or_11_out), .I(multiplexer_3_out));
  Register #(.trigger("falling")) IR (.D(DI), .en(LDIR), .Q(A_CTRL[8:1]), .clk(C), .clr(R));
  or or_12 (LDIR, ACY0, and_19_out);
  or or_13 (or_13_out, ABT_t, NMI_t, IRQ_t);
  Multiplexer #(.enable("false"), .width(8)) multiplexer_4 (
    .in0(INST_data), .in1(IRQ_NMI_ABT_data), .out(multiplexer_4_out), .sel(or_13_out));
  Multiplexer #(.enable("false"), .width(8)) multiplexer_5 (
    .in0(multiplexer_4_out), .in1(RES_data), .out(multiplexer_5_out), .sel(RES));
  Multiplexer #(.enable("false"), .width(8)) multiplexer_6 (
    .in0(A_CTRL[8:1]), .in1(DI), .out(multiplexer_6_out), .sel(LDIR));
  Multiplexer #(.enable("false")) multiplexer_7 (.in0(A_CTRL[9]), .in1(OP2C), .out(multiplexer_7_out[8]), .sel(LDIR));
  ROM #(.dataWidth(32)) ROM_32 (.addr(multiplexer_5_out), .data(ROM_32_data));
  ROM #(.dataWidth(12)) ROM_12 (.addr(multiplexer_5_out), .data(ROM_12_data));
  ROM #(.addrWidth(9), .dataWidth(3)) u_PCO (.addr({multiplexer_7_out[8], multiplexer_6_out}), .data(PCO_data));
  Multiplexer #(.enable("false"), .width(12)) multiplexer_8 (
    .in0(ROM_12_data), .in1({12{1'b0}}), .out(multiplexer_8_out), .sel(ACY0));
  nor nor_1 (nor_1_out, A_CTRL[1], A_CTRL[2], A_CTRL[3], A_CTRL[4], A_CTRL[6], A_CTRL[7], A_CTRL[8], A_CTRL[5]);
  or or_14 (or_14_out, nor_1_out, IRQ_t);
  Multiplexer #(.enable("false"), .width(32)) multiplexer_9 (
    .in0(ROM_32_data), .in1(32'h4000000), .out(multiplexer_9_out), .sel(ACY0));
  Priority_Encoder #(.select(2)) priority_encoder_1 (
    .in0(or_14_out), .in1(NMI_t), .in2(ABT_t), .in3(RES), .out(priority_encoder_1_out), .gs(INT));  // open: en_out, en_in
  or or_15 (or_15_out, CY0, multiplexer_8_out[10]);
  and and_20 (and_20_out, ~or_15_out, CABT);  // AND_Gate
  Multiplexer #(.enable("false"), .width(32)) multiplexer_10 (
    .in0(multiplexer_9_out), .in1({32{1'b0}}), .out({multiplexer_10_out, R_CTRL[28:0]}), .sel(and_20_out));
  Multiplexer #(.enable("false"), .width(12)) multiplexer_11 (
    .in0(multiplexer_8_out), .in1({12{1'b0}}), .out({END, SKIP, CLR_INT, COND_E, A_CTRL[0], M_CTRL, SPO}),
    .sel(and_20_out));
  // Probe on negator_1_out
  Adder #(.width(3)) adder_1 (.a(3'b000), .b(PCO_data), .out(adder_1_out), .cin(A_CTRL[9]));  // open: cout
  Negator #(.width(3)) negator_1 (.in(adder_1_out), .out(negator_1_out));
  and and_21 (and_21_out, INTQ, SKIP);
  Pull_Resistor pull_resistor_1 (.node(priority_encoder_1_out));
  PLA #(.in_width(3), .\table ("xx0 00 # NONE\n001 11 # IRQ/BRK\n011 01 # NMI\n101 00 # ABORT\n111 10 # RESET")) PRI (
    .in({priority_encoder_1_out, INT}), .out(ANRI));
  Multiplexer #(.enable("false"), .width(3)) multiplexer_12 (
    .in0(multiplexer_10_out), .in1(negator_1_out), .out(R_CTRL[31:29]), .sel(ABT_t));
  Multiplexer #(.enable("false"), .width(3)) multiplexer_13 (.in0(PCO_data), .in1(3'b000), .out(PCO), .sel(and_21_out));

  // Other names for the same wires on the sheet: ALU_EN = A_CTRL[0]; OPC[7:0] = A_CTRL[8:1]; OP2 = A_CTRL[9];
  //   FL_t[3:0] = {FL[6:5], FL[1:0]}

  // Notes on the sheet:
  //   contents of INST (hex, n*v repeats v):
  //   93 89 8d 79 32 0 0 0 6f 7*0 e 7*0 94 8a 76 2c 4*0 3c 37 94 8a 77 30 0 0 3c 37 94 8a 78 31 0 0 94 8a
  //   76 1 4*0 8 44 2e 72 4*0 43 2d 71 5*0 3b 45 2f 7b 4*0 42 2c 6*0 3c 37 46 30 4*0 3c 37 48 31 4*0 2 7*0
  //   42 1 6*0 4 2 0 0 0 6f 0 0 4 6f 0 0 0 2 0 0 4 42 1 0 0 6f 0 0 4 6f 0 0 0 42 1 0 42 3 2 6f 4*0 42 3 6f
  //   2 4*0 f 7*0 1e 7*0 41 1c 6*0 41 1d 6*0 3c 37 21 5*0 3c 37 22 5*0 3c 37 23 5*0 41 3a 36 21 4*0 41 39
  //   35 23 4*0 41 39 35 24 4*0 41 3d 38 23 4*0 52 7*0 5d 7*0 67 7*0 41 50 6*0 41 5b 6*0 41 51 6*0 41 5c
  //   6*0 3c 37 54 5*0 3c 37 5f 5*0 3c 37 69 5*0 3c 37 55 5*0 3c 37 60 5*0 3c 37 6a 5*0 41 3d 38 a5 4*0 41
  //   3a 36 9b 4*0 41 39 35 a5 4*0 41 39 35 a7 4*0 41 81 6*0 41 82 6*0 41 83 6*0 41 84 6*0 41 85 6*0 41 88
  //   6*0 41 86 6*0 41 87 6*0 3c 37 9b 5*0 3c 37 9e 5*0 3c 37 9f 5*0 3c 37 a0 5*0 3c 37 a1 5*0 3c 37 a3
  //   5*0 3c 37 a4 5*0 3c 37 a5 5*0 3c 37 a6 5*0 7 7*0 41 5 6*0 41 6 6*0 3c 37 a 5*0 3c 37 b 5*0 3c 37 c
  //   5*0 41 3a 36 a 4*0 41 39 35 c 4*0 41 39 35 d 4*0 13 7*0 16 7*0 19 7*0 41 12 6*0 41 15 6*0 41 18 6*0
  //   3c 37 14 5*0 3c 37 17 5*0 3c 37 1a 5*0 25 7*0 3b 49 7f 5*0 3b 4a 80 5*0 3c 37 4b 9d 4*0 3c 37 4c a2
  //   4*0 3b 40 4d 7e 7d 0 0 0 3c 37 47 4e 9c 9a 0 0 92 74 6*0 91 74 6*0 96 74 6*0 97 74 6*0 98 74 6*0 42
  //   3e 95 8b 75 0 0 0 3c 37 46 3f 95 8b 75 0 8 70 6*0 1f 70 6*0 53 70 6*0 5e 70 6*0 68 70 6*0 58 7*0 63
  //   7*0 6c 7*0 58 7*0 63 7*0 6c 7*0 2b 7*0 56 7*0 61 7*0 6b 7*0 26 7*0 27 7*0 28 7*0 29 7*0 34 7*0 33
  //   7*0 57 7*0 62 7*0 6f 7*0 10 7*0 11 7*0 65 59 6*0 6d 59 6*0 6e 64 6*0 20 7*0 99 7*0 98 8c 8e 8f 90 7a
  //   0 0 1b 2a 4f 5a 66 73 0 0 7c 7*0 4 4*0 4 0 0 41 3a 36 23 4*0 41 3a 36 9b 4*0 aa 7*0 ab
  //   contents of IRQ_NMI_ABT (hex, n*v repeats v):
  //   93 89 8d 79 a9
  //   contents of RES (hex, n*v repeats v):
  //   79 a9
  //   contents of ROM_32 (hex, n*v repeats v):
  //   0 e6000000 e5000000 5000 1000 5018 6018 e0000018 b018 b018 1018 2018 3018 4018 4000000 4800c1c
  //   4800e1c 4800a1c 5019 e0000019 1019 501a e000001a 101a 501b e000001b 101b 80b000 805218 806218
  //   e0800218 80b218 80c218 801218 802218 803218 804218 4800200 4800204 4800208 480020c 4800210 90b000
  //   4900200 e7000000 7f0b000 700b000 7f0e000 27001000 27002000 700f000 14f00000 cf00000 20d05000
  //   20d06000 e0d00000 d0d000 e05000 e06000 e0e00000 c0e00000 e0d000 e0080000 20081000 48000 e0040000
  //   c0040000 4b000 4b000 4e000 41000 41000 42000 58018 59018 51018 52018 200d8018 200d1018 a0b000 a05218
  //   a07218 e0a00218 a0b218 a01218 a03218 4a00200 4a00214 4a00208 4a00400 b0b000 b05218 b06218 e0b00218
  //   b0b218 b01218 b02218 4b00200 4b00214 4b0020c 4b00400 b60600 c0b000 e0c00218 c0b218 c01218 c02218
  //   4c00200 4c00210 c70600 c70800 4000000 6*1c000000 d8040000 18041000 18042000 1804f000 1c000000
  //   1c000200 0 200080e0 80c0 80c0 90c0 5000 5040 5060 5080 6000 6060 6080 7040 b100 e000b100 b0c0 b060
  //   b0a0 b040 b020 b000 b000 b0a0 b120 e000b120 b0e0 b040 b060 b080 c000 200010e0 1000 10c0 10c0 1040
  //   1060 1080 2000 20c0 2060 2080 3000 3040 4000 b0a0 700f000 80a218 a000 83*0 4000000
  //   contents of ROM_12 (hex, n*v repeats v):
  //   0 800 800 100 100 880 880 880 81 881 4*880 4*c80 9*880 1 880 880 880 81 5*880 5*c80 2 c00 800 2 3 2
  //   800 800 800 c00 c00 0 0 0 2 4*0 1 0 0 20 0 0 1 2 1 0 20 0 6*a0 3 880 880 880 81 880 880 c80 c80 c80
  //   c00 4 880 880 880 881 880 880 c80 c80 c80 c00 0 5 880 81 880 880 c80 c80 0 0 c00 c01 c02 c03 c05 c0f
  //   c0e e e e d c0b c02 100 830 30 830 830 8*810 4*1f 1e 1e 1d 1c 8*10 810 830 810 30 830 4*810 830
  //   5*810 5e a00 880 810
  //   contents of PCO (hex, n*v repeats v):
  //   2 2 1 1 4*2 1 2 1 1 4*3 2 2 2 3 4*2 1 3 1 1 5*3 2 3 3 4*2 1 2 1 1 4*3 2 2 2 3 4*2 1 3 1 1 4*3 1 2 1
  //   1 4*2 1 2 1 1 4*3 2 2 2 3 4*2 1 3 1 1 1 3 3 3 1 2 2 3 4*2 1 2 1 1 4*3 2 2 2 3 4*2 1 3 1 1 4*3 2 2 2
  //   3 4*2 1 2 1 5*3 2 2 2 3 4*2 1 3 1 5*3 8*2 1 2 1 5*3 2 2 2 3 4*2 1 3 1 5*3 8*2 1 2 1 5*3 2 2 2 3 4*2
  //   1 3 1 1 4*3 8*2 1 2 1 5*3 2 2 2 3 3 2 2 2 1 3 1 1 4*3 5*0 2 0 0 0 2 0 0 0 3 7*0 2 0 0 0 3 0 0 0 3
  //   7*0 2 0 0 0 2 0 0 0 3 7*0 2 0 0 0 3 0 1 0 3 7*0 2 0 0 1 2 0 1 0 3 7*0 2 0 0 0 3 0 1 0 3 7*0 2 0 0 1
  //   2 0 1 0 3 7*0 2 0 0 0 3 0 1 0 3 0 0 0 2 1 14*0 1 52*0 2 0 1 0 3 3 0 0 3 7*0 2 7*0 3 0 0 2 1 0 0 0 2
  //   0 1 0 0 3 0 0 3 1 0 1 4*0 2 7*0 3 1
endmodule

module ADDER (
  input  D_I,
  input  C_I,
  input  [3:0] SEL,
  input  [7:0] A,
  input  [15:0] B,
  output [7:0] QL,
  output V_O,
  output C_O,
  output [7:0] QH
);

  wire adder_1_cout, adder_2_cout, adder_3_cout, adder_4_cout, adder_5_cout, and_1_out, and_2_out, and_3_out,
       and_4_out, and_5_out, multiplexer_4_out, multiplexer_5_out, nand_1_out, xor_1_out, xor_2_out,
       xor_3_out;
  wire [2:2] or_1_out, or_2_out;
  wire [3:0] adder_4_out, adder_5_out, adder_6_out, adder_7_out, multiplexer_2_out, multiplexer_2_out_2;
  wire [6:0] adder_1_out;
  wire [7:0] bit_extender_1_out, complement_1_o, multiplexer_1_p6, multiplexer_3_out;
  wire [7:7] adder_2_out;

  and and_1 (and_1_out, D_I, SEL[2]);
  // Multiplexer #(.enable("false"), .select(2), .width(8)) multiplexer_1: pin names not known; wires that end beside it: A, {8{1'b0}}, A, B[7:0], SEL[1:0], multiplexer_1_p6
  Multiplexer #(.enable("false"), .select(2), .width(8)) multiplexer_2 (
    .in0(B[7:0]), .in1(B[7:0]), .in2(complement_1_o), .in3(multiplexer_3_out),
    .out({multiplexer_2_out_2, multiplexer_2_out}));  // open: sel
  Complement complement_1 (.O(complement_1_o), .D(and_1_out), .I(B[7:0]));
  Multiplexer #(.enable("false"), .width(8)) multiplexer_3 (
    .in0({8{1'b1}}), .in1(8'h99), .out(multiplexer_3_out), .sel(and_1_out));
  assign bit_extender_1_out = {{7{SEL[1]}}, SEL[1]};  // Bit_Extender bit_extender_1
  Multiplexer #(.enable("false"), .select(3)) multiplexer_4 (
    .in0(1'b0), .in1(1'b1), .in2(1'b1), .in3(1'b0), .in4(C_I), .in5(C_I), .in6(C_I), .in7(C_I),
    .out(multiplexer_4_out));  // open: sel
  Adder #(.width(7)) adder_1 (
    .a(multiplexer_1_p6[6:0]), .b({multiplexer_2_out_2[2:0], multiplexer_2_out}), .out(adder_1_out),
    .cin(multiplexer_4_out), .cout(adder_1_cout));
  Adder #(.width(1)) adder_2 (
    .a(multiplexer_1_p6[7]), .b(multiplexer_2_out_2[3]), .out(adder_2_out[7]), .cin(adder_1_cout),
    .cout(adder_2_cout));
  Adder adder_3 (.a(B[15:8]), .b(bit_extender_1_out), .out(QH), .cin(adder_2_cout), .cout(adder_3_cout));
  Adder #(.width(4)) adder_4 (
    .a(multiplexer_1_p6[3:0]), .b(multiplexer_2_out), .out(adder_4_out), .cin(C_I), .cout(adder_4_cout));
  and and_2 (and_2_out, adder_4_out[3], adder_4_out[1]);
  and and_3 (and_3_out, adder_4_out[3], adder_4_out[2]);
  or or_1 (or_1_out[2], adder_4_cout, and_2_out, and_3_out);
  Adder #(.width(4)) adder_5 (
    .a(multiplexer_1_p6[7:4]), .b(multiplexer_2_out_2), .out(adder_5_out), .cin(or_1_out[2]),
    .cout(adder_5_cout));
  and and_4 (and_4_out, adder_5_out[3], adder_5_out[1]);
  and and_5 (and_5_out, adder_5_out[3], adder_5_out[2]);
  or or_2 (or_2_out[2], adder_5_cout, and_4_out, and_5_out);
  xor xor_1 (xor_1_out, multiplexer_1_p6[7], multiplexer_2_out_2[3]);
  xor xor_2 (xor_2_out, multiplexer_1_p6[7], adder_7_out[3]);
  xor xor_3 (xor_3_out, adder_1_cout, adder_2_cout);
  Multiplexer #(.enable("false")) multiplexer_5 (
    .in0(adder_2_cout), .in1(adder_3_cout), .out(multiplexer_5_out), .sel(SEL[3]));
  Adder #(.width(4)) adder_6 (
    .a(adder_4_out), .b({1'b0, {2{or_1_out[2]}}, 1'b0}), .out(adder_6_out));  // open: cin, cout
  Adder #(.width(4)) adder_7 (
    .a(adder_5_out), .b({1'b0, {2{or_2_out[2]}}, 1'b0}), .out(adder_7_out));  // open: cin, cout
  nand nand_1 (nand_1_out, xor_1_out, xor_2_out);
  Multiplexer #(.enable("false"), .width(8)) multiplexer_6 (
    .in0({adder_2_out[7], adder_1_out}), .in1({adder_7_out, adder_6_out}), .out(QL), .sel(and_1_out));
  Multiplexer #(.enable("false")) multiplexer_7 (.in0(xor_3_out), .in1(nand_1_out), .out(V_O), .sel(and_1_out));
  Multiplexer #(.enable("false")) multiplexer_8 (
    .in0(multiplexer_5_out), .in1(or_2_out[2]), .out(C_O), .sel(and_1_out));
  // Probe on A
  // Probe on B
  // Probe on {QH, QL}

  // Other names for the same wires on the sheet: B_t[7:0] = B[7:0]; BH[7:0] = B[15:8]; C = C_I

  // Notes on the sheet:
  //   0000 ADD (C/D has no effect)
  //   0001 INC (C/D has no effect)
  //   0010 SUB (C/D has no effect)
  //   0011 DEC (C/D has no effect)
  //   0100 ADC
  //   0101 ICC
  //   0110 SBC
  //   0111 DCC
  //   1001 INC WORD
  //   1011 DEC WORD
endmodule

module PSREG (
  input  R,
  input  C,
  input  L,
  input  [7:0] I,
  input  [7:0] S,
  output [7:0] O
);

  wire d_ff_1_qn, multiplexer_1_out;
  wire [7:0] register_1_q;

  Multiplexer #(.enable("false")) multiplexer_1 (.in0(1'b1), .in1(L), .out(multiplexer_1_out), .sel(d_ff_1_qn));
  Register #(.trigger("falling")) register_1 (.D(I), .en(L), .Q(register_1_q), .clk(C), .clr(R));
  D_Flip_Flop #(.trigger("falling")) d_ff_1 (
    .clk(C), .D(multiplexer_1_out), .Qn(d_ff_1_qn), .reset(R));  // open: Q, preset
  Multiplexer #(.enable("false"), .width(8)) multiplexer_2 (.in0(register_1_q), .in1(S), .out(O), .sel(d_ff_1_qn));
endmodule

module LFSR (
  input  C,
  output [7:0] O_8
);

  wire shift_register_1_p1, shift_register_1_p7, xor_1_out, xor_2_out;
  wire [7:0] not_1_out, shift_register_1_p9, shift_register_1_p13, xor_3_out;

  // Shift_Register #(.length(17)) shift_register_1: pin names not known; wires that end beside it: shift_register_1_p1, C, shift_register_1_p13[7], shift_register_1_p13[2], shift_register_1_p9[2], shift_register_1_p13[5], shift_register_1_p7, shift_register_1_p13[3], shift_register_1_p9[0], shift_register_1_p9[4], shift_register_1_p9[6], shift_register_1_p13[1], shift_register_1_p13[0], shift_register_1_p13[4], shift_register_1_p9[3], shift_register_1_p13[6], shift_register_1_p9[5], shift_register_1_p9[7], shift_register_1_p9[1]
  xnor xnor_1 (shift_register_1_p1, shift_register_1_p13[0], xor_1_out);
  xor xor_1 (xor_1_out, shift_register_1_p9[3], xor_2_out);
  xor xor_2 (xor_2_out, shift_register_1_p13[6], shift_register_1_p9[7]);
  assign xor_3_out = shift_register_1_p9 ^ shift_register_1_p13;  // XOR_Gate xor_3, 8 bits wide
  Multiplexer #(.enable("false"), .width(8)) multiplexer_1 (
    .in0(xor_3_out), .in1(not_1_out), .out(O_8), .sel(shift_register_1_p7));
  assign not_1_out = ~xor_3_out;  // NOT_Gate not_1, 8 bits wide
endmodule

module STATE (
  input  R,
  input  C,
  input  L,
  input  [3:0] I,
  output RES,
  output [3:0] O
);

  wire multiplexer_1_out;

  Counter #(.max('hf), .trigger("falling"), .width(4)) STATE (
    .load(L), .D(I), .count(1'b1), .Q(O), .clk(C), .clr(R));  // open: carry
  D_Flip_Flop #(.trigger("falling")) d_ff_1 (.clk(C), .D(multiplexer_1_out), .Qn(RES), .reset(R));  // open: Q, preset
  Multiplexer #(.enable("false")) multiplexer_1 (.in0(1'b1), .in1(L), .out(multiplexer_1_out), .sel(RES));
endmodule

module Complement (
  input  D,
  input  [7:0] I,
  output [7:0] O
);

  wire [3:0] pla_1_out, pla_2_out;
  wire [7:0] not_1_out;

  PLA #(.in_width(4), .out_width(4), .\table ("0000 1001 # 0\n0001 1000 # 1\n0010 0111 # 2\n0011 0110 # 3\n0100 0101 # 4\n0101 0100 # 5\n0110 0011 # 6\n0111 0010 # 7\n1000 0001 # 8\n1011 0000 # 9")) pla_1 (
    .in(I[3:0]), .out(pla_1_out));
  PLA #(.in_width(4), .out_width(4), .\table ("0000 1001 # 0\n0001 1000 # 1\n0010 0111 # 2\n0011 0110 # 3\n0100 0101 # 4\n0101 0100 # 5\n0110 0011 # 6\n0111 0010 # 7\n1000 0001 # 8\n1011 0000 # 9")) pla_2 (
    .in(I[7:4]), .out(pla_2_out));
  assign not_1_out = ~I;  // NOT_Gate not_1, 8 bits wide
  Multiplexer #(.enable("false"), .width(8)) multiplexer_1 (
    .in0(not_1_out), .in1({pla_2_out, pla_1_out}), .out(O), .sel(D));
endmodule

module ED (
  input  CLK,
  input  IN,
  output FE,
  output RE
);

  wire d_ff_1_q, d_ff_2_q, d_ff_2_qn;

  D_Flip_Flop d_ff_1 (.clk(CLK), .D(IN), .Q(d_ff_1_q));  // open: Qn, preset, reset
  D_Flip_Flop d_ff_2 (.clk(CLK), .D(d_ff_1_q), .Q(d_ff_2_q), .Qn(d_ff_2_qn));  // open: preset, reset
  and and_1 (FE, ~d_ff_1_q, d_ff_2_q);  // AND_Gate
  and and_2 (RE, d_ff_2_qn, d_ff_1_q);
endmodule

module DB8 (
  input  SE,
  input  [7:0] DI,
  output [7:0] DO
);

  wire [7:0] bit_extender_1_out;

  assign bit_extender_1_out = {{7{SE}}, SE};  // Bit_Extender bit_extender_1
  assign DO = bit_extender_1_out & DI;  // AND_Gate and_1, 8 bits wide
endmodule

module CHB (
  input  [7:0] IN,
  output [8:0] OUT
);

  wire and_1_out, and_2_out, and_3_out, and_4_out, and_5_out, and_6_out, and_7_out, and_8_out, and_9_out,
       and_10_out, and_11_out, and_12_out, and_13_out, and_14_out, and_15_out, and_16_out, and_17_out,
       and_18_out, and_19_out, and_20_out, and_21_out, and_22_out, and_23_out, and_24_out, and_25_out,
       and_26_out, and_27_out, and_28_out, and_29_out, and_30_out, and_31_out, and_32_out, and_33_out,
       and_34_out, and_35_out, and_36_out, and_37_out, and_38_out, and_39_out, and_40_out, and_41_out,
       and_42_out, and_43_out, and_44_out, and_45_out, and_46_out, and_47_out, and_48_out, and_49_out,
       and_50_out, and_51_out, and_52_out, and_53_out, and_54_out, and_55_out, and_56_out, and_57_out,
       and_58_out, and_59_out, and_60_out, and_61_out, and_62_out, and_63_out, and_64_out;

  and and_1 (and_1_out, IN[6], IN[5], IN[2]);
  and and_2 (and_2_out, IN[6], IN[5], IN[3]);
  and and_3 (and_3_out, IN[6], IN[5], IN[4]);
  and and_4 (and_4_out, ~IN[7], IN[6], ~IN[5], IN[4]);  // AND_Gate
  and and_5 (and_5_out, ~IN[7], IN[6], IN[5], ~IN[4], ~IN[3], ~IN[2]);  // AND_Gate
  and and_6 (and_6_out, ~IN[7], ~IN[6], IN[5], IN[3]);  // AND_Gate
  and and_7 (and_7_out, ~IN[7], ~IN[6], IN[5], IN[4]);  // AND_Gate
  and and_8 (and_8_out, ~IN[7], IN[6], ~IN[5], ~IN[4]);  // AND_Gate
  and and_9 (and_9_out, ~IN[7], ~IN[6], ~IN[5], IN[4], IN[2]);  // AND_Gate
  and and_10 (and_10_out, ~IN[7], ~IN[6], ~IN[5], IN[4], IN[3]);  // AND_Gate
  and and_11 (and_11_out, ~IN[7], ~IN[6], IN[4], IN[3], IN[2]);  // AND_Gate
  and and_12 (and_12_out, ~IN[7], ~IN[6], IN[5], ~IN[4], ~IN[3]);  // AND_Gate
  and and_13 (and_13_out, ~IN[7], IN[6], ~IN[5], ~IN[4]);  // AND_Gate
  and and_14 (and_14_out, ~IN[7], ~IN[5], ~IN[4], IN[3], IN[1]);  // AND_Gate
  and and_15 (and_15_out, ~IN[7], ~IN[5], ~IN[4], IN[3], IN[2]);  // AND_Gate
  and and_16 (and_16_out, ~IN[7], ~IN[5], IN[3], IN[2], IN[1]);  // AND_Gate
  and and_17 (and_17_out, ~IN[7], ~IN[6], ~IN[5], IN[4], ~IN[3], ~IN[2]);  // AND_Gate
  and and_18 (and_18_out, ~IN[7], IN[5], ~IN[4], ~IN[3], ~IN[2]);  // AND_Gate
  and and_19 (and_19_out, ~IN[7], ~IN[6], IN[5], ~IN[3], IN[1]);  // AND_Gate
  and and_20 (and_20_out, ~IN[7], ~IN[6], IN[5], ~IN[3], IN[2]);  // AND_Gate
  and and_21 (and_21_out, ~IN[7], ~IN[6], IN[5], IN[4], IN[3], ~IN[2]);  // AND_Gate
  and and_22 (and_22_out, ~IN[7], IN[6], ~IN[5], ~IN[4], IN[2], IN[1]);  // AND_Gate
  and and_23 (and_23_out, ~IN[7], IN[6], ~IN[5], ~IN[4], IN[3]);  // AND_Gate
  and and_24 (and_24_out, ~IN[7], IN[6], ~IN[5], IN[3], IN[1]);  // AND_Gate
  and and_25 (and_25_out, ~IN[7], IN[6], ~IN[5], IN[3], IN[2]);  // AND_Gate
  and and_26 (and_26_out, ~IN[7], ~IN[6], ~IN[5], ~IN[4], IN[3], ~IN[2], ~IN[1]);  // AND_Gate
  and and_27 (and_27_out, ~IN[7], ~IN[6], ~IN[5], IN[4], ~IN[3], ~IN[2], IN[1]);  // AND_Gate
  and and_28 (and_28_out, ~IN[7], ~IN[6], ~IN[5], IN[4], IN[3], IN[2], ~IN[1]);  // AND_Gate
  and and_29 (and_29_out, ~IN[7], ~IN[6], IN[5], ~IN[4], ~IN[3], IN[2], IN[1]);  // AND_Gate
  and and_30 (and_30_out, ~IN[7], ~IN[6], IN[5], IN[4], ~IN[3], ~IN[2], ~IN[1]);  // AND_Gate
  and and_31 (and_31_out, ~IN[7], ~IN[6], IN[5], IN[4], IN[3], ~IN[2], IN[1]);  // AND_Gate
  and and_32 (and_32_out, ~IN[7], IN[6], ~IN[5], ~IN[4], ~IN[3], IN[2], ~IN[1]);  // AND_Gate
  and and_33 (and_33_out, ~IN[7], IN[6], ~IN[5], ~IN[4], IN[3], IN[2], IN[1]);  // AND_Gate
  and and_34 (and_34_out, ~IN[7], IN[6], ~IN[5], IN[4], IN[3], ~IN[2], ~IN[1]);  // AND_Gate
  and and_35 (and_35_out, ~IN[7], IN[6], IN[5], ~IN[4], ~IN[3], ~IN[2], IN[1]);  // AND_Gate
  and and_36 (and_36_out, ~IN[7], ~IN[6], ~IN[4], ~IN[3], IN[2], ~IN[1]);  // AND_Gate
  and and_37 (and_37_out, ~IN[7], ~IN[6], ~IN[5], ~IN[4], IN[2], IN[1]);  // AND_Gate
  and and_38 (and_38_out, ~IN[7], ~IN[6], ~IN[5], IN[4], ~IN[2], ~IN[1]);  // AND_Gate
  and and_39 (and_39_out, ~IN[7], ~IN[6], ~IN[5], IN[4], IN[3], ~IN[2]);  // AND_Gate
  and and_40 (and_40_out, ~IN[7], ~IN[6], IN[4], IN[3], ~IN[2], ~IN[1]);  // AND_Gate
  and and_41 (and_41_out, ~IN[7], ~IN[6], IN[5], ~IN[4], ~IN[3], ~IN[2], IN[1]);  // AND_Gate
  and and_42 (and_42_out, ~IN[7], ~IN[6], IN[5], ~IN[4], IN[3], IN[2]);  // AND_Gate
  and and_43 (and_43_out, ~IN[7], ~IN[6], IN[5], IN[4], ~IN[3], IN[2], IN[1]);  // AND_Gate
  and and_44 (and_44_out, ~IN[7], IN[6], ~IN[4], ~IN[3], ~IN[2], ~IN[1]);  // AND_Gate
  and and_45 (and_45_out, ~IN[7], IN[6], ~IN[5], ~IN[4], ~IN[2], IN[1]);  // AND_Gate
  and and_46 (and_46_out, ~IN[7], IN[6], ~IN[5], ~IN[4], IN[3], IN[2], ~IN[1]);  // AND_Gate
  and and_47 (and_47_out, ~IN[7], IN[6], ~IN[5], IN[4], ~IN[3], IN[2]);  // AND_Gate
  and and_48 (and_48_out, ~IN[7], IN[6], ~IN[5], IN[4], IN[2], IN[1]);  // AND_Gate
  and and_49 (and_49_out, ~IN[7], ~IN[5], ~IN[4], ~IN[3], ~IN[2], IN[1]);  // AND_Gate
  and and_50 (and_50_out, ~IN[7], ~IN[6], ~IN[5], ~IN[3], IN[2], IN[1]);  // AND_Gate
  and and_51 (and_51_out, ~IN[7], ~IN[5], ~IN[4], IN[3], IN[2], ~IN[1]);  // AND_Gate
  and and_52 (and_52_out, ~IN[7], ~IN[6], ~IN[5], IN[4], ~IN[3], ~IN[2], ~IN[1]);  // AND_Gate
  and and_53 (and_53_out, ~IN[7], ~IN[6], ~IN[5], IN[4], IN[3], ~IN[2], IN[1]);  // AND_Gate
  and and_54 (and_54_out, ~IN[7], IN[5], ~IN[4], ~IN[3], ~IN[2], ~IN[1]);  // AND_Gate
  and and_55 (and_55_out, ~IN[7], ~IN[6], IN[5], ~IN[3], IN[2], ~IN[1]);  // AND_Gate
  and and_56 (and_56_out, ~IN[7], ~IN[6], IN[5], ~IN[4], IN[3], IN[1]);  // AND_Gate
  and and_57 (and_57_out, ~IN[7], ~IN[6], IN[5], IN[3], IN[2], IN[1]);  // AND_Gate
  and and_58 (and_58_out, ~IN[7], ~IN[6], IN[5], IN[4], IN[3], ~IN[2], ~IN[1]);  // AND_Gate
  and and_59 (and_59_out, ~IN[7], IN[6], ~IN[5], ~IN[4], IN[3], ~IN[1]);  // AND_Gate
  and and_60 (and_60_out, ~IN[7], IN[6], ~IN[5], IN[3], IN[2], ~IN[1]);  // AND_Gate
  and and_61 (and_61_out, ~IN[7], IN[6], ~IN[5], IN[4], ~IN[3], IN[1]);  // AND_Gate
  and and_62 (and_62_out, ~IN[7], ~IN[6], IN[0]);  // AND_Gate
  and and_63 (and_63_out, ~IN[7], ~IN[5], IN[0]);  // AND_Gate
  and and_64 (and_64_out, ~IN[7], ~IN[4], ~IN[3], ~IN[2], IN[0]);  // AND_Gate
  or or_1 (OUT[8], and_1_out, and_2_out, and_3_out, IN[7]);
  or or_2 (OUT[7], and_4_out, and_5_out);
  or or_3 (OUT[6], and_6_out, and_7_out, and_8_out);
  or or_4 (OUT[5], and_9_out, and_10_out, and_11_out, and_12_out, and_13_out);
  or or_5 (OUT[4], and_14_out, and_15_out, and_16_out, and_17_out, and_18_out, and_19_out, and_20_out, and_21_out, and_22_out, and_23_out, and_24_out, and_25_out);
  or or_6 (OUT[3], and_26_out, and_27_out, and_28_out, and_29_out, and_30_out, and_31_out, and_32_out, and_33_out, and_34_out, and_35_out);
  or or_7 (OUT[2], and_36_out, and_37_out, and_38_out, and_39_out, and_40_out, and_41_out, and_42_out, and_43_out, and_44_out, and_45_out, and_46_out, and_47_out, and_48_out);
  or or_8 (OUT[1], and_49_out, and_50_out, and_51_out, and_52_out, and_53_out, and_54_out, and_55_out, and_56_out, and_57_out, and_58_out, and_59_out, and_60_out, and_61_out);
  or or_9 (OUT[0], and_62_out, and_63_out, and_64_out);
endmodule

module CBH (
  input  [7:0] IN,
  output [8:0] OUT
);

  wire and_1_out, and_2_out, and_3_out, and_4_out, and_5_out, and_6_out, and_7_out, and_8_out, and_9_out,
       and_10_out, and_11_out, and_12_out, and_13_out, and_14_out, and_15_out, and_16_out, and_17_out,
       and_18_out, and_19_out, and_20_out, and_21_out, and_22_out, and_23_out, and_24_out, and_25_out,
       and_26_out, and_27_out, and_28_out, and_29_out, and_30_out, and_31_out, and_32_out, and_33_out,
       and_34_out, and_35_out, and_36_out, and_37_out, and_38_out, and_39_out, and_40_out, and_41_out,
       and_42_out, and_43_out, and_44_out, and_45_out, and_46_out, and_47_out, and_48_out, and_49_out,
       and_50_out, and_51_out, and_52_out, and_53_out, and_54_out, and_55_out, and_56_out, and_57_out,
       and_58_out, and_59_out, and_60_out;

  and and_1 (and_1_out, IN[3], IN[1]);
  and and_2 (and_2_out, IN[3], IN[2]);
  and and_3 (and_3_out, IN[7], IN[5]);
  and and_4 (and_4_out, IN[7], IN[6]);
  and and_5 (and_5_out, ~IN[7], IN[6], IN[5], ~IN[3], IN[2]);  // AND_Gate
  and and_6 (and_6_out, ~IN[7], IN[6], IN[5], IN[3], ~IN[2], ~IN[1]);  // AND_Gate
  and and_7 (and_7_out, ~IN[7], IN[6], IN[5], IN[4], ~IN[3]);  // AND_Gate
  and and_8 (and_8_out, IN[7], ~IN[6], ~IN[5], ~IN[3]);  // AND_Gate
  and and_9 (and_9_out, IN[7], ~IN[6], ~IN[5], ~IN[2], ~IN[1]);  // AND_Gate
  and and_10 (and_10_out, ~IN[7], ~IN[6], IN[5], IN[4], ~IN[3], IN[1]);  // AND_Gate
  and and_11 (and_11_out, ~IN[7], ~IN[6], IN[5], IN[4], ~IN[3], IN[2]);  // AND_Gate
  and and_12 (and_12_out, ~IN[7], ~IN[6], IN[5], IN[4], IN[3], ~IN[2], ~IN[1]);  // AND_Gate
  and and_13 (and_13_out, ~IN[7], IN[6], ~IN[5], ~IN[3]);  // AND_Gate
  and and_14 (and_14_out, ~IN[7], IN[6], ~IN[5], ~IN[2], ~IN[1]);  // AND_Gate
  and and_15 (and_15_out, ~IN[7], IN[6], ~IN[4], ~IN[3], ~IN[2]);  // AND_Gate
  and and_16 (and_16_out, IN[7], ~IN[6], ~IN[5], IN[4], ~IN[3], IN[2], IN[1]);  // AND_Gate
  and and_17 (and_17_out, IN[7], ~IN[6], ~IN[5], IN[4], IN[3], ~IN[2], ~IN[1]);  // AND_Gate
  and and_18 (and_18_out, ~IN[7], ~IN[5], IN[4], ~IN[3], IN[2], IN[1]);  // AND_Gate
  and and_19 (and_19_out, ~IN[7], ~IN[5], IN[4], IN[3], ~IN[2], ~IN[1]);  // AND_Gate
  and and_20 (and_20_out, ~IN[7], ~IN[6], IN[5], ~IN[4], ~IN[3]);  // AND_Gate
  and and_21 (and_21_out, ~IN[7], ~IN[6], IN[5], ~IN[4], ~IN[2], ~IN[1]);  // AND_Gate
  and and_22 (and_22_out, ~IN[7], ~IN[6], IN[5], ~IN[3], ~IN[2], ~IN[1]);  // AND_Gate
  and and_23 (and_23_out, ~IN[7], IN[5], ~IN[4], ~IN[3], ~IN[2]);  // AND_Gate
  and and_24 (and_24_out, ~IN[7], IN[6], ~IN[5], IN[3], ~IN[2], ~IN[1]);  // AND_Gate
  and and_25 (and_25_out, ~IN[7], IN[6], ~IN[5], IN[4], ~IN[3]);  // AND_Gate
  and and_26 (and_26_out, IN[7], ~IN[6], ~IN[5], ~IN[4], ~IN[3]);  // AND_Gate
  and and_27 (and_27_out, IN[7], ~IN[6], ~IN[5], ~IN[4], ~IN[2], ~IN[1]);  // AND_Gate
  and and_28 (and_28_out, IN[7], ~IN[6], ~IN[5], ~IN[3], ~IN[2]);  // AND_Gate
  and and_29 (and_29_out, IN[7], ~IN[6], ~IN[5], ~IN[3], ~IN[1]);  // AND_Gate
  and and_30 (and_30_out, ~IN[7], ~IN[6], ~IN[4], IN[3], ~IN[2], ~IN[1]);  // AND_Gate
  and and_31 (and_31_out, ~IN[6], ~IN[5], ~IN[4], IN[3], ~IN[2], ~IN[1]);  // AND_Gate
  and and_32 (and_32_out, ~IN[7], ~IN[6], IN[4], ~IN[3], ~IN[2], ~IN[1]);  // AND_Gate
  and and_33 (and_33_out, ~IN[6], ~IN[5], IN[4], ~IN[3], ~IN[2]);  // AND_Gate
  and and_34 (and_34_out, ~IN[6], ~IN[5], IN[4], ~IN[3], ~IN[1]);  // AND_Gate
  and and_35 (and_35_out, ~IN[7], ~IN[6], IN[5], ~IN[4], ~IN[3], IN[2]);  // AND_Gate
  and and_36 (and_36_out, ~IN[7], IN[6], ~IN[5], ~IN[4], ~IN[3]);  // AND_Gate
  and and_37 (and_37_out, ~IN[7], IN[6], ~IN[4], ~IN[3], ~IN[2]);  // AND_Gate
  and and_38 (and_38_out, ~IN[7], IN[6], ~IN[5], ~IN[3], IN[2], IN[1]);  // AND_Gate
  and and_39 (and_39_out, ~IN[7], IN[6], IN[4], IN[3], ~IN[2], ~IN[1]);  // AND_Gate
  and and_40 (and_40_out, ~IN[7], IN[6], IN[5], ~IN[3], ~IN[2], IN[1]);  // AND_Gate
  and and_41 (and_41_out, ~IN[7], IN[6], IN[5], IN[4], ~IN[3], IN[2]);  // AND_Gate
  and and_42 (and_42_out, ~IN[7], ~IN[5], ~IN[4], ~IN[3], IN[2]);  // AND_Gate
  and and_43 (and_43_out, ~IN[7], ~IN[5], ~IN[3], IN[2], ~IN[1]);  // AND_Gate
  and and_44 (and_44_out, ~IN[6], ~IN[5], ~IN[4], ~IN[3], IN[2]);  // AND_Gate
  and and_45 (and_45_out, ~IN[6], ~IN[5], ~IN[3], IN[2], ~IN[1]);  // AND_Gate
  and and_46 (and_46_out, ~IN[7], ~IN[5], IN[4], ~IN[3], ~IN[2], IN[1]);  // AND_Gate
  and and_47 (and_47_out, ~IN[6], ~IN[5], IN[4], ~IN[3], ~IN[2], IN[1]);  // AND_Gate
  and and_48 (and_48_out, ~IN[7], IN[5], ~IN[4], ~IN[3], ~IN[2]);  // AND_Gate
  and and_49 (and_49_out, ~IN[7], IN[5], ~IN[2], ~IN[1]);  // AND_Gate
  and and_50 (and_50_out, ~IN[7], IN[5], IN[4], ~IN[3], IN[2], IN[1]);  // AND_Gate
  and and_51 (and_51_out, ~IN[7], ~IN[4], ~IN[3], IN[1]);  // AND_Gate
  and and_52 (and_52_out, ~IN[6], ~IN[5], ~IN[4], ~IN[3], IN[1]);  // AND_Gate
  and and_53 (and_53_out, ~IN[7], IN[4], ~IN[3], ~IN[1]);  // AND_Gate
  and and_54 (and_54_out, ~IN[7], IN[4], ~IN[2], ~IN[1]);  // AND_Gate
  and and_55 (and_55_out, ~IN[6], ~IN[5], IN[4], ~IN[3], ~IN[1]);  // AND_Gate
  and and_56 (and_56_out, ~IN[6], ~IN[5], IN[4], ~IN[2], ~IN[1]);  // AND_Gate
  and and_57 (and_57_out, ~IN[7], ~IN[3], IN[0]);  // AND_Gate
  and and_58 (and_58_out, ~IN[7], ~IN[2], ~IN[1], IN[0]);  // AND_Gate
  and and_59 (and_59_out, ~IN[6], ~IN[5], ~IN[3], IN[0]);  // AND_Gate
  and and_60 (and_60_out, ~IN[6], ~IN[5], ~IN[2], ~IN[1], IN[0]);  // AND_Gate
  or or_1 (OUT[8], and_1_out, and_2_out, and_3_out, and_4_out);
  or or_2 (OUT[6], and_5_out, and_6_out, and_7_out, and_8_out, and_9_out);
  or or_3 (OUT[5], and_10_out, and_11_out, and_12_out, and_13_out, and_14_out, and_15_out, and_16_out, and_17_out);
  or or_4 (OUT[4], and_18_out, and_19_out, and_20_out, and_21_out, and_22_out, and_23_out, and_24_out, and_25_out, and_26_out, and_27_out, and_28_out, and_29_out);
  or or_5 (OUT[3], and_30_out, and_31_out, and_32_out, and_33_out, and_34_out, and_35_out, and_36_out, and_37_out, and_38_out, and_39_out, and_40_out, and_41_out);
  or or_6 (OUT[2], and_42_out, and_43_out, and_44_out, and_45_out, and_46_out, and_47_out, and_48_out, and_49_out, and_50_out);
  or or_7 (OUT[1], and_51_out, and_52_out, and_53_out, and_54_out, and_55_out, and_56_out);
  or or_8 (OUT[0], and_57_out, and_58_out, and_59_out, and_60_out);

  assign OUT[7] = 1'b0;
endmodule

module _4t5 (
  input  N0,
  input  N1,
  input  N2,
  input  N3,
  output O0,
  output O1,
  output O2,
  output O3,
  output O4
);

  wire and_1_out, multiplexer_1_out, or_1_out, or_2_out, or_3_out, xnor_1_out, xnor_2_out, xor_1_out,
       xor_3_out;

  and and_1 (and_1_out, N2, or_1_out);
  or or_1 (or_1_out, N0, N1);
  or or_2 (or_2_out, N1, N2);
  xnor xnor_1 (xnor_1_out, N1, N2);
  xor xor_1 (xor_1_out, O4, N1);
  xnor xnor_2 (xnor_2_out, N1, N0);
  Multiplexer #(.enable("false")) multiplexer_1 (.in0(N2), .in1(xnor_1_out), .out(multiplexer_1_out), .sel(O4));
  or or_3 (or_3_out, and_1_out, N3);
  and and_2 (O4, or_2_out, N3);
  xor xor_2 (O0, N0, O3);
  Multiplexer #(.enable("false")) multiplexer_2 (.in0(xor_1_out), .in1(xnor_2_out), .out(O1), .sel(O3));
  Multiplexer #(.enable("false")) multiplexer_3 (.in0(multiplexer_1_out), .in1(xor_3_out), .out(O2), .sel(O3));
  xor xor_3 (xor_3_out, multiplexer_1_out, or_1_out);
  xor xor_4 (O3, or_3_out, O4);
endmodule

module _5t5 (
  input  N0,
  input  N1,
  input  N2,
  input  N3,
  input  N4,
  output O0,
  output O1,
  output O2,
  output O3,
  output O4
);

  wire and_1_out, and_2_out, and_3_out, and_5_out, F, multiplexer_1_out, multiplexer_3_out,
       multiplexer_4_out, not_1_out, or_1_out, or_2_out, or_4_out, P, S, xnor_1_out, xnor_2_out, xor_2_out,
       xor_3_out, xor_4_out;

  and and_1 (and_1_out, N1, N0);
  or or_1 (or_1_out, N1, N0);
  xor xor_1 (O0, O3, N0);
  xor xor_2 (xor_2_out, O4, N1);
  Multiplexer #(.enable("false")) multiplexer_1 (.in0(xor_2_out), .in1(xnor_1_out), .out(multiplexer_1_out), .sel(O3));
  xnor xnor_1 (xnor_1_out, N0, N1);
  xnor xnor_2 (xnor_2_out, N1, N2);
  xor xor_3 (xor_3_out, N2, or_1_out);
  xor xor_4 (xor_4_out, and_1_out, N2);
  and and_2 (and_2_out, and_1_out, N2);
  and and_3 (and_3_out, or_1_out, N2);
  or or_2 (or_2_out, N1, N2);
  Multiplexer #(.enable("false")) multiplexer_2 (.in0(multiplexer_1_out), .in1(not_1_out), .out(O1), .sel(S));
  not not_1 (not_1_out, xnor_1_out);
  Multiplexer #(.enable("false")) multiplexer_3 (.in0(N2), .in1(xnor_2_out), .out(multiplexer_3_out), .sel(O4));
  Multiplexer #(.enable("false")) multiplexer_4 (
    .in0(multiplexer_3_out), .in1(xor_3_out), .out(multiplexer_4_out), .sel(O3));
  and and_4 (P, and_2_out, N3);
  or or_3 (S, P, N4);
  or or_4 (or_4_out, N3, and_3_out);
  and and_5 (and_5_out, or_2_out, N3);
  or or_5 (O4, and_5_out, N4);
  Multiplexer #(.enable("false")) multiplexer_5 (.in0(multiplexer_4_out), .in1(xor_4_out), .out(O2), .sel(S));
  xor xor_5 (F, or_4_out, O4);
  or or_6 (O3, P, F);

  // Other names for the same wires on the sheet: T = O3; X = O4
endmodule
