// Logisim project Instruction Progammer.circ as structural Verilog: 5 circuits, main circuit main
module main (
  input  DI,
  input  A,
  input  ALIL,
  input  X,
  input  TBL,
  input  Y,
  input  X_2,
  input  Z,
  input  [3:0] SPO,
  input  Y_2,
  input  SWP_A,
  input  A_2,
  input  [2:0] OFS,
  input  nA,
  input  B,
  input  END,
  input  RND,
  input  X_3,
  input  PC,
  input  SKIP,
  input  Y_3,
  input  TA,
  input  A_3,
  input  Z_2,
  input  TA_X,
  input  B_2,
  input  SPL_SPH,
  input  TA_Y,
  input  X_4,
  input  DI_TBL,
  input  TA_Z,
  input  Y_4,
  input  IN_SEL,
  input  BP_B,
  input  OR,
  input  Z_3,
  input  BP_B_X,
  input  TAH,
  input  A_4,
  input  BP_B_Y,
  input  TAL,
  input  B_3,
  input  BP_A,
  input  SPS,
  input  X_5,
  input  BP_A_X,
  input  Y_5,
  input  BP_A_Y,
  input  DI_2,
  input  Z_4,
  input  SP,
  input  ALIL_H,
  input  P,
  input  SP_Y,
  input  Y_6,
  input  TBL_2,
  input  SP_TBL,
  input  Z_5,
  input  TBH,
  input  SP_TAL,
  input  PCL,
  input  V,
  input  PC_PCO,
  input  PCH,
  input  PC_DI,
  input  WRITE,
  input  PC_TBL_DI,
  input  MLB,
  input  TBL_DI___OFS,
  input  LD_SPL,
  input  BRK,
  input  LD_SPH,
  input  LD_TBL,
  input  EN_CON,
  input  LD_TBH,
  input  CLR_INT,
  output DI_3,
  output A_5,
  output ALIL_2,
  output X_6,
  output TBL_3,
  output Y_7,
  output X_7,
  output Z_6,
  output Y_8,
  output SWP_A_2,
  output A_6,
  output nA_2,
  output B_4,
  output X_8,
  output PC_2,
  output Y_9,
  output TA_2,
  output A_7,
  output Z_7,
  output TA_X_2,
  output B_5,
  output SPL_SPH_2,
  output TA_Y_2,
  output X_9,
  output DI_TBL_2,
  output TA_Z_2,
  output Y_10,
  output RND_2,
  output BP,
  output Z_8,
  output BP_X,
  output TAH_2,
  output A_8,
  output BP_Y,
  output TAL_2,
  output B_6,
  output BP_Z,
  output SPS_2,
  output X_10,
  output SP_2,
  output Y_11,
  output SP_Y_2,
  output DI_4,
  output Z_9,
  output SP_TAL_2,
  output ALIL_H_2,
  output FL,
  output V_2,
  output Y_12,
  output TBL_4,
  output Z_10,
  output TBH_2,
  output WRITE_2,
  output PCL_2,
  output MLB_2,
  output PC_PCO_2,
  output PCH_2,
  output BRK_2,
  output PC_DI_2,
  output PC_TBL_DI_2,
  output EN_ALU,
  output TBL_DI___OFS_2,
  output LD_PC,
  output EN_CON_2,
  output LD_SPL_2,
  output CLR_INT_2,
  output LD_SPH_2,
  output LD_TBL_2,
  output LD_TBH_2
);

  wire ALU_EN, END_t, ENDo, LPC, LRE, LREo, NEXT_2_out, NEXT_out, NEXT_ST_out, or_1_out, or_3_out, or_4_out,
       PREV_2_out, PREV_out, PREV_ST_out, SKIPo, ST;
  wire [1:0] ALAS, ALASo, PCS, PCSo, TBS, TBSo;
  wire [2:0] ALBS, ALBSo, CY, LRS, LRSo, OFSo, RGS, RGSo;
  wire [3:0] AOS, AOSo, DOS, DOSo, SPOo;
  wire [3:3] pull_resistor_1_node;
  wire [7:0] A_t, D, fileviewer_2_p1;
  wire [7:7] decoder_1_out7;
  wire [11:0] multiplexer_2_out, or_6_out;
  wire [14:12] decoder_8_out12;
  wire [15:10] undriven;
  wire [31:0] multiplexer_1_out, or_5_out;

  Button NEXT (.out(NEXT_out));
  or or_1 (or_1_out, NEXT_out, PREV_out);
  Button PREV (.out(PREV_out));
  Button STORE (.out(ST));
  or or_2 (END_t, END, SKIP);
  Hex_Digit_Display OPC (.value(A_t[7:4]));  // open: dp
  Hex_Digit_Display hex_digit_display_1 (.value(A_t[3:0]));  // open: dp
  Hex_Digit_Display STATE (.value({pull_resistor_1_node[3], CY}));  // open: dp
  Pull_Resistor pull_resistor_1 (.node({pull_resistor_1_node[3], CY}));
  Counter #(.ongoal("stay")) counter_1 (
    .count(or_1_out), .Q(A_t), .up(NEXT_out), .clk(or_1_out));  // open: load, D, carry, clr
  // FileViewer #(.addrWidth(8), .cols(72), .lines(1)) fileviewer_1: pin names not known; wires that end beside it: A_t
  // Probe on A_t
  Button NEXT_2 (.out(NEXT_2_out));
  Button PREV_2 (.out(PREV_2_out));
  Button NEXT_ST (.out(NEXT_ST_out));
  Button PREV_ST (.out(PREV_ST_out));
  _8_ENC u_8_enc_1 (.OUT(RGS), .IN({RND, nA, SWP_A, Y_2, X_2, TBL, ALIL, DI}));  // open: EN_OUT
  _8_ENC u_8_enc_2 (.OUT(LRS), .EN_OUT(LRE), .IN({SPS, TAL, TAH, Z_3, Y_4, X_4, B_2, A_3}));
  _4_ENC u_4_enc_1 (.OUT(TBS), .IN({Z_5, Y_6, ALIL_H, DI_2}));  // open: EN_OUT
  _4_ENC u_4_enc_2 (.OUT(PCS), .EN_OUT(LPC), .IN({TBL_DI___OFS, PC_TBL_DI, PC_DI, PC_PCO}));
  Counter #(.ongoal("stay")) counter_2 (
    .count(or_3_out), .Q(D), .up(NEXT_2_out), .clk(or_3_out));  // open: load, D, carry, clr
  or or_3 (or_3_out, NEXT_2_out, PREV_2_out);
  Counter #(.max('h7), .ongoal("stay"), .width(3)) u_CY (
    .count(or_4_out), .Q(CY), .up(NEXT_ST_out), .clk(or_4_out));  // open: load, D, carry, clr
  or or_4 (or_4_out, NEXT_ST_out, PREV_ST_out);
  // FileViewer #(.addrWidth(8), .cols(72), .lines(1)) fileviewer_2: pin names not known; wires that end beside it: fileviewer_2_p1
  _4_ENC u_4_enc_3 (.OUT(ALAS), .IN({Z, Y, X, A}));  // open: EN_OUT
  _8_ENC u_8_enc_3 (.OUT(ALBS), .EN_OUT(ALU_EN), .IN({IN_SEL, DI_TBL, SPL_SPH, Z_2, Y_3, X_3, B, A_2}));
  _16_ENC u_16_enc_1 (.OUT(DOS), .IN({undriven, PCH, PCL, TBH, TBL_2, P, Z_4, Y_5, X_5, B_3, A_4}));  // open: EN_OUT
  // Probe on SPO
  // Probe on OFS
  _16_ENC u_16_enc_2 (
    .OUT(AOS),
    .IN({V, SP_TAL, SP_TBL, SP_Y, SP, BP_A_Y, BP_A_X, BP_A, BP_B_Y, BP_B_X, BP_B, TA_Z, TA_Y, TA_X, TA, PC}));  // open: EN_OUT
  RAM #(.addrWidth(11)) ram_1 (.addr({D, CY}), .we(ST), .clk(ST), .din(A_t), .dout(fileviewer_2_p1));
  // FileViewer #(.addrWidth(8), .cols(16), .lines(1)) fileviewer_3: pin names not known; wires that end beside it: D
  assign or_5_out = {OFS, LD_SPH, LD_SPL, LPC, PCS, LRE, LRS, LD_TBH, LD_TBL, TBS, AOS, RGS, DOS, ALBS, ALAS} | {OFSo, LD_SPH_2, LD_SPL_2, LD_PC, PCSo, LREo, LRSo, LD_TBH_2, LD_TBL_2, TBSo, AOSo, RGSo, DOSo, ALBSo, ALASo};  // OR_Gate or_5, 32 bits wide
  assign or_6_out = {END_t, SKIP, CLR_INT, EN_CON, ALU_EN, BRK, MLB, WRITE, SPO} | {ENDo, SKIPo, CLR_INT_2, EN_CON_2, EN_ALU, BRK_2, MLB_2, WRITE_2, SPOo};  // OR_Gate or_6, 12 bits wide
  RAM #(.dataWidth(32), .\type ("nonvolatile")) ram_2 (
    .addr(A_t), .we(ST), .clk(ST), .din(multiplexer_1_out),
    .dout({OFSo, LD_SPH_2, LD_SPL_2, LD_PC, PCSo, LREo, LRSo, LD_TBH_2, LD_TBL_2, TBSo, AOSo, RGSo, DOSo, ALBSo, ALASo}));
  Multiplexer #(.enable("false"), .width(32)) multiplexer_1 (
    .in0({OFS, LD_SPH, LD_SPL, LPC, PCS, LRE, LRS, LD_TBH, LD_TBL, TBS, AOS, RGS, DOS, ALBS, ALAS}),
    .in1(or_5_out), .out(multiplexer_1_out), .sel(OR));
  RAM #(.dataWidth(12), .\type ("nonvolatile")) ram_3 (
    .addr(A_t), .we(ST), .clk(ST), .din(multiplexer_2_out),
    .dout({ENDo, SKIPo, CLR_INT_2, EN_CON_2, EN_ALU, BRK_2, MLB_2, WRITE_2, SPOo}));
  Multiplexer #(.enable("false"), .width(12)) multiplexer_2 (
    .in0({END_t, SKIP, CLR_INT, EN_CON, ALU_EN, BRK, MLB, WRITE, SPO}), .in1(or_6_out),
    .out(multiplexer_2_out), .sel(OR));
  // Probe on multiplexer_1_out
  // Probe on multiplexer_2_out
  Decoder #(.enable("false"), .select(3)) decoder_1 (
    .out0(DI_3), .out1(ALIL_2), .out2(TBL_3), .out3(X_7), .out4(Y_8), .out5(SWP_A_2), .out6(nA_2),
    .out7(decoder_1_out7[7]), .sel(RGSo));
  Decoder #(.select(3)) decoder_2 (
    .out0(A_7), .out1(B_5), .out2(X_9), .out3(Y_10), .out4(Z_8), .out5(TAH_2), .out6(TAL_2), .out7(SPS_2),
    .sel(LRSo), .en(LREo));
  Decoder #(.enable("false"), .select(2)) decoder_3 (
    .out0(DI_4), .out1(ALIL_H_2), .out2(Y_12), .out3(Z_10), .sel(TBSo));
  Decoder #(.enable("false"), .select(2)) decoder_4 (
    .out0(PC_PCO_2), .out1(PC_DI_2), .out2(PC_TBL_DI_2), .out3(TBL_DI___OFS_2), .sel(PCSo));
  Decoder #(.enable("false"), .select(2)) decoder_5 (.out0(A_5), .out1(X_6), .out2(Y_7), .out3(Z_6), .sel(ALASo));
  Decoder #(.enable("false"), .select(3)) decoder_6 (
    .out0(A_6), .out1(B_4), .out2(X_8), .out3(Y_9), .out4(Z_7), .out5(SPL_SPH_2), .out6(DI_TBL_2),
    .out7(RND_2), .sel(ALBSo));
  Decoder #(.enable("false"), .select(4)) decoder_7 (
    .out0(A_8), .out1(B_6), .out2(X_10), .out3(Y_11), .out4(Z_9), .out5(FL), .out6(TBL_4), .out7(TBH_2),
    .out8(PCL_2), .out9(PCH_2), .sel(DOSo));  // open: out10, out11, out12, out13, out14, out15
  // Probe on SPOo
  // Probe on OFSo
  Decoder #(.enable("false"), .select(4)) decoder_8 (
    .out0(PC_2), .out1(TA_2), .out2(TA_X_2), .out3(TA_Y_2), .out4(TA_Z_2), .out5(BP), .out6(BP_X),
    .out7(BP_Y), .out8(BP_Z), .out9(SP_2), .out10(SP_Y_2), .out11(SP_TAL_2), .out12(decoder_8_out12[12]),
    .out13(decoder_8_out12[13]), .out14(decoder_8_out12[14]), .out15(V_2), .sel(AOSo));
  // Probe on nothing

  // Other names for the same wires on the sheet: LBL = LD_TBL; LBH = LD_TBH; LSL = LD_SPL; LSH = LD_SPH;
  //   MEM[2:0] = {BRK, MLB, WRITE}; COND_E = EN_CON; MEMo[2:0] = {BRK_2, MLB_2, WRITE_2}; ALU_ENo = EN_ALU;
  //   COND_Eo = EN_CON_2; CLR_INTo = CLR_INT_2; LBLo = LD_TBL_2; LBHo = LD_TBH_2; LPCo = LD_PC; LSLo = LD_SPL_2;
  //   LSHo = LD_SPH_2

  // Notes on the sheet:
  //   contents of fileviewer_1 (hex, n*v repeats v):
  //   01      - Add into PC from (PC - 1) and TBL; ----END 02         - Add into PC from (PC - 1); ----END
  //   03         - Check <bit> from (BL/B), Jump to 5. if set 04         - Check <bit>, Jump to 5. if set
  //   05     - Do an <ALU> Operation with A and (BL/B); ----END 06   - Do an <ALU> Operation with A and
  //   (BL/B+X); ----END 07         - Do an <ALU> Operation with A and (PC - 1); ----END 08         - Do an
  //   <ALU> Operation with A and (SP + 1) 09  - Do an <ALU> Operation with A and (SP + 1); ----END 0A
  //   - Do an <ALU> Operation with A and (TA); ----END 0B     - Do an <ALU> Operation with A and (TA+X);
  //   ----END 0C   - Do an <ALU> Operation with A and (TA+Y); ----END 0D   - Do an <ALU> Operation with A
  //   and (TA+Z); ----END 0E   - Do an <ALU> Operation with A and A; ----SK0 0F        - Do an <ALU>
  //   Operation with A and INSEL; Load into A from !A; ----SK0 10       - Do an <ALU> Operation with A and
  //   INSEL; Load into A from LFSR; ----SK0 11     - Do an <ALU> Operation with A and INSEL; Load into A
  //   from SWP A; ----SK0 12    - Do an <ALU> Operation with X and (BL/B); ----END 13   - Do an <ALU>
  //   Operation with X and (PC - 1); ----END 14 - Do an <ALU> Operation with X and (TA); ----END 15     -
  //   Do an <ALU> Operation with Y and (BL/B); ----END 16   - Do an <ALU> Operation with Y and (PC - 1);
  //   ----END 17 - Do an <ALU> Operation with Y and (TA); ----END 18     - Do an <ALU> Operation with Z
  //   and (BL/B); ----END 19   - Do an <ALU> Operation with Z and (PC - 1); ----END 1A - Do an <ALU>
  //   Operation with Z and (TA); ----END 1B     - Load into A from (SP + 1) 1C  - Load into A from <ALU>
  //   given A and (BL/B); ----END 1D - Load into A from <ALU> given A and (BL/B+X); ----END 1E       -
  //   Load into A from <ALU> given A and (PC - 1); ----END 1F       - Load into A from <ALU> given A and
  //   (SP + 1) 20        - Load into A from <ALU> given A and (SP+Y); ----END 21 - Load into A from <ALU>
  //   given A and (TA); ----END 22   - Load into A from <ALU> given A and (TA+X); ----END 23 - Load into A
  //   from <ALU> given A and (TA+Y); ----END 24 - Load into A from <ALU> given A and (TA+Z); ----END 25 -
  //   Load into A from <ALU> given A and A; ----SK0 26      - Load into A from <ALU> given A and B;
  //   ----SK0 27      - Load into A from <ALU> given A and X; ----SK0 28      - Load into A from <ALU>
  //   given A and Y; ----SK0 29      - Load into A from <ALU> given A and Z; ----SK0 2A      - Load into B
  //   from (SP + 2) 2B  - Load into B from A; ----SK0 2C        - Load into PC from (PC - 1) and TBL;
  //   ----END 2D        - Load into PC from (SP + 2) and TBL (+ 1) 2E   - Load into PC from (SP + 3) and
  //   TBL 2F - Load into PC from (SP+TAL + 2) and TBL (+ 1) 30       - Load into PC from (TA + 1) and TBL;
  //   ----END 31        - Load into PC from (TA+X + 1) and TBL; ----END 32      - Load into PC from
  //   (VECTOR + 1) and TBL; ----END 33    - Load into SPH from Y; ----SK0 34      - Load into SPL from X;
  //   ----SK0 35      - Load into TAH from (BL/B + 1) 36      - Load into TAH from (BL/B+X + 1) 37    -
  //   Load into TAH from (PC - 1) 38        - Load into TAH from (SP+TBL + 2) 39    - Load into TAL from
  //   (BL/B) 3A  - Load into TAL from (BL/B+X) 3B        - Load into TAL from (PC - 1) 3C        - Load
  //   into TAL from (PC - 2) 3D        - Load into TAL from (SP+TBL + 1) 3E    - Load into TBH from (PC -
  //   1) 3F        - Load into TBH from (TA + 1) 40        - Load into TBL from (BL/A) (MLB) 41    - Load
  //   into TBL from (PC - 1) 42        - Load into TBL from (PC - 2) 43        - Load into TBL from (SP +
  //   1) 44        - Load into TBL from (SP + 2) 45        - Load into TBL from (SP+TAL + 1) 46    - Load
  //   into TBL from (TA) 47    - Load into TBL from (TA) (MLB) 48      - Load into TBL from (TA+X) 49  -
  //   Load into TBL from <ALU> given A and (BL/A) (MLB) 4A  - Load into TBL from <ALU> given A and
  //   (BL/A+X) (MLB) 4B        - Load into TBL from <ALU> given A and (TA) (MLB) 4C    - Load into TBL
  //   from <ALU> given A and (TA+X) (MLB) 4D  - Load into TBL/TBH from <ALU> given A and (BL/A + 1) (MLB)
  //   4E  - Load into TBL/TBH from <ALU> given A and (TA + 1) (MLB) 4F    - Load into X from (SP + 3) 50
  //   - Load into X from <ALU> given A and (BL/B); ----END 51 - Load into X from <ALU> given A and
  //   (BL/B+Y); ----END 52       - Load into X from <ALU> given A and (PC - 1); ----END 53       - Load
  //   into X from <ALU> given A and (SP + 1) 54        - Load into X from <ALU> given A and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
  //   IN-SEL
  //   REG-E
  //   TMP-B
  //   PC-SEL
  //   ALU-A
  //   ALU-B
  //   OUT-SEL
  //   LOADS
  //   contents of fileviewer_2 (hex, n*v repeats v):
  //   01      - Add into PC from (PC - 1) and TBL; ----END 02         - Add into PC from (PC - 1); ----END
  //   03         - Check <bit> from (BL/B), Jump to 5. if set 04         - Check <bit>, Jump to 5. if set
  //   05     - Do an <ALU> Operation with A and (BL/B); ----END 06   - Do an <ALU> Operation with A and
  //   (BL/B+X); ----END 07         - Do an <ALU> Operation with A and (PC - 1); ----END 08         - Do an
  //   <ALU> Operation with A and (SP + 1) 09  - Do an <ALU> Operation with A and (SP + 1); ----END 0A
  //   - Do an <ALU> Operation with A and (TA); ----END 0B     - Do an <ALU> Operation with A and (TA+X);
  //   ----END 0C   - Do an <ALU> Operation with A and (TA+Y); ----END 0D   - Do an <ALU> Operation with A
  //   and (TA+Z); ----END 0E   - Do an <ALU> Operation with A and A; ----SK0 0F        - Do an <ALU>
  //   Operation with A and INSEL; Load into A from !A; ----SK0 10       - Do an <ALU> Operation with A and
  //   INSEL; Load into A from LFSR; ----SK0 11     - Do an <ALU> Operation with A and INSEL; Load into A
  //   from SWP A; ----SK0 12    - Do an <ALU> Operation with X and (BL/B); ----END 13   - Do an <ALU>
  //   Operation with X and (PC - 1); ----END 14 - Do an <ALU> Operation with X and (TA); ----END 15     -
  //   Do an <ALU> Operation with Y and (BL/B); ----END 16   - Do an <ALU> Operation with Y and (PC - 1);
  //   ----END 17 - Do an <ALU> Operation with Y and (TA); ----END 18     - Do an <ALU> Operation with Z
  //   and (BL/B); ----END 19   - Do an <ALU> Operation with Z and (PC - 1); ----END 1A - Do an <ALU>
  //   Operation with Z and (TA); ----END 1B     - Load into A from (SP + 1) 1C  - Load into A from <ALU>
  //   given A and (BL/B); ----END 1D - Load into A from <ALU> given A and (BL/B+X); ----END 1E       -
  //   Load into A from <ALU> given A and (PC - 1); ----END 1F       - Load into A from <ALU> given A and
  //   (SP + 1) 20        - Load into A from <ALU> given A and (SP+Y); ----END 21 - Load into A from <ALU>
  //   given A and (TA); ----END 22   - Load into A from <ALU> given A and (TA+X); ----END 23 - Load into A
  //   from <ALU> given A and (TA+Y); ----END 24 - Load into A from <ALU> given A and (TA+Z); ----END 25 -
  //   Load into A from <ALU> given A and A; ----SK0 26      - Load into A from <ALU> given A and B;
  //   ----SK0 27      - Load into A from <ALU> given A and X; ----SK0 28      - Load into A from <ALU>
  //   given A and Y; ----SK0 29      - Load into A from <ALU> given A and Z; ----SK0 2A      - Load into B
  //   from (SP + 2) 2B  - Load into B from A; ----SK0 2C        - Load into PC from (PC - 1) and TBL;
  //   ----END 2D        - Load into PC from (SP + 2) and TBL (+ 1) 2E   - Load into PC from (SP + 3) and
  //   TBL 2F - Load into PC from (SP+TAL + 2) and TBL (+ 1) 30       - Load into PC from (TA + 1) and TBL;
  //   ----END 31        - Load into PC from (TA+X + 1) and TBL; ----END 32      - Load into PC from
  //   (VECTOR + 1) and TBL; ----END 33    - Load into SPH from Y; ----SK0 34      - Load into SPL from X;
  //   ----SK0 35      - Load into TAH from (BL/B + 1) 36      - Load into TAH from (BL/B+X + 1) 37    -
  //   Load into TAH from (PC - 1) 38        - Load into TAH from (SP+TBL + 1) 39    - Load into TAL from
  //   (BL/B) 3A  - Load into TAL from (BL/B+X) 3B        - Load into TAL from (PC - 1) 3C        - Load
  //   into TAL from (PC - 2) 3D        - Load into TAL from (SP+TBL) 3E        - Load into TBH from (PC -
  //   1) 3F        - Load into TBH from (TA + 1) 40        - Load into TBL from (BL/A) (MLB) 41    - Load
  //   into TBL from (PC - 1) 42        - Load into TBL from (PC - 2) 43        - Load into TBL from (SP +
  //   1) 44        - Load into TBL from (SP + 2) 45        - Load into TBL from (SP+TAL + 1) 46    - Load
  //   into TBL from (TA) 47    - Load into TBL from (TA) (MLB) 48      - Load into TBL from (TA+X) 49  -
  //   Load into TBL from <ALU> given A and (BL/A) (MLB) 4A  - Load into TBL from <ALU> given A and
  //   (BL/A+X) (MLB) 4B        - Load into TBL from <ALU> given A and (TA) (MLB) 4C    - Load into TBL
  //   from <ALU> given A and (TA+X) (MLB) 4D  - Load into TBL/TBH from <ALU> given A and (BL/A + 1) (MLB)
  //   4E  - Load into TBL/TBH from <ALU> given A and (TA + 1) (MLB) 4F    - Load into X from (SP + 3) 50
  //   - Load into X from <ALU> given A and (BL/B); ----END 51 - Load into X from <ALU> given A and
  //   (BL/B+Y); ----END 52       - Load into X from <ALU> given A and (PC - 1); ----END 53       - Load
  //   into X from <ALU> given A and (SP + 1) 54        - Load into X from <ALU> given A and (TA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
  //   INTERNAL
  //   AD-SEL
  //   MEMORY
  //   contents of fileviewer_3 (hex, n*v repeats v):
  //   1   - NOP 2   - CLE/SEE/CLC/SEC/CLI/SEI/CLV/CLD/SED 3   - JSR a 4   - JSR (a) 5   - JSR (a,x) 6   -
  //   BSR rr 7   - RTI s 8   - RTS s 9   - RTN # 10  - JMP a 11  - JMP (a) 12  - JMP (a,x) 13  - BRA r 14
  //   - BRA rr 15  - BPL/BCC/BNE/BVC r 16  - BMI/BCS/BEQ/BVS r 17  - BPL/BCC/BNE/BVC rr 18  -
  //   BMI/BCS/BEQ/BVS rr 19  - BBR bp, r 20  - BBS bp, r 21  - NEG A 22  -
  //   ORA/AND/XOR/ADC/LDA/SBC/MUL/MLH/MOD/DIV # 23  - ORA/AND/XOR/ADC/LDA/SBC/MUL/MLH/MOD/DIV bp 24  -
  //   ORA/AND/XOR/ADC/LDA/SBC/MUL/MLH/MOD/DIV bp,x 25  - ORA/AND/XOR/ADC/LDA/SBC/MUL/MLH/MOD/DIV a 26  -
  //   ORA/AND/XOR/ADC/LDA/SBC/MUL/MLH/MOD/DIV a,x 27  - ORA/AND/XOR/ADC/LDA/SBC/MUL/MLH/MOD/DIV a,y 28  -
  //   ORA/AND/XOR/ADC/LDA/SBC (bp,x) 29  - ORA/AND/XOR/ADC/LDA/SBC (BL/B),y 30  - ORA/AND/XOR/ADC/LDA/SBC
  //   (BL/B),z 31  - LDA (d.SP),Y 32  - LDX # 33  - LDY # 34  - LDZ # 35  - LDX bp 36  - LDY bp 37  - LDX
  //   bp,y 38  - LDY bp,x 39  - LDX a 40  - LDY a 41  - LDZ a 42  - LDX a,y 43  - LDY a,x 44  - LDZ a,x 45
  //   - STA (d.SP),Y 46  - STA (bp,x) 47  - STA (BL/B),y 48  - STA (BL/B),z 49  - STA bp 50  - STX bp 51
  //   - STY bp 52  - STZ bp 53  - STA bp,x 54  - STX bp,y 55  - STY bp,x 56  - STZ bp,x 57  - STA a 58  -
  //   STX a 59  - STY a 60  - STZ a 61  - STA a,x 62  - STY a,x 63  - STZ a,x 64  - STA a,y 65  - STX a,y
  //   66  - CMP/BIT # 67  - CMP/BIT bp 68  - CMP/BIT bp,x 69  - CMP/BIT a 70  - CMP/BIT a,x 71  - CMP a,y
  //   72  - CMP (bp,x) 73  - CMP (BL/B),y 74  - CMP (BL/B),z 75  - CPX # 76  - CPY # 77  - CPZ # 78  - CPX
  //   bp 79  - CPY bp 80  - CPZ bp 81  - CPX a 82  - CPY a 83  - CPZ a 84  -
  //   ASL/ASR/LSR/ROL/ROR/INC/DEC/CHB/CBH A 85  - ASL/ASR/LSR/ROL/ROR/TSB/TRB/RMB/SMB/INC/DEC/ICC/DCC bp
  //   86  - ASL/ASR/LSR/ROL/ROR//INC/DEC/ICC/DCC bp,x 87  - ASL/LSR/ROL/ROR/TSB/TRB/INC/DEC/ICC/DCC a 88
  //   - ASL/LSR/ROL/ROR/INC/DEC/ICC/DCC a,x 89  - INW/DEW bp 90  - AWL/AWR/LWR/RWL/RWR a 91  - PHP s 92  -
  //   PHA s 93  - PHX s 94  - PHY s 95  - PHZ s 96  - PHW ##/s 97  - PHW a/s 98  - PLP s 99  - PLA s 100 -
  //   PLX s 101 - PLY s 102 - PLZ s 103 - INX 104 - INY 105 - INZ 106 - DEX 107 - DEY 108 - DEZ 109 - TAB
  //   110 - TAX 111 - TAY 112 - TAZ 113 - TBA 114 - TXA 115 - TYA 116 - TZA 117 - TXS 118 - TYS 119 - TSX
  //   120 - TSY 121 - AUG 122 - RND A 123 - SWP 124 - SXY 125 - SXZ 126 - SYZ 127 - LDA sp,y 128 - STA
  //   sp,y 129 - PHR s 130 - PLR s 131 - WAI 132 - STP
  //   IN-SEL
  //   REG-E
  //   TMP-B
  //   PC-SEL
  //   ALU-A
  //   ALU-B
  //   OUT-SEL
  //   LOADS
  //   AD-SEL
  //   MEMORY
  //   INTERNAL
endmodule

module _32_ENC (
  input  [31:0] IN,
  output [4:0] OUT,
  output EN_OUT
);

  Pull_Resistor pull_resistor_1 (.node(OUT));
  Priority_Encoder #(.select(5)) priority_encoder_1 (
    .in0(IN[0]), .in1(IN[1]), .in2(IN[2]), .in3(IN[3]), .in4(IN[4]), .in5(IN[5]), .in6(IN[6]), .in7(IN[7]),
    .in8(IN[8]), .in9(IN[9]), .in10(IN[10]), .in11(IN[11]), .in12(IN[12]), .in13(IN[13]), .in14(IN[14]),
    .in15(IN[15]), .in16(IN[16]), .in17(IN[17]), .in18(IN[18]), .in19(IN[19]), .in20(IN[20]), .in21(IN[21]),
    .in22(IN[22]), .in23(IN[23]), .in24(IN[24]), .in25(IN[25]), .in26(IN[26]), .in27(IN[27]), .in28(IN[28]),
    .in29(IN[29]), .in30(IN[30]), .in31(IN[31]), .out(OUT), .gs(EN_OUT), .en_in(1'b1));  // open: en_out
endmodule

module _16_ENC (
  input  [15:0] IN,
  output [3:0] OUT,
  output EN_OUT
);

  Pull_Resistor pull_resistor_1 (.node(OUT));
  Priority_Encoder #(.select(4)) priority_encoder_1 (
    .in0(IN[0]), .in1(IN[1]), .in2(IN[2]), .in3(IN[3]), .in4(IN[4]), .in5(IN[5]), .in6(IN[6]), .in7(IN[7]),
    .in8(IN[8]), .in9(IN[9]), .in10(IN[10]), .in11(IN[11]), .in12(IN[12]), .in13(IN[13]), .in14(IN[14]),
    .in15(IN[15]), .out(OUT), .gs(EN_OUT), .en_in(1'b1));  // open: en_out
endmodule

module _8_ENC (
  input  [7:0] IN,
  output [2:0] OUT,
  output EN_OUT
);

  Pull_Resistor pull_resistor_1 (.node(OUT));
  Priority_Encoder priority_encoder_1 (
    .in0(IN[0]), .in1(IN[1]), .in2(IN[2]), .in3(IN[3]), .in4(IN[4]), .in5(IN[5]), .in6(IN[6]), .in7(IN[7]),
    .out(OUT), .en_in(1'b1), .gs(EN_OUT));  // open: en_out
endmodule

module _4_ENC (
  input  [3:0] IN,
  output [1:0] OUT,
  output EN_OUT
);

  Pull_Resistor pull_resistor_1 (.node(OUT));
  Priority_Encoder #(.select(2)) priority_encoder_1 (
    .in0(IN[0]), .in1(IN[1]), .in2(IN[2]), .in3(IN[3]), .out(OUT), .gs(EN_OUT), .en_in(1'b1));  // open: en_out
endmodule
